// Logisim project cpu21-riscv .circ as structural Verilog: 24 circuits, main circuit ◇单周期RISC-V
module \单周期RISC_V  (
  input  IR1,
  input  IR2,
  input  IR3,
  output RegWrite,
  output MemWrite,
  output [31:0] PC,
  output [31:0] IR,
  output [31:0] RDin,
  output [31:0] MDin,
  output [31:0] LedData
);

  wire ALU, ALU_t, ALU_t_t, and_2_out, and_3_out, and_4_out, and_5_out, Beq, BGE, Bne, CLK, clock_1_out,
       comparator_1_eq, comparator_2_eq, comparator_2_lt, d_ff_2_q, ecall, Go, halt, IR1_t, IR2_t, IR3_t,
       IRA, IRB, IRC, JAL, JALR, mips_ram_1_p7, nand_1_out, not_1_out, not_2_out, not_3_out, or_1_out,
       riscv_probe_1_p3, riscv_probe_1_p4, RST, SH, SLTIU, W1, W2, W3, \单周期硬布线控制器_1_alu_src ,
       \单周期硬布线控制器_1_s_type ;
  wire [1:0] priority_encoder_1_out, \单周期硬布线控制器_1_memtoreg ;
  wire [3:0] RAM_Sel, \单周期硬布线控制器_1_alu_op ;
  wire [3:1] multiplexer_11_out;
  wire [4:0] multiplexer_2_out, multiplexer_3_out;
  wire [11:0] multiplexer_4_out;
  wire [12:0] CNT_num;
  wire [15:0] \总周期数 ;
  wire [31:0] ALUresult, and_1_out, B_ADD, bit_extender_1_out, bit_extender_2_out, bit_extender_3_out,
       JAL_ADD, mips_ram_1_p8, multiplexer_1_out, multiplexer_6_out, multiplexer_7_out, multiplexer_8_out,
       PC_4, R2, regifile_1_r1, shifter_1_out, shifter_2_out, shifter_3_out;

  Button \u_继续运行  (.out(Go));
  Button _1 (.out(IRA));
  Button _2 (.out(IRB));
  Button _3 (.out(IRC));
  LED #(.active("true")) led_1 (.in(W1));
  LED #(.active("true")) led_2 (.in(W2));
  LED #(.active("true")) led_3 (.in(W3));
  Hex_Digit_Display hex_digit_display_1 (.value(LedData[31:28]));  // open: dp
  assign and_1_out = 32'hfffffffe & ALUresult;  // AND_Gate and_1, 32 bits wide
  Hex_Digit_Display hex_digit_display_2 (.value(LedData[23:20]));  // open: dp
  Hex_Digit_Display hex_digit_display_3 (.value(LedData[27:24]));  // open: dp
  Priority_Encoder #(.select(2), .disabled(0)) priority_encoder_1 (
    .in0(1'b1), .in1(JALR), .in2(JAL), .in3(or_1_out), .out(priority_encoder_1_out));  // open: gs, en_out, en_in
  Multiplexer #(.select(2), .width(32), .disabled("Z"), .enable("false")) multiplexer_1 (
    .in0(PC_4), .in1(and_1_out), .in2(JAL_ADD), .in3(B_ADD), .out(multiplexer_1_out),
    .sel(priority_encoder_1_out));
  not not_1 (not_1_out, halt);
  Hex_Digit_Display hex_digit_display_4 (.value(LedData[15:12]));  // open: dp
  Hex_Digit_Display hex_digit_display_5 (.value(LedData[19:16]));  // open: dp
  or or_1 (or_1_out, and_2_out, and_3_out, and_4_out);
  Register #(.width(32), .trigger("rising"), .Select("low")) u_PC (
    .D(multiplexer_1_out), .en(not_1_out), .Q(PC), .clk(CLK), .clr(RST));
  Hex_Digit_Display hex_digit_display_6 (.value(LedData[11:8]));  // open: dp
  Hex_Digit_Display hex_digit_display_7 (.value(LedData[7:4]));  // open: dp
  // Probe on \总周期数 
  and and_2 (and_2_out, Beq, ALU_t);
  and and_3 (and_3_out, ~ALU_t, Bne);  // AND_Gate
  and and_4 (and_4_out, BGE, ALU_t_t);
  Adder #(.width(32)) adder_1 (.a(PC), .b(32'h4), .out(PC_4), .cin(1'b0));  // open: cout
  Hex_Digit_Display hex_digit_display_8 (.value(LedData[3:0]));  // open: dp
  // RiscV_Probe riscv_probe_1: pin names not known; wires that end beside it: 1'b1, IR, riscv_probe_1_p3, riscv_probe_1_p4
  ROM #(.addrWidth(10), .dataWidth(32), .Select("high")) rom_1 (.addr(PC[11:2]), .data(IR));
  or or_2 (IR1_t, IR1, IRA);
  or or_3 (IR2_t, IR2, IRB);
  \单周期硬布线控制器  \u_单周期硬布线控制器_1  (
    .Funct({IR[30], IR[25], IR[14:12]}), .OP(IR[6:2]), .ALU_OP(\单周期硬布线控制器_1_alu_op ),
    .MemToReg(\单周期硬布线控制器_1_memtoreg [0]), .MemWrite(MemWrite), .ALU_SRC(\单周期硬布线控制器_1_alu_src ),
    .RegWrite(RegWrite), .ecall(ecall), .S_type(\单周期硬布线控制器_1_s_type ), .Jalr(JALR), .Beq(Beq), .JAL(JAL),
    .Bne(Bne), .in_3(IR[21]), .uret(riscv_probe_1_p3), .SRL(riscv_probe_1_p4), .SLTIU(SLTIU), .SH(SH),
    .BGE(BGE));  // open: rs1_used, rs2_used, CSRRSI, CSRRCI
  assign bit_extender_1_out = {{20{IR[31]}}, {IR[31], IR[7], IR[30:25], IR[11:8]}};  // Bit_Extender bit_extender_1
  assign bit_extender_2_out = {{12{IR[31]}}, {IR[31], IR[19:12], IR[20], IR[30:21]}};  // Bit_Extender bit_extender_2
  Multiplexer #(.select(1), .width(5), .disabled("Z"), .enable("false")) multiplexer_2 (
    .in0(IR[19:15]), .in1(5'b10001), .out(multiplexer_2_out), .sel(ecall));
  Multiplexer #(.select(1), .width(5), .disabled("Z"), .enable("false")) multiplexer_3 (
    .in0(IR[24:20]), .in1(5'b01010), .out(multiplexer_3_out), .sel(ecall));
  Multiplexer #(.select(1), .width(12), .disabled("Z"), .enable("false")) multiplexer_4 (
    .in0(IR[31:20]), .in1({IR[31:25], IR[11:7]}), .out(multiplexer_4_out), .sel(\单周期硬布线控制器_1_s_type ));
  Shifter #(.width(32), .shift("ll")) shifter_1 (.in(bit_extender_1_out), .\dist (5'b00001), .out(shifter_1_out));
  Shifter #(.width(32), .shift("ll")) shifter_2 (.in(bit_extender_2_out), .\dist (5'b00001), .out(shifter_2_out));
  Multiplexer #(.select(1), .width(32), .disabled("Z"), .enable("false")) multiplexer_5 (
    .in0(multiplexer_8_out), .in1(multiplexer_6_out), .out(RDin), .sel(SLTIU));
  Multiplexer #(.select(1), .width(32), .disabled("Z"), .enable("false")) multiplexer_6 (
    .in0({32{1'b0}}), .in1(32'h1), .out(multiplexer_6_out), .sel(ALU));
  or or_4 (IR3_t, IR3, IRC);
  not not_2 (not_2_out, halt);
  Regifile regifile_1 (
    .Din(RDin), .Clk(CLK), .R1(regifile_1_r1), .R2(R2), .WE(RegWrite), .W_num(IR[11:7]),
    .R1_num(multiplexer_2_out), .R2_num(multiplexer_3_out));
  assign bit_extender_3_out = {{20{multiplexer_4_out[11]}}, multiplexer_4_out};  // Bit_Extender bit_extender_3
  Adder #(.width(32)) adder_2 (.a(PC), .b(shifter_1_out), .out(B_ADD), .cin(1'b0));  // open: cout
  Adder #(.width(32)) adder_3 (.a(PC), .b(shifter_2_out), .out(JAL_ADD), .cin(1'b0));  // open: cout
  Counter #(.width(16), .max('hffff), .ongoal("wrap"), .trigger("rising"), .behavior("new")) counter_1 (
    .count(not_2_out), .Q(\总周期数 ), .clk(CLK));  // open: load, D, carry, clr, preset, down
  Multiplexer #(.select(1), .width(32), .disabled("Z"), .enable("false")) multiplexer_7 (
    .in0(R2), .in1(bit_extender_3_out), .out(multiplexer_7_out), .sel(\单周期硬布线控制器_1_alu_src ));
  Comparator #(.width(32), .mode("twosComplement")) comparator_1 (
    .a(regifile_1_r1), .b(32'h22), .eq(comparator_1_eq));  // open: gt, lt
  // Probe on \单周期硬布线控制器_1_alu_op 
  ALU alu_1 (
    .X(regifile_1_r1), .Y(multiplexer_7_out), .AluOP(\单周期硬布线控制器_1_alu_op ), .Equal(ALU_t),
    .Result(ALUresult), .out_4(ALU_t_t), .out_6(ALU));  // open: Result_2
  not not_3 (not_3_out, comparator_1_eq);
  Register #(.width(32), .trigger("rising"), .Select("low")) PC_2 (
    .D(R2), .en(and_5_out), .Q(LedData), .clk(CLK));  // open: clr
  and and_5 (and_5_out, comparator_1_eq, ecall);
  D_Flip_Flop #(.trigger("falling"), .Pre_Clr_Positions("ABOVE_BELOW"), .NegatePresetClear("false"), .enable("true"), .NewFFLayout("true")) d_ff_1 (
    .clk(CLK), .D(not_3_out), .Q(halt), .en(ecall), .reset(Go));  // open: Qn, preset
  D_Flip_Flop #(.trigger("high"), .Pre_Clr_Positions("LEGACY"), .NegatePresetClear("false"), .enable("true"), .NewFFLayout("false")) d_ff_2 (.Q(d_ff_2_q));  // open: clk, D, Qn, preset, en, reset
  // Probe on 13'h9
  Comparator #(.width(13), .mode("twosComplement")) comparator_2 (
    .a(CNT_num), .b(13'h9), .eq(comparator_2_eq), .lt(comparator_2_lt));  // open: gt
  Clock #(.highDuration(1), .lowDuration(1)) clock_1 (.out(clock_1_out));
  // MIPS_RAM mips_ram_1: pin names not known; wires that end beside it: ALUresult[11:2], MDin, MemWrite, RAM_Sel, CLK, 1'b1, mips_ram_1_p7, mips_ram_1_p8
  Button button_1 (.out(mips_ram_1_p7));
  Counter #(.width(13), .max('h1fff), .ongoal("stay"), .trigger("rising"), .behavior("old")) counter_2 (
    .count(comparator_2_lt), .Q(CNT_num), .clk(clock_1_out));  // open: load, D, carry, clr, preset
  nand nand_1 (nand_1_out, d_ff_2_q, comparator_2_eq);
  or or_5 (\单周期硬布线控制器_1_memtoreg [1], JAL, JALR);
  Multiplexer #(.select(2), .width(32), .disabled("Z"), .enable("false")) multiplexer_8 (
    .in0(ALUresult), .in1(mips_ram_1_p8), .in2(PC_4), .out(multiplexer_8_out), .sel(\单周期硬布线控制器_1_memtoreg ));  // open: in3
  assign CLK = nand_1_out ? clock_1_out : 1'bz;  // Controlled_Buffer controlled_buffer_1
  Pull_Resistor #(.pull(1)) pull_resistor_1 (.node(CLK));
  Shifter #(.width(32), .shift("ll")) shifter_3 (.in(R2), .\dist (5'b10000), .out(shifter_3_out));
  Multiplexer #(.select(1), .width(32), .disabled("Z"), .enable("false")) multiplexer_9 (
    .in0(R2), .in1(shifter_3_out), .out(MDin), .sel(ALUresult[1]));
  Multiplexer #(.select(1), .width(4), .disabled("Z"), .enable("false")) multiplexer_10 (
    .in0(4'b1111), .in1({{2{multiplexer_11_out[3]}}, {2{multiplexer_11_out[1]}}}), .out(RAM_Sel), .sel(SH));
  Multiplexer #(.select(1), .width(1), .disabled("Z"), .enable("false")) multiplexer_11 (
    .in0(1'b1), .in1(1'b0), .out(multiplexer_11_out[1]), .sel(ALUresult[1]));
  Multiplexer #(.select(1), .width(1), .disabled("Z"), .enable("false")) multiplexer_12 (
    .in0(1'b0), .in1(1'b1), .out(multiplexer_11_out[3]), .sel(ALUresult[1]));

  // Other names for the same wires on the sheet: JALR_ADD[31:0] = ALUresult

  // Notes on the sheet:
  //   中断源
  //   中断等待指示
  //   数码管输出应该用寄存器锁存，否则显示数据只能一闪而过
  //   指令存储器
  //   指令探针
  //   指令字
  //   contents of rom_1 (hex, n*v repeats v):
  //   100493 100006f 100493 200913 300993 100006f 100493 200913 300993 100006f 100493 200913 300993
  //   100006f 100493 200913 300993 3a0000ef 100413 100493 1f49493 900533 2200893 73 24d493 48463 fedff06f
  //   900533 2200893 73 100493 249493 900533 2200893 73 48463 fedff06f 100493 1f49493 900533 2200893 73
  //   4034d493 900533 2200893 73 4044d493 900533 2200893 73 4044d493 900533 2200893 73 4044d493 900533
  //   2200893 73 4044d493 900533 2200893 73 4044d493 900533 2200893 73 4044d493 900533 2200893 73 4044d493
  //   900533 2200893 73 100413 1f41993 41f9d993 433 c00913 300b13 140413 f47413 800293 100313 499993
  //   89e9b3 1300533 2200893 73 406282b3 fe0294e3 140413 f00f93 1f47433 1c41413 800293 100313 49d993
  //   89e9b3 1300533 2200893 73 406282b3 fe0294e3 1c45413 406b0b33 b0463 f95ff06f 2b3 fff2c293 829293
  //   ff2e293 500533 2200893 73 fff00413 493 84a023 140413 448493 84a023 140413 448493 84a023 140413
  //   448493 84a023 140413 448493 84a023 140413 448493 84a023 140413 448493 84a023 140413 448493 84a023
  //   140413 448493 84a023 140413 448493 84a023 140413 448493 84a023 140413 448493 84a023 140413 448493
  //   84a023 140413 448493 84a023 140413 448493 84a023 140413 448493 84a023 140413 448493 140413 433
  //   3c00493 42983 4aa03 149a2b3 28663 134a023 1442023 ffc48493 fe9412e3 800533 2200893 73 440413 3c00493
  //   fc9416e3 3200893 73 100293 300313 800493 849493 7648493 1449493 900533 2200893 73 800e13 54d4b3
  //   64d4b3 900533 2200893 73 fffe0e13 fe0e14e3 a00893 73 fff00293 313 1900413 841413 9700493 940533
  //   2200893 73 5484b3 494b313 fe0306e3 a00893 73 313 2000e13 100493 100913 931023 900533 2200893 73
  //   12484b3 230313 fffe0e13 fe0e12e3 1000e13 313 32483 900533 2200893 73 430313 fffe0e13 fe0e14e3 a00893
  //   73 f00493 900533 2200893 73 fff48493 fe04d8e3 a00893 73 a00893 73 413 140413 800533 2200893 73
  //   240413 800533 2200893 73 340413 800533 2200893 73 440413 800533 2200893 73 540413 800533 2200893 73
  //   640413 800533 2200893 73 740413 800533 2200893 73 840413 800533 2200893 2200893 73 8067
  //   JAL
  //   JALR
  //   URET
  //   SRL
  //   rs1
  //   rs2
  //   rd
  //   imm-i
  //   rd
  //   imm-j
  //   beq/bne
  //   jal
  //   Beq
  //   Bne
  //   MemToReg
  //   MemWrite
  //   AluOP
  //   AluSrcB
  //   RegWrite
  //   S_type
  //   SignImm
  //   为方便自动评测，需要输出PC，IR，寄存器堆写如数据RDin
  //   RAM写使能MemWrite、RAM写入数据MDin等信号
  //   控制位
  //   暂停节拍，不能为0
  //   戳工具置1进入计数暂停模式，ctrl+k时钟自动运行到对应节拍暂停
  //   ctrl+k关闭时钟连续运行，将控制位置零，进入单步调试模式调试
  //   用这个时钟源需要去掉电路中的其他时钟源
  //   数据存储器
  //   可计数暂停的时钟源
endmodule

// 单周期硬布线控制器
module \单周期硬布线控制器  (
  input  [4:0] OP,
  input  [4:0] Funct,
  input  in_3,
  output [3:0] ALU_OP,
  output uret,
  output MemToReg,
  output ecall,
  output MemWrite,
  output ALU_SRC,
  output RegWrite,
  output S_type,
  output Beq,
  output Bne,
  output Jalr,
  output JAL,
  output SRL,
  output SLTIU,
  output SH,
  output BGE,
  output rs1_used,
  output rs2_used,
  output CSRRSI,
  output CSRRCI
);

  wire \控制信号自动生成_1_ecall ;

  \运算控制器自动生成  \u_运算控制器自动生成_1  (
    .OP2(OP[0]), .OP3(OP[1]), .OP4(OP[2]), .OP5(OP[3]), .OP6(OP[4]), .F12(Funct[0]), .F13(Funct[1]),
    .F14(Funct[2]), .F25(Funct[3]), .F30(Funct[4]), .S0(ALU_OP[0]), .S1(ALU_OP[1]), .S2(ALU_OP[2]),
    .S3(ALU_OP[3]));
  \控制信号自动生成  \u_控制信号自动生成_1  (
    .OP2(OP[0]), .OP3(OP[1]), .MemToReg(MemToReg), .OP4(OP[2]), .OP5(OP[3]), .OP6(OP[4]), .F12(Funct[0]),
    .F13(Funct[1]), .F14(Funct[2]), .MemWrite(MemWrite), .F25(Funct[3]), .F30(Funct[4]), .ALU_SRC(ALU_SRC),
    .RegWrite(RegWrite), .ecall(\控制信号自动生成_1_ecall ), .S_Type(S_type), .BEQ(Beq), .BNE(Bne), .JALR(Jalr),
    .JAL(JAL), .SRL(SRL), .SLTIU(SLTIU), .SH(SH), .BGE(BGE), .rs1_used(rs1_used), .rs2_used(rs2_used),
    .CSRRSI(CSRRSI), .CSRRCI(CSRRCI));
  and and_1 (uret, in_3, \控制信号自动生成_1_ecall );
  and and_2 (ecall, ~in_3, \控制信号自动生成_1_ecall );  // AND_Gate

  // Other names for the same wires on the sheet: IR21 = in_3; OP_CODE[4:0] = OP

  // Notes on the sheet:
  //   运算器控制器，根据指令生成运算器功能选择信号
  //   控制信号生成，产生数据通路需要的其他控制信号
endmodule

// 运算器控制器
module \运算控制器自动生成  (
  input  OP2,
  input  OP3,
  input  OP4,
  input  OP5,
  input  OP6,
  input  F12,
  input  F13,
  input  F14,
  input  F25,
  input  F30,
  output S0,
  output S1,
  output S2,
  output S3
);

  wire and_1_out, and_2_out, and_3_out, and_4_out, and_5_out, and_6_out, and_7_out, and_8_out, and_9_out,
       and_10_out, and_11_out, and_12_out, and_13_out, and_14_out, and_15_out, and_16_out, and_17_out,
       and_18_out, and_19_out, and_20_out, and_21_out, and_22_out, and_23_out, and_24_out, and_25_out,
       and_26_out, and_27_out, and_28_out, and_29_out, and_30_out, and_31_out, and_32_out, and_33_out,
       and_34_out, and_35_out, and_36_out, and_37_out, and_38_out, and_39_out, and_40_out, and_41_out,
       and_42_out, not_1_out, not_2_out, not_3_out, not_4_out, not_5_out, not_6_out, not_7_out, not_8_out,
       not_9_out, not_10_out, not_11_out, not_12_out, not_13_out, not_14_out, not_15_out, not_16_out,
       not_17_out, not_18_out, not_19_out, not_20_out, not_21_out, not_22_out, not_23_out, not_24_out,
       not_25_out, not_26_out, not_27_out, not_28_out, not_29_out, not_30_out, not_31_out, not_32_out,
       not_33_out, not_34_out, not_35_out, not_36_out, not_37_out, not_38_out, not_39_out, not_40_out,
       not_41_out, not_42_out, not_43_out, not_44_out, not_45_out, not_46_out, not_47_out, not_48_out,
       not_49_out, not_50_out, not_51_out, not_52_out, not_53_out, not_54_out, not_55_out, not_56_out,
       not_57_out, not_58_out, not_59_out, not_60_out, not_61_out, not_62_out, not_63_out, not_64_out,
       not_65_out, not_66_out, not_67_out, not_68_out, not_69_out, not_70_out, not_71_out, not_72_out,
       not_73_out, not_74_out, not_75_out, not_76_out, not_77_out, not_78_out, not_79_out, not_80_out,
       not_81_out, not_82_out, not_83_out, not_84_out, not_85_out, not_86_out, not_87_out, not_88_out,
       not_89_out, not_90_out, not_91_out, not_92_out, not_93_out, not_94_out, not_95_out, not_96_out,
       not_97_out, not_98_out, not_99_out, not_100_out, not_101_out, not_102_out, not_103_out, not_104_out,
       not_105_out, not_106_out, not_107_out, not_108_out, not_109_out, not_110_out, not_111_out,
       not_112_out, not_113_out, not_114_out, not_115_out, not_116_out, not_117_out, not_118_out,
       not_119_out, not_120_out, not_121_out, not_122_out, not_123_out, not_124_out, not_125_out,
       not_126_out, not_127_out, not_128_out, not_129_out, not_130_out, not_131_out, not_132_out,
       not_133_out, not_134_out, not_135_out, not_136_out, not_137_out, not_138_out, not_139_out,
       not_140_out, not_141_out, not_142_out, not_143_out, not_144_out, not_145_out, not_146_out,
       not_147_out, not_148_out, not_149_out, not_150_out, not_151_out, not_152_out, not_153_out,
       not_154_out, not_155_out, not_156_out, not_157_out, not_158_out, not_159_out, not_160_out,
       not_161_out, not_162_out, not_163_out, not_164_out, not_165_out, not_166_out, not_167_out,
       not_168_out, not_169_out, not_170_out, not_171_out, not_172_out, not_173_out, not_174_out,
       not_175_out, not_176_out, not_177_out, not_178_out, not_179_out, not_180_out, not_181_out,
       not_182_out, not_183_out, not_184_out, not_185_out, not_186_out, not_187_out, not_188_out,
       not_189_out, not_190_out, not_191_out, not_192_out, not_193_out, not_194_out, not_195_out,
       not_196_out, not_197_out, not_198_out, not_199_out, not_200_out, not_201_out, not_202_out,
       not_203_out, not_204_out, not_205_out, not_206_out, not_207_out, not_208_out, not_209_out,
       not_210_out, not_211_out, not_212_out, not_213_out, not_214_out, not_215_out, not_216_out,
       not_217_out, not_218_out, not_219_out, not_220_out, not_221_out, not_222_out, not_223_out,
       not_224_out, not_225_out, not_226_out, not_227_out, not_228_out, not_229_out, not_230_out,
       not_231_out, not_232_out, not_233_out, not_234_out, not_235_out, not_236_out, not_237_out,
       not_238_out, not_239_out, not_240_out, not_241_out, not_242_out, not_243_out, not_244_out;

  not not_1 (not_1_out, F30);
  not not_2 (not_2_out, F25);
  not not_3 (not_3_out, F14);
  not not_4 (not_4_out, F13);
  not not_5 (not_5_out, F12);
  not not_6 (not_6_out, OP6);
  not not_7 (not_7_out, OP3);
  not not_8 (not_8_out, OP2);
  not not_9 (not_9_out, F30);
  not not_10 (not_10_out, F25);
  not not_11 (not_11_out, OP6);
  not not_12 (not_12_out, OP3);
  not not_13 (not_13_out, OP2);
  not not_14 (not_14_out, F30);
  not not_15 (not_15_out, F25);
  not not_16 (not_16_out, F14);
  not not_17 (not_17_out, F12);
  not not_18 (not_18_out, OP6);
  not not_19 (not_19_out, OP3);
  not not_20 (not_20_out, OP2);
  not not_21 (not_21_out, F14);
  not not_22 (not_22_out, F13);
  not not_23 (not_23_out, F12);
  not not_24 (not_24_out, OP6);
  not not_25 (not_25_out, OP5);
  not not_26 (not_26_out, OP3);
  not not_27 (not_27_out, OP2);
  not not_28 (not_28_out, OP6);
  not not_29 (not_29_out, OP5);
  not not_30 (not_30_out, OP3);
  not not_31 (not_31_out, OP2);
  not not_32 (not_32_out, F13);
  not not_33 (not_33_out, F12);
  not not_34 (not_34_out, OP6);
  not not_35 (not_35_out, OP5);
  not not_36 (not_36_out, OP3);
  not not_37 (not_37_out, OP2);
  not not_38 (not_38_out, F14);
  not not_39 (not_39_out, F12);
  not not_40 (not_40_out, OP6);
  not not_41 (not_41_out, OP5);
  not not_42 (not_42_out, OP3);
  not not_43 (not_43_out, OP2);
  not not_44 (not_44_out, F25);
  not not_45 (not_45_out, F13);
  not not_46 (not_46_out, OP6);
  not not_47 (not_47_out, OP5);
  not not_48 (not_48_out, OP3);
  not not_49 (not_49_out, OP2);
  not not_50 (not_50_out, F14);
  not not_51 (not_51_out, F12);
  not not_52 (not_52_out, OP6);
  not not_53 (not_53_out, OP5);
  not not_54 (not_54_out, OP4);
  not not_55 (not_55_out, OP3);
  not not_56 (not_56_out, OP2);
  not not_57 (not_57_out, F14);
  not not_58 (not_58_out, F12);
  not not_59 (not_59_out, OP6);
  not not_60 (not_60_out, OP4);
  not not_61 (not_61_out, OP3);
  not not_62 (not_62_out, OP2);
  not not_63 (not_63_out, F14);
  not not_64 (not_64_out, F13);
  not not_65 (not_65_out, F12);
  not not_66 (not_66_out, OP4);
  not not_67 (not_67_out, OP3);
  not not_68 (not_68_out, F13);
  not not_69 (not_69_out, OP4);
  not not_70 (not_70_out, OP3);
  not not_71 (not_71_out, OP2);
  not not_72 (not_72_out, F25);
  not not_73 (not_73_out, F14);
  not not_74 (not_74_out, F13);
  not not_75 (not_75_out, F12);
  not not_76 (not_76_out, OP6);
  not not_77 (not_77_out, OP3);
  not not_78 (not_78_out, OP2);
  not not_79 (not_79_out, F30);
  not not_80 (not_80_out, F25);
  not not_81 (not_81_out, OP6);
  not not_82 (not_82_out, OP3);
  not not_83 (not_83_out, OP2);
  not not_84 (not_84_out, F30);
  not not_85 (not_85_out, F25);
  not not_86 (not_86_out, F14);
  not not_87 (not_87_out, F12);
  not not_88 (not_88_out, OP6);
  not not_89 (not_89_out, OP3);
  not not_90 (not_90_out, OP2);
  not not_91 (not_91_out, OP6);
  not not_92 (not_92_out, OP5);
  not not_93 (not_93_out, OP3);
  not not_94 (not_94_out, OP2);
  not not_95 (not_95_out, F14);
  not not_96 (not_96_out, F12);
  not not_97 (not_97_out, OP6);
  not not_98 (not_98_out, OP5);
  not not_99 (not_99_out, OP3);
  not not_100 (not_100_out, OP2);
  not not_101 (not_101_out, F30);
  not not_102 (not_102_out, F25);
  not not_103 (not_103_out, F13);
  not not_104 (not_104_out, OP6);
  not not_105 (not_105_out, OP5);
  not not_106 (not_106_out, OP3);
  not not_107 (not_107_out, OP2);
  not not_108 (not_108_out, F14);
  not not_109 (not_109_out, F13);
  not not_110 (not_110_out, F12);
  not not_111 (not_111_out, OP4);
  not not_112 (not_112_out, OP3);
  not not_113 (not_113_out, OP2);
  not not_114 (not_114_out, F14);
  not not_115 (not_115_out, F13);
  not not_116 (not_116_out, OP4);
  not not_117 (not_117_out, OP3);
  not not_118 (not_118_out, OP2);
  not not_119 (not_119_out, F30);
  not not_120 (not_120_out, F25);
  not not_121 (not_121_out, F13);
  not not_122 (not_122_out, OP6);
  not not_123 (not_123_out, OP3);
  not not_124 (not_124_out, OP2);
  not not_125 (not_125_out, F13);
  not not_126 (not_126_out, OP4);
  not not_127 (not_127_out, OP3);
  not not_128 (not_128_out, OP2);
  not not_129 (not_129_out, F30);
  not not_130 (not_130_out, F25);
  not not_131 (not_131_out, F14);
  not not_132 (not_132_out, F13);
  not not_133 (not_133_out, F12);
  not not_134 (not_134_out, OP6);
  not not_135 (not_135_out, OP3);
  not not_136 (not_136_out, OP2);
  not not_137 (not_137_out, F25);
  not not_138 (not_138_out, F14);
  not not_139 (not_139_out, F13);
  not not_140 (not_140_out, F12);
  not not_141 (not_141_out, OP6);
  not not_142 (not_142_out, OP3);
  not not_143 (not_143_out, OP2);
  not not_144 (not_144_out, F30);
  not not_145 (not_145_out, F25);
  not not_146 (not_146_out, OP6);
  not not_147 (not_147_out, OP3);
  not not_148 (not_148_out, OP2);
  not not_149 (not_149_out, F30);
  not not_150 (not_150_out, F25);
  not not_151 (not_151_out, F14);
  not not_152 (not_152_out, OP6);
  not not_153 (not_153_out, OP3);
  not not_154 (not_154_out, OP2);
  not not_155 (not_155_out, F14);
  not not_156 (not_156_out, F13);
  not not_157 (not_157_out, F12);
  not not_158 (not_158_out, OP6);
  not not_159 (not_159_out, OP5);
  not not_160 (not_160_out, OP3);
  not not_161 (not_161_out, OP2);
  not not_162 (not_162_out, OP6);
  not not_163 (not_163_out, OP5);
  not not_164 (not_164_out, OP3);
  not not_165 (not_165_out, OP2);
  not not_166 (not_166_out, F14);
  not not_167 (not_167_out, F12);
  not not_168 (not_168_out, OP6);
  not not_169 (not_169_out, OP5);
  not not_170 (not_170_out, OP4);
  not not_171 (not_171_out, OP3);
  not not_172 (not_172_out, OP2);
  not not_173 (not_173_out, F14);
  not not_174 (not_174_out, F12);
  not not_175 (not_175_out, OP6);
  not not_176 (not_176_out, OP4);
  not not_177 (not_177_out, OP3);
  not not_178 (not_178_out, OP2);
  not not_179 (not_179_out, F14);
  not not_180 (not_180_out, F13);
  not not_181 (not_181_out, F12);
  not not_182 (not_182_out, OP4);
  not not_183 (not_183_out, OP3);
  not not_184 (not_184_out, OP2);
  not not_185 (not_185_out, F14);
  not not_186 (not_186_out, F13);
  not not_187 (not_187_out, OP4);
  not not_188 (not_188_out, OP3);
  not not_189 (not_189_out, OP2);
  not not_190 (not_190_out, F14);
  not not_191 (not_191_out, F13);
  not not_192 (not_192_out, F12);
  not not_193 (not_193_out, OP4);
  not not_194 (not_194_out, OP3);
  not not_195 (not_195_out, F14);
  not not_196 (not_196_out, OP6);
  not not_197 (not_197_out, OP5);
  not not_198 (not_198_out, OP3);
  not not_199 (not_199_out, OP2);
  not not_200 (not_200_out, F30);
  not not_201 (not_201_out, F25);
  not not_202 (not_202_out, F12);
  not not_203 (not_203_out, OP6);
  not not_204 (not_204_out, OP3);
  not not_205 (not_205_out, OP2);
  not not_206 (not_206_out, F30);
  not not_207 (not_207_out, F25);
  not not_208 (not_208_out, F14);
  not not_209 (not_209_out, F12);
  not not_210 (not_210_out, OP6);
  not not_211 (not_211_out, OP3);
  not not_212 (not_212_out, OP2);
  not not_213 (not_213_out, F30);
  not not_214 (not_214_out, F25);
  not not_215 (not_215_out, F14);
  not not_216 (not_216_out, OP6);
  not not_217 (not_217_out, OP3);
  not not_218 (not_218_out, OP2);
  not not_219 (not_219_out, F12);
  not not_220 (not_220_out, OP6);
  not not_221 (not_221_out, OP5);
  not not_222 (not_222_out, OP3);
  not not_223 (not_223_out, OP2);
  not not_224 (not_224_out, F13);
  not not_225 (not_225_out, F12);
  not not_226 (not_226_out, OP6);
  not not_227 (not_227_out, OP5);
  not not_228 (not_228_out, OP3);
  not not_229 (not_229_out, OP2);
  not not_230 (not_230_out, F14);
  not not_231 (not_231_out, F12);
  not not_232 (not_232_out, OP6);
  not not_233 (not_233_out, OP5);
  not not_234 (not_234_out, OP3);
  not not_235 (not_235_out, OP2);
  not not_236 (not_236_out, F14);
  not not_237 (not_237_out, OP6);
  not not_238 (not_238_out, OP5);
  not not_239 (not_239_out, OP3);
  not not_240 (not_240_out, OP2);
  not not_241 (not_241_out, F13);
  not not_242 (not_242_out, OP4);
  not not_243 (not_243_out, OP3);
  not not_244 (not_244_out, OP2);
  and and_1 (and_1_out, not_1_out, not_2_out, not_3_out, not_4_out, not_5_out, not_6_out, OP5, OP4, not_7_out, not_8_out);
  and and_2 (and_2_out, not_9_out, not_10_out, F14, F13, F12, not_11_out, OP5, OP4, not_12_out, not_13_out);
  and and_3 (and_3_out, not_14_out, not_15_out, not_16_out, F13, not_17_out, not_18_out, OP5, OP4, not_19_out, not_20_out);
  and and_4 (and_4_out, not_21_out, not_22_out, not_23_out, not_24_out, not_25_out, OP4, not_26_out, not_27_out);
  and and_5 (and_5_out, F14, F13, F12, not_28_out, not_29_out, OP4, not_30_out, not_31_out);
  and and_6 (and_6_out, F14, not_32_out, not_33_out, not_34_out, not_35_out, OP4, not_36_out, not_37_out);
  and and_7 (and_7_out, not_38_out, F13, not_39_out, not_40_out, not_41_out, OP4, not_42_out, not_43_out);
  and and_8 (and_8_out, F30, not_44_out, F14, not_45_out, F12, not_46_out, not_47_out, OP4, not_48_out, not_49_out);
  and and_9 (and_9_out, not_50_out, F13, not_51_out, not_52_out, not_53_out, not_54_out, not_55_out, not_56_out);
  and and_10 (and_10_out, not_57_out, F13, not_58_out, not_59_out, OP5, not_60_out, not_61_out, not_62_out);
  and and_11 (and_11_out, not_63_out, not_64_out, not_65_out, OP6, OP5, not_66_out, not_67_out, OP2);
  and and_12 (and_12_out, F14, not_68_out, F12, OP6, OP5, not_69_out, not_70_out, not_71_out);
  and and_13 (and_13_out, F30, not_72_out, not_73_out, not_74_out, not_75_out, not_76_out, OP5, OP4, not_77_out, not_78_out);
  and and_14 (and_14_out, not_79_out, not_80_out, F14, F13, F12, not_81_out, OP5, OP4, not_82_out, not_83_out);
  and and_15 (and_15_out, not_84_out, not_85_out, not_86_out, F13, not_87_out, not_88_out, OP5, OP4, not_89_out, not_90_out);
  and and_16 (and_16_out, F14, F13, F12, not_91_out, not_92_out, OP4, not_93_out, not_94_out);
  and and_17 (and_17_out, not_95_out, F13, not_96_out, not_97_out, not_98_out, OP4, not_99_out, not_100_out);
  and and_18 (and_18_out, not_101_out, not_102_out, F14, not_103_out, F12, not_104_out, not_105_out, OP4, not_106_out, not_107_out);
  and and_19 (and_19_out, not_108_out, not_109_out, not_110_out, OP6, OP5, not_111_out, not_112_out, not_113_out);
  and and_20 (and_20_out, not_114_out, not_115_out, F12, OP6, OP5, not_116_out, not_117_out, not_118_out);
  and and_21 (and_21_out, not_119_out, not_120_out, F14, not_121_out, F12, not_122_out, OP5, OP4, not_123_out, not_124_out);
  and and_22 (and_22_out, F14, not_125_out, F12, OP6, OP5, not_126_out, not_127_out, not_128_out);
  and and_23 (and_23_out, not_129_out, not_130_out, not_131_out, not_132_out, not_133_out, not_134_out, OP5, OP4, not_135_out, not_136_out);
  and and_24 (and_24_out, F30, not_137_out, not_138_out, not_139_out, not_140_out, not_141_out, OP5, OP4, not_142_out, not_143_out);
  and and_25 (and_25_out, not_144_out, not_145_out, F14, F13, F12, not_146_out, OP5, OP4, not_147_out, not_148_out);
  and and_26 (and_26_out, not_149_out, not_150_out, not_151_out, F13, F12, not_152_out, OP5, OP4, not_153_out, not_154_out);
  and and_27 (and_27_out, not_155_out, not_156_out, not_157_out, not_158_out, not_159_out, OP4, not_160_out, not_161_out);
  and and_28 (and_28_out, F14, F13, F12, not_162_out, not_163_out, OP4, not_164_out, not_165_out);
  and and_29 (and_29_out, not_166_out, F13, not_167_out, not_168_out, not_169_out, not_170_out, not_171_out, not_172_out);
  and and_30 (and_30_out, not_173_out, F13, not_174_out, not_175_out, OP5, not_176_out, not_177_out, not_178_out);
  and and_31 (and_31_out, not_179_out, not_180_out, not_181_out, OP6, OP5, not_182_out, not_183_out, not_184_out);
  and and_32 (and_32_out, not_185_out, not_186_out, F12, OP6, OP5, not_187_out, not_188_out, not_189_out);
  and and_33 (and_33_out, not_190_out, not_191_out, not_192_out, OP6, OP5, not_193_out, not_194_out, OP2);
  and and_34 (and_34_out, not_195_out, F13, F12, not_196_out, not_197_out, OP4, not_198_out, not_199_out);
  and and_35 (and_35_out, not_200_out, not_201_out, F14, F13, not_202_out, not_203_out, OP5, OP4, not_204_out, not_205_out);
  and and_36 (and_36_out, not_206_out, not_207_out, not_208_out, F13, not_209_out, not_210_out, OP5, OP4, not_211_out, not_212_out);
  and and_37 (and_37_out, not_213_out, not_214_out, not_215_out, F13, F12, not_216_out, OP5, OP4, not_217_out, not_218_out);
  and and_38 (and_38_out, F14, F13, not_219_out, not_220_out, not_221_out, OP4, not_222_out, not_223_out);
  and and_39 (and_39_out, F14, not_224_out, not_225_out, not_226_out, not_227_out, OP4, not_228_out, not_229_out);
  and and_40 (and_40_out, not_230_out, F13, not_231_out, not_232_out, not_233_out, OP4, not_234_out, not_235_out);
  and and_41 (and_41_out, not_236_out, F13, F12, not_237_out, not_238_out, OP4, not_239_out, not_240_out);
  and and_42 (and_42_out, F14, not_241_out, F12, OP6, OP5, not_242_out, not_243_out, not_244_out);
  or or_1 (S0, and_1_out, and_2_out, and_3_out, and_4_out, and_5_out, and_6_out, and_7_out, and_8_out, and_9_out, and_10_out, and_11_out, and_12_out);
  or or_2 (S1, and_13_out, and_14_out, and_15_out, and_16_out, and_17_out, and_18_out, and_19_out, and_20_out, and_21_out, and_22_out);
  or or_3 (S2, and_23_out, and_24_out, and_25_out, and_26_out, and_27_out, and_28_out, and_29_out, and_30_out, and_31_out, and_32_out, and_33_out, and_34_out);
  or or_4 (S3, and_35_out, and_36_out, and_37_out, and_38_out, and_39_out, and_40_out, and_41_out, and_42_out);
endmodule

// 控制信号生成
module \控制信号自动生成  (
  input  OP2,
  input  OP3,
  input  OP4,
  input  OP5,
  input  OP6,
  input  F12,
  input  F13,
  input  F14,
  input  F25,
  input  F30,
  output MemToReg,
  output MemWrite,
  output ALU_SRC,
  output RegWrite,
  output ecall,
  output S_Type,
  output BEQ,
  output BNE,
  output JALR,
  output JAL,
  output SRL,
  output SLTIU,
  output SH,
  output BGE,
  output rs1_used,
  output rs2_used,
  output CSRRSI,
  output CSRRCI
);

  wire and_2_out, and_3_out, and_4_out, and_5_out, and_6_out, and_7_out, and_8_out, and_9_out, and_10_out,
       and_11_out, and_12_out, and_13_out, and_14_out, and_15_out, and_16_out, and_17_out, and_18_out,
       and_19_out, and_20_out, and_21_out, and_22_out, and_23_out, and_24_out, and_25_out, and_26_out,
       and_27_out, and_28_out, and_29_out, and_30_out, and_31_out, and_32_out, and_33_out, and_34_out,
       and_35_out, and_37_out, and_38_out, and_47_out, and_48_out, and_49_out, and_50_out, and_51_out,
       and_52_out, and_53_out, and_54_out, and_55_out, and_56_out, and_57_out, and_58_out, and_59_out,
       and_60_out, and_61_out, and_62_out, and_63_out, and_64_out, and_65_out, and_66_out, and_67_out,
       and_68_out, and_69_out, and_70_out, and_71_out, and_72_out, and_73_out, and_74_out, and_75_out,
       and_76_out, and_77_out, and_78_out, and_79_out, and_80_out, and_81_out, and_82_out, and_83_out,
       not_1_out, not_2_out, not_3_out, not_4_out, not_5_out, not_6_out, not_7_out, not_8_out, not_9_out,
       not_10_out, not_11_out, not_12_out, not_13_out, not_14_out, not_15_out, not_16_out, not_17_out,
       not_18_out, not_19_out, not_20_out, not_21_out, not_22_out, not_23_out, not_24_out, not_25_out,
       not_26_out, not_27_out, not_28_out, not_29_out, not_30_out, not_31_out, not_32_out, not_33_out,
       not_34_out, not_35_out, not_36_out, not_37_out, not_38_out, not_39_out, not_40_out, not_41_out,
       not_42_out, not_43_out, not_44_out, not_45_out, not_46_out, not_47_out, not_48_out, not_49_out,
       not_50_out, not_51_out, not_52_out, not_53_out, not_54_out, not_55_out, not_56_out, not_57_out,
       not_58_out, not_59_out, not_60_out, not_61_out, not_62_out, not_63_out, not_64_out, not_65_out,
       not_66_out, not_67_out, not_68_out, not_69_out, not_70_out, not_71_out, not_72_out, not_73_out,
       not_74_out, not_75_out, not_76_out, not_77_out, not_78_out, not_79_out, not_80_out, not_81_out,
       not_82_out, not_83_out, not_84_out, not_85_out, not_86_out, not_87_out, not_88_out, not_89_out,
       not_90_out, not_91_out, not_92_out, not_93_out, not_94_out, not_95_out, not_96_out, not_97_out,
       not_98_out, not_99_out, not_100_out, not_101_out, not_102_out, not_103_out, not_104_out, not_105_out,
       not_106_out, not_107_out, not_108_out, not_109_out, not_110_out, not_111_out, not_112_out,
       not_113_out, not_114_out, not_115_out, not_116_out, not_117_out, not_118_out, not_119_out,
       not_120_out, not_121_out, not_122_out, not_123_out, not_124_out, not_125_out, not_126_out,
       not_127_out, not_128_out, not_129_out, not_130_out, not_131_out, not_132_out, not_133_out,
       not_134_out, not_135_out, not_136_out, not_137_out, not_138_out, not_139_out, not_140_out,
       not_141_out, not_142_out, not_143_out, not_144_out, not_145_out, not_146_out, not_147_out,
       not_148_out, not_149_out, not_150_out, not_151_out, not_152_out, not_153_out, not_154_out,
       not_155_out, not_156_out, not_157_out, not_158_out, not_159_out, not_160_out, not_161_out,
       not_162_out, not_163_out, not_164_out, not_165_out, not_166_out, not_167_out, not_168_out,
       not_169_out, not_170_out, not_171_out, not_172_out, not_173_out, not_174_out, not_175_out,
       not_176_out, not_177_out, not_178_out, not_179_out, not_180_out, not_181_out, not_182_out,
       not_183_out, not_184_out, not_185_out, not_186_out, not_187_out, not_188_out, not_189_out,
       not_190_out, not_191_out, not_192_out, not_193_out, not_194_out, not_195_out, not_196_out,
       not_197_out, not_198_out, not_199_out, not_200_out, not_201_out, not_202_out, not_203_out,
       not_204_out, not_205_out, not_206_out, not_207_out, not_208_out, not_209_out, not_210_out,
       not_211_out, not_212_out, not_213_out, not_214_out, not_215_out, not_216_out, not_217_out,
       not_218_out, not_219_out, not_220_out, not_221_out, not_222_out, not_223_out, not_224_out,
       not_225_out, not_226_out, not_227_out, not_228_out, not_229_out, not_230_out, not_231_out,
       not_232_out, not_233_out, not_234_out, not_235_out, not_236_out, not_237_out, not_238_out,
       not_239_out, not_240_out, not_241_out, not_242_out, not_243_out, not_244_out, not_245_out,
       not_246_out, not_247_out, not_248_out, not_249_out, not_250_out, not_251_out, not_252_out,
       not_253_out, not_254_out, not_255_out, not_256_out, not_257_out, not_258_out, not_259_out,
       not_260_out, not_261_out, not_262_out, not_263_out, not_264_out, not_265_out, not_266_out,
       not_267_out, not_268_out, not_269_out, not_270_out, not_271_out, not_272_out, not_273_out,
       not_274_out, not_275_out, not_276_out, not_277_out, not_278_out, not_279_out, not_280_out,
       not_281_out, not_282_out, not_283_out, not_284_out, not_285_out, not_286_out, not_287_out,
       not_288_out, not_289_out, not_290_out, not_291_out, not_292_out, not_293_out, not_294_out,
       not_295_out, not_296_out, not_297_out, not_298_out, not_299_out, not_300_out, not_301_out,
       not_302_out, not_303_out, not_304_out, not_305_out, not_306_out, not_307_out, not_308_out,
       not_309_out, not_310_out, not_311_out, not_312_out, not_313_out, not_314_out, not_315_out,
       not_316_out, not_317_out, not_318_out, not_319_out, not_320_out, not_321_out, not_322_out,
       not_323_out, not_324_out, not_325_out, not_326_out, not_327_out, not_328_out, not_329_out,
       not_330_out, not_331_out, not_332_out, not_333_out, not_334_out, not_335_out, not_336_out,
       not_337_out, not_338_out, not_339_out, not_340_out, not_341_out, not_342_out, not_343_out,
       not_344_out, not_345_out, not_346_out, not_347_out, not_348_out, not_349_out, not_350_out,
       not_351_out, not_352_out, not_353_out, not_354_out, not_355_out, not_356_out, not_357_out,
       not_358_out, not_359_out, not_360_out, not_361_out, not_362_out, not_363_out, not_364_out,
       not_365_out, not_366_out, not_367_out, not_368_out, not_369_out, not_370_out, not_371_out,
       not_372_out, not_373_out, not_374_out, not_375_out, not_376_out, not_377_out, not_378_out,
       not_379_out, not_380_out, not_381_out, not_382_out, not_383_out, not_384_out, not_385_out,
       not_386_out, not_387_out, not_388_out, not_389_out, not_390_out, not_391_out, not_392_out,
       not_393_out, not_394_out, not_395_out, not_396_out, not_397_out, not_398_out, not_399_out,
       not_400_out, not_401_out, not_402_out, not_403_out, not_404_out, not_405_out, not_406_out,
       not_407_out, not_408_out, not_409_out, not_410_out, not_411_out, not_412_out, not_413_out,
       not_414_out, not_415_out, not_416_out, not_417_out, not_418_out, not_419_out, not_420_out,
       not_421_out, not_422_out, not_423_out, not_424_out, not_425_out, not_426_out, not_427_out,
       not_428_out, not_429_out, not_430_out, not_431_out, not_432_out, not_433_out, not_434_out,
       not_435_out, not_436_out, not_437_out, not_438_out, not_439_out, not_440_out, not_441_out,
       not_442_out, not_443_out, not_444_out, not_445_out, not_446_out, not_447_out, not_448_out,
       not_449_out, not_450_out, not_451_out, not_452_out, not_453_out, not_454_out, not_455_out,
       not_456_out, not_457_out, not_458_out, not_459_out, not_460_out, not_461_out, not_462_out,
       not_463_out, not_464_out, not_465_out, not_466_out, not_467_out, not_468_out, not_469_out,
       not_470_out, not_471_out, not_472_out, not_473_out, not_474_out, not_475_out, not_476_out,
       not_477_out, not_478_out, not_479_out, not_480_out, not_481_out, not_482_out, not_483_out,
       not_484_out, not_485_out, not_486_out;

  not not_1 (not_1_out, F14);
  not not_2 (not_2_out, F12);
  not not_3 (not_3_out, OP6);
  not not_4 (not_4_out, OP5);
  not not_5 (not_5_out, OP4);
  not not_6 (not_6_out, OP3);
  not not_7 (not_7_out, OP2);
  not not_8 (not_8_out, F14);
  not not_9 (not_9_out, F12);
  not not_10 (not_10_out, OP6);
  not not_11 (not_11_out, OP4);
  not not_12 (not_12_out, OP3);
  not not_13 (not_13_out, OP2);
  not not_14 (not_14_out, F14);
  not not_15 (not_15_out, F13);
  not not_16 (not_16_out, OP6);
  not not_17 (not_17_out, OP4);
  not not_18 (not_18_out, OP3);
  not not_19 (not_19_out, OP2);
  not not_20 (not_20_out, F14);
  not not_21 (not_21_out, F13);
  not not_22 (not_22_out, F12);
  not not_23 (not_23_out, OP6);
  not not_24 (not_24_out, OP5);
  not not_25 (not_25_out, OP3);
  not not_26 (not_26_out, OP2);
  not not_27 (not_27_out, OP6);
  not not_28 (not_28_out, OP5);
  not not_29 (not_29_out, OP3);
  not not_30 (not_30_out, OP2);
  not not_31 (not_31_out, F12);
  not not_32 (not_32_out, OP6);
  not not_33 (not_33_out, OP5);
  not not_34 (not_34_out, OP3);
  not not_35 (not_35_out, OP2);
  not not_36 (not_36_out, F13);
  not not_37 (not_37_out, F12);
  not not_38 (not_38_out, OP6);
  not not_39 (not_39_out, OP5);
  not not_40 (not_40_out, OP3);
  not not_41 (not_41_out, OP2);
  not not_42 (not_42_out, F14);
  not not_43 (not_43_out, F12);
  not not_44 (not_44_out, OP6);
  not not_45 (not_45_out, OP5);
  not not_46 (not_46_out, OP3);
  not not_47 (not_47_out, OP2);
  not not_48 (not_48_out, F30);
  not not_49 (not_49_out, F25);
  not not_50 (not_50_out, F14);
  not not_51 (not_51_out, F13);
  not not_52 (not_52_out, OP6);
  not not_53 (not_53_out, OP5);
  not not_54 (not_54_out, OP3);
  not not_55 (not_55_out, OP2);
  not not_56 (not_56_out, F30);
  not not_57 (not_57_out, F25);
  not not_58 (not_58_out, F13);
  not not_59 (not_59_out, OP6);
  not not_60 (not_60_out, OP5);
  not not_61 (not_61_out, OP3);
  not not_62 (not_62_out, OP2);
  not not_63 (not_63_out, F25);
  not not_64 (not_64_out, F13);
  not not_65 (not_65_out, OP6);
  not not_66 (not_66_out, OP5);
  not not_67 (not_67_out, OP3);
  not not_68 (not_68_out, OP2);
  not not_69 (not_69_out, F14);
  not not_70 (not_70_out, F12);
  not not_71 (not_71_out, OP6);
  not not_72 (not_72_out, OP5);
  not not_73 (not_73_out, OP4);
  not not_74 (not_74_out, OP3);
  not not_75 (not_75_out, OP2);
  not not_76 (not_76_out, F14);
  not not_77 (not_77_out, F12);
  not not_78 (not_78_out, OP6);
  not not_79 (not_79_out, OP4);
  not not_80 (not_80_out, OP3);
  not not_81 (not_81_out, OP2);
  not not_82 (not_82_out, F14);
  not not_83 (not_83_out, F13);
  not not_84 (not_84_out, F12);
  not not_85 (not_85_out, OP4);
  not not_86 (not_86_out, OP3);
  not not_87 (not_87_out, F14);
  not not_88 (not_88_out, OP6);
  not not_89 (not_89_out, OP5);
  not not_90 (not_90_out, OP3);
  not not_91 (not_91_out, OP2);
  not not_92 (not_92_out, F14);
  not not_93 (not_93_out, F13);
  not not_94 (not_94_out, OP6);
  not not_95 (not_95_out, OP4);
  not not_96 (not_96_out, OP3);
  not not_97 (not_97_out, OP2);
  not not_98 (not_98_out, F30);
  not not_99 (not_99_out, F25);
  not not_100 (not_100_out, F14);
  not not_101 (not_101_out, F13);
  not not_102 (not_102_out, F12);
  not not_103 (not_103_out, OP6);
  not not_104 (not_104_out, OP3);
  not not_105 (not_105_out, OP2);
  not not_106 (not_106_out, F25);
  not not_107 (not_107_out, F14);
  not not_108 (not_108_out, F13);
  not not_109 (not_109_out, F12);
  not not_110 (not_110_out, OP6);
  not not_111 (not_111_out, OP3);
  not not_112 (not_112_out, OP2);
  not not_113 (not_113_out, F30);
  not not_114 (not_114_out, F25);
  not not_115 (not_115_out, OP6);
  not not_116 (not_116_out, OP3);
  not not_117 (not_117_out, OP2);
  not not_118 (not_118_out, F30);
  not not_119 (not_119_out, F25);
  not not_120 (not_120_out, F12);
  not not_121 (not_121_out, OP6);
  not not_122 (not_122_out, OP3);
  not not_123 (not_123_out, OP2);
  not not_124 (not_124_out, F30);
  not not_125 (not_125_out, F25);
  not not_126 (not_126_out, F14);
  not not_127 (not_127_out, F12);
  not not_128 (not_128_out, OP6);
  not not_129 (not_129_out, OP3);
  not not_130 (not_130_out, OP2);
  not not_131 (not_131_out, F30);
  not not_132 (not_132_out, F25);
  not not_133 (not_133_out, F14);
  not not_134 (not_134_out, OP6);
  not not_135 (not_135_out, OP3);
  not not_136 (not_136_out, OP2);
  not not_137 (not_137_out, F14);
  not not_138 (not_138_out, F13);
  not not_139 (not_139_out, F12);
  not not_140 (not_140_out, OP6);
  not not_141 (not_141_out, OP5);
  not not_142 (not_142_out, OP3);
  not not_143 (not_143_out, OP2);
  not not_144 (not_144_out, OP6);
  not not_145 (not_145_out, OP5);
  not not_146 (not_146_out, OP3);
  not not_147 (not_147_out, OP2);
  not not_148 (not_148_out, F12);
  not not_149 (not_149_out, OP6);
  not not_150 (not_150_out, OP5);
  not not_151 (not_151_out, OP3);
  not not_152 (not_152_out, OP2);
  not not_153 (not_153_out, F13);
  not not_154 (not_154_out, F12);
  not not_155 (not_155_out, OP6);
  not not_156 (not_156_out, OP5);
  not not_157 (not_157_out, OP3);
  not not_158 (not_158_out, OP2);
  not not_159 (not_159_out, F14);
  not not_160 (not_160_out, F12);
  not not_161 (not_161_out, OP6);
  not not_162 (not_162_out, OP5);
  not not_163 (not_163_out, OP3);
  not not_164 (not_164_out, OP2);
  not not_165 (not_165_out, F30);
  not not_166 (not_166_out, F25);
  not not_167 (not_167_out, F14);
  not not_168 (not_168_out, F13);
  not not_169 (not_169_out, OP6);
  not not_170 (not_170_out, OP5);
  not not_171 (not_171_out, OP3);
  not not_172 (not_172_out, OP2);
  not not_173 (not_173_out, F30);
  not not_174 (not_174_out, F25);
  not not_175 (not_175_out, F13);
  not not_176 (not_176_out, OP6);
  not not_177 (not_177_out, OP5);
  not not_178 (not_178_out, OP3);
  not not_179 (not_179_out, OP2);
  not not_180 (not_180_out, F25);
  not not_181 (not_181_out, F13);
  not not_182 (not_182_out, OP6);
  not not_183 (not_183_out, OP5);
  not not_184 (not_184_out, OP3);
  not not_185 (not_185_out, OP2);
  not not_186 (not_186_out, F14);
  not not_187 (not_187_out, F12);
  not not_188 (not_188_out, OP6);
  not not_189 (not_189_out, OP5);
  not not_190 (not_190_out, OP4);
  not not_191 (not_191_out, OP3);
  not not_192 (not_192_out, OP2);
  not not_193 (not_193_out, OP4);
  not not_194 (not_194_out, F14);
  not not_195 (not_195_out, F13);
  not not_196 (not_196_out, F12);
  not not_197 (not_197_out, OP4);
  not not_198 (not_198_out, OP3);
  not not_199 (not_199_out, F30);
  not not_200 (not_200_out, F25);
  not not_201 (not_201_out, F13);
  not not_202 (not_202_out, OP6);
  not not_203 (not_203_out, OP3);
  not not_204 (not_204_out, OP2);
  not not_205 (not_205_out, F14);
  not not_206 (not_206_out, OP6);
  not not_207 (not_207_out, OP5);
  not not_208 (not_208_out, OP3);
  not not_209 (not_209_out, OP2);
  not not_210 (not_210_out, F30);
  not not_211 (not_211_out, F25);
  not not_212 (not_212_out, F14);
  not not_213 (not_213_out, F13);
  not not_214 (not_214_out, F12);
  not not_215 (not_215_out, OP3);
  not not_216 (not_216_out, OP2);
  not not_217 (not_217_out, F14);
  not not_218 (not_218_out, F12);
  not not_219 (not_219_out, OP6);
  not not_220 (not_220_out, OP4);
  not not_221 (not_221_out, OP3);
  not not_222 (not_222_out, OP2);
  not not_223 (not_223_out, F14);
  not not_224 (not_224_out, F13);
  not not_225 (not_225_out, OP6);
  not not_226 (not_226_out, OP4);
  not not_227 (not_227_out, OP3);
  not not_228 (not_228_out, OP2);
  not not_229 (not_229_out, F14);
  not not_230 (not_230_out, F13);
  not not_231 (not_231_out, F12);
  not not_232 (not_232_out, OP4);
  not not_233 (not_233_out, OP3);
  not not_234 (not_234_out, OP2);
  not not_235 (not_235_out, F14);
  not not_236 (not_236_out, F13);
  not not_237 (not_237_out, OP4);
  not not_238 (not_238_out, OP3);
  not not_239 (not_239_out, OP2);
  not not_240 (not_240_out, F14);
  not not_241 (not_241_out, F13);
  not not_242 (not_242_out, F12);
  not not_243 (not_243_out, OP4);
  not not_244 (not_244_out, OP3);
  not not_245 (not_245_out, OP4);
  not not_246 (not_246_out, F30);
  not not_247 (not_247_out, F25);
  not not_248 (not_248_out, F13);
  not not_249 (not_249_out, OP6);
  not not_250 (not_250_out, OP3);
  not not_251 (not_251_out, OP2);
  not not_252 (not_252_out, F14);
  not not_253 (not_253_out, OP6);
  not not_254 (not_254_out, OP5);
  not not_255 (not_255_out, OP3);
  not not_256 (not_256_out, OP2);
  not not_257 (not_257_out, F14);
  not not_258 (not_258_out, F13);
  not not_259 (not_259_out, OP6);
  not not_260 (not_260_out, OP4);
  not not_261 (not_261_out, OP3);
  not not_262 (not_262_out, OP2);
  not not_263 (not_263_out, F13);
  not not_264 (not_264_out, OP4);
  not not_265 (not_265_out, OP3);
  not not_266 (not_266_out, OP2);
  not not_267 (not_267_out, F30);
  not not_268 (not_268_out, F25);
  not not_269 (not_269_out, F14);
  not not_270 (not_270_out, F13);
  not not_271 (not_271_out, F12);
  not not_272 (not_272_out, OP6);
  not not_273 (not_273_out, OP3);
  not not_274 (not_274_out, OP2);
  not not_275 (not_275_out, F25);
  not not_276 (not_276_out, F14);
  not not_277 (not_277_out, F13);
  not not_278 (not_278_out, F12);
  not not_279 (not_279_out, OP6);
  not not_280 (not_280_out, OP3);
  not not_281 (not_281_out, OP2);
  not not_282 (not_282_out, F30);
  not not_283 (not_283_out, F25);
  not not_284 (not_284_out, OP6);
  not not_285 (not_285_out, OP3);
  not not_286 (not_286_out, OP2);
  not not_287 (not_287_out, F30);
  not not_288 (not_288_out, F25);
  not not_289 (not_289_out, F12);
  not not_290 (not_290_out, OP6);
  not not_291 (not_291_out, OP3);
  not not_292 (not_292_out, OP2);
  not not_293 (not_293_out, F30);
  not not_294 (not_294_out, F25);
  not not_295 (not_295_out, F14);
  not not_296 (not_296_out, F12);
  not not_297 (not_297_out, OP6);
  not not_298 (not_298_out, OP3);
  not not_299 (not_299_out, OP2);
  not not_300 (not_300_out, F30);
  not not_301 (not_301_out, F25);
  not not_302 (not_302_out, F14);
  not not_303 (not_303_out, OP6);
  not not_304 (not_304_out, OP3);
  not not_305 (not_305_out, OP2);
  not not_306 (not_306_out, F14);
  not not_307 (not_307_out, F13);
  not not_308 (not_308_out, F12);
  not not_309 (not_309_out, OP6);
  not not_310 (not_310_out, OP5);
  not not_311 (not_311_out, OP3);
  not not_312 (not_312_out, OP2);
  not not_313 (not_313_out, OP6);
  not not_314 (not_314_out, OP5);
  not not_315 (not_315_out, OP3);
  not not_316 (not_316_out, OP2);
  not not_317 (not_317_out, F12);
  not not_318 (not_318_out, OP6);
  not not_319 (not_319_out, OP5);
  not not_320 (not_320_out, OP3);
  not not_321 (not_321_out, OP2);
  not not_322 (not_322_out, F13);
  not not_323 (not_323_out, F12);
  not not_324 (not_324_out, OP6);
  not not_325 (not_325_out, OP5);
  not not_326 (not_326_out, OP3);
  not not_327 (not_327_out, OP2);
  not not_328 (not_328_out, F14);
  not not_329 (not_329_out, F12);
  not not_330 (not_330_out, OP6);
  not not_331 (not_331_out, OP5);
  not not_332 (not_332_out, OP3);
  not not_333 (not_333_out, OP2);
  not not_334 (not_334_out, F30);
  not not_335 (not_335_out, F25);
  not not_336 (not_336_out, F14);
  not not_337 (not_337_out, F13);
  not not_338 (not_338_out, OP6);
  not not_339 (not_339_out, OP5);
  not not_340 (not_340_out, OP3);
  not not_341 (not_341_out, OP2);
  not not_342 (not_342_out, F30);
  not not_343 (not_343_out, F25);
  not not_344 (not_344_out, F13);
  not not_345 (not_345_out, OP6);
  not not_346 (not_346_out, OP5);
  not not_347 (not_347_out, OP3);
  not not_348 (not_348_out, OP2);
  not not_349 (not_349_out, F25);
  not not_350 (not_350_out, F13);
  not not_351 (not_351_out, OP6);
  not not_352 (not_352_out, OP5);
  not not_353 (not_353_out, OP3);
  not not_354 (not_354_out, OP2);
  not not_355 (not_355_out, F14);
  not not_356 (not_356_out, F12);
  not not_357 (not_357_out, OP6);
  not not_358 (not_358_out, OP5);
  not not_359 (not_359_out, OP4);
  not not_360 (not_360_out, OP3);
  not not_361 (not_361_out, OP2);
  not not_362 (not_362_out, F14);
  not not_363 (not_363_out, F12);
  not not_364 (not_364_out, OP6);
  not not_365 (not_365_out, OP4);
  not not_366 (not_366_out, OP3);
  not not_367 (not_367_out, OP2);
  not not_368 (not_368_out, F14);
  not not_369 (not_369_out, F13);
  not not_370 (not_370_out, F12);
  not not_371 (not_371_out, OP4);
  not not_372 (not_372_out, OP3);
  not not_373 (not_373_out, OP2);
  not not_374 (not_374_out, F14);
  not not_375 (not_375_out, F13);
  not not_376 (not_376_out, OP4);
  not not_377 (not_377_out, OP3);
  not not_378 (not_378_out, OP2);
  not not_379 (not_379_out, F14);
  not not_380 (not_380_out, F13);
  not not_381 (not_381_out, F12);
  not not_382 (not_382_out, OP4);
  not not_383 (not_383_out, OP3);
  not not_384 (not_384_out, F12);
  not not_385 (not_385_out, OP3);
  not not_386 (not_386_out, OP2);
  not not_387 (not_387_out, OP3);
  not not_388 (not_388_out, OP2);
  not not_389 (not_389_out, F30);
  not not_390 (not_390_out, F25);
  not not_391 (not_391_out, F13);
  not not_392 (not_392_out, OP6);
  not not_393 (not_393_out, OP3);
  not not_394 (not_394_out, OP2);
  not not_395 (not_395_out, F14);
  not not_396 (not_396_out, OP6);
  not not_397 (not_397_out, OP5);
  not not_398 (not_398_out, OP3);
  not not_399 (not_399_out, OP2);
  not not_400 (not_400_out, F14);
  not not_401 (not_401_out, F13);
  not not_402 (not_402_out, OP6);
  not not_403 (not_403_out, OP4);
  not not_404 (not_404_out, OP3);
  not not_405 (not_405_out, OP2);
  not not_406 (not_406_out, F13);
  not not_407 (not_407_out, OP4);
  not not_408 (not_408_out, OP3);
  not not_409 (not_409_out, OP2);
  not not_410 (not_410_out, F30);
  not not_411 (not_411_out, F25);
  not not_412 (not_412_out, F14);
  not not_413 (not_413_out, F13);
  not not_414 (not_414_out, F12);
  not not_415 (not_415_out, OP6);
  not not_416 (not_416_out, OP3);
  not not_417 (not_417_out, OP2);
  not not_418 (not_418_out, F25);
  not not_419 (not_419_out, F14);
  not not_420 (not_420_out, F13);
  not not_421 (not_421_out, F12);
  not not_422 (not_422_out, OP6);
  not not_423 (not_423_out, OP3);
  not not_424 (not_424_out, OP2);
  not not_425 (not_425_out, F30);
  not not_426 (not_426_out, F25);
  not not_427 (not_427_out, OP6);
  not not_428 (not_428_out, OP3);
  not not_429 (not_429_out, OP2);
  not not_430 (not_430_out, F30);
  not not_431 (not_431_out, F25);
  not not_432 (not_432_out, F12);
  not not_433 (not_433_out, OP6);
  not not_434 (not_434_out, OP3);
  not not_435 (not_435_out, OP2);
  not not_436 (not_436_out, F30);
  not not_437 (not_437_out, F25);
  not not_438 (not_438_out, F14);
  not not_439 (not_439_out, F12);
  not not_440 (not_440_out, OP6);
  not not_441 (not_441_out, OP3);
  not not_442 (not_442_out, OP2);
  not not_443 (not_443_out, F30);
  not not_444 (not_444_out, F25);
  not not_445 (not_445_out, F14);
  not not_446 (not_446_out, OP6);
  not not_447 (not_447_out, OP3);
  not not_448 (not_448_out, OP2);
  not not_449 (not_449_out, F14);
  not not_450 (not_450_out, F12);
  not not_451 (not_451_out, OP6);
  not not_452 (not_452_out, OP4);
  not not_453 (not_453_out, OP3);
  not not_454 (not_454_out, OP2);
  not not_455 (not_455_out, F14);
  not not_456 (not_456_out, F13);
  not not_457 (not_457_out, F12);
  not not_458 (not_458_out, OP4);
  not not_459 (not_459_out, OP3);
  not not_460 (not_460_out, OP2);
  not not_461 (not_461_out, F14);
  not not_462 (not_462_out, F13);
  not not_463 (not_463_out, OP4);
  not not_464 (not_464_out, OP3);
  not not_465 (not_465_out, OP2);
  not not_466 (not_466_out, F30);
  not not_467 (not_467_out, F25);
  not not_468 (not_468_out, F13);
  not not_469 (not_469_out, OP6);
  not not_470 (not_470_out, OP3);
  not not_471 (not_471_out, OP2);
  not not_472 (not_472_out, F14);
  not not_473 (not_473_out, F13);
  not not_474 (not_474_out, OP6);
  not not_475 (not_475_out, OP4);
  not not_476 (not_476_out, OP3);
  not not_477 (not_477_out, OP2);
  not not_478 (not_478_out, F13);
  not not_479 (not_479_out, OP4);
  not not_480 (not_480_out, OP3);
  not not_481 (not_481_out, OP2);
  not not_482 (not_482_out, F12);
  not not_483 (not_483_out, OP3);
  not not_484 (not_484_out, OP2);
  not not_485 (not_485_out, OP3);
  not not_486 (not_486_out, OP2);
  and and_1 (MemToReg, not_1_out, F13, not_2_out, not_3_out, not_4_out, not_5_out, not_6_out, not_7_out);
  and and_2 (and_2_out, not_8_out, F13, not_9_out, not_10_out, OP5, not_11_out, not_12_out, not_13_out);
  and and_3 (and_3_out, not_14_out, not_15_out, F12, not_16_out, OP5, not_17_out, not_18_out, not_19_out);
  and and_4 (and_4_out, not_20_out, not_21_out, not_22_out, not_23_out, not_24_out, OP4, not_25_out, not_26_out);
  and and_5 (and_5_out, F14, F13, F12, not_27_out, not_28_out, OP4, not_29_out, not_30_out);
  and and_6 (and_6_out, F14, F13, not_31_out, not_32_out, not_33_out, OP4, not_34_out, not_35_out);
  and and_7 (and_7_out, F14, not_36_out, not_37_out, not_38_out, not_39_out, OP4, not_40_out, not_41_out);
  and and_8 (and_8_out, not_42_out, F13, not_43_out, not_44_out, not_45_out, OP4, not_46_out, not_47_out);
  and and_9 (and_9_out, not_48_out, not_49_out, not_50_out, not_51_out, F12, not_52_out, not_53_out, OP4, not_54_out, not_55_out);
  and and_10 (and_10_out, not_56_out, not_57_out, F14, not_58_out, F12, not_59_out, not_60_out, OP4, not_61_out, not_62_out);
  and and_11 (and_11_out, F30, not_63_out, F14, not_64_out, F12, not_65_out, not_66_out, OP4, not_67_out, not_68_out);
  and and_12 (and_12_out, not_69_out, F13, not_70_out, not_71_out, not_72_out, not_73_out, not_74_out, not_75_out);
  and and_13 (and_13_out, not_76_out, F13, not_77_out, not_78_out, OP5, not_79_out, not_80_out, not_81_out);
  and and_14 (and_14_out, not_82_out, not_83_out, not_84_out, OP6, OP5, not_85_out, not_86_out, OP2);
  and and_15 (and_15_out, not_87_out, F13, F12, not_88_out, not_89_out, OP4, not_90_out, not_91_out);
  and and_16 (and_16_out, not_92_out, not_93_out, F12, not_94_out, OP5, not_95_out, not_96_out, not_97_out);
  and and_17 (and_17_out, not_98_out, not_99_out, not_100_out, not_101_out, not_102_out, not_103_out, OP5, OP4, not_104_out, not_105_out);
  and and_18 (and_18_out, F30, not_106_out, not_107_out, not_108_out, not_109_out, not_110_out, OP5, OP4, not_111_out, not_112_out);
  and and_19 (and_19_out, not_113_out, not_114_out, F14, F13, F12, not_115_out, OP5, OP4, not_116_out, not_117_out);
  and and_20 (and_20_out, not_118_out, not_119_out, F14, F13, not_120_out, not_121_out, OP5, OP4, not_122_out, not_123_out);
  and and_21 (and_21_out, not_124_out, not_125_out, not_126_out, F13, not_127_out, not_128_out, OP5, OP4, not_129_out, not_130_out);
  and and_22 (and_22_out, not_131_out, not_132_out, not_133_out, F13, F12, not_134_out, OP5, OP4, not_135_out, not_136_out);
  and and_23 (and_23_out, not_137_out, not_138_out, not_139_out, not_140_out, not_141_out, OP4, not_142_out, not_143_out);
  and and_24 (and_24_out, F14, F13, F12, not_144_out, not_145_out, OP4, not_146_out, not_147_out);
  and and_25 (and_25_out, F14, F13, not_148_out, not_149_out, not_150_out, OP4, not_151_out, not_152_out);
  and and_26 (and_26_out, F14, not_153_out, not_154_out, not_155_out, not_156_out, OP4, not_157_out, not_158_out);
  and and_27 (and_27_out, not_159_out, F13, not_160_out, not_161_out, not_162_out, OP4, not_163_out, not_164_out);
  and and_28 (and_28_out, not_165_out, not_166_out, not_167_out, not_168_out, F12, not_169_out, not_170_out, OP4, not_171_out, not_172_out);
  and and_29 (and_29_out, not_173_out, not_174_out, F14, not_175_out, F12, not_176_out, not_177_out, OP4, not_178_out, not_179_out);
  and and_30 (and_30_out, F30, not_180_out, F14, not_181_out, F12, not_182_out, not_183_out, OP4, not_184_out, not_185_out);
  and and_31 (and_31_out, not_186_out, F13, not_187_out, not_188_out, not_189_out, not_190_out, not_191_out, not_192_out);
  and and_32 (and_32_out, OP6, OP5, not_193_out, OP3, OP2);
  and and_33 (and_33_out, not_194_out, not_195_out, not_196_out, OP6, OP5, not_197_out, not_198_out, OP2);
  and and_34 (and_34_out, not_199_out, not_200_out, F14, not_201_out, F12, not_202_out, OP5, OP4, not_203_out, not_204_out);
  and and_35 (and_35_out, not_205_out, F13, F12, not_206_out, not_207_out, OP4, not_208_out, not_209_out);
  and and_36 (ecall, not_210_out, not_211_out, not_212_out, not_213_out, not_214_out, OP6, OP5, OP4, not_215_out, not_216_out);
  and and_37 (and_37_out, not_217_out, F13, not_218_out, not_219_out, OP5, not_220_out, not_221_out, not_222_out);
  and and_38 (and_38_out, not_223_out, not_224_out, F12, not_225_out, OP5, not_226_out, not_227_out, not_228_out);
  and and_39 (BEQ, not_229_out, not_230_out, not_231_out, OP6, OP5, not_232_out, not_233_out, not_234_out);
  and and_40 (BNE, not_235_out, not_236_out, F12, OP6, OP5, not_237_out, not_238_out, not_239_out);
  and and_41 (JALR, not_240_out, not_241_out, not_242_out, OP6, OP5, not_243_out, not_244_out, OP2);
  and and_42 (JAL, OP6, OP5, not_245_out, OP3, OP2);
  and and_43 (SRL, not_246_out, not_247_out, F14, not_248_out, F12, not_249_out, OP5, OP4, not_250_out, not_251_out);
  and and_44 (SLTIU, not_252_out, F13, F12, not_253_out, not_254_out, OP4, not_255_out, not_256_out);
  and and_45 (SH, not_257_out, not_258_out, F12, not_259_out, OP5, not_260_out, not_261_out, not_262_out);
  and and_46 (BGE, F14, not_263_out, F12, OP6, OP5, not_264_out, not_265_out, not_266_out);
  and and_47 (and_47_out, not_267_out, not_268_out, not_269_out, not_270_out, not_271_out, not_272_out, OP5, OP4, not_273_out, not_274_out);
  and and_48 (and_48_out, F30, not_275_out, not_276_out, not_277_out, not_278_out, not_279_out, OP5, OP4, not_280_out, not_281_out);
  and and_49 (and_49_out, not_282_out, not_283_out, F14, F13, F12, not_284_out, OP5, OP4, not_285_out, not_286_out);
  and and_50 (and_50_out, not_287_out, not_288_out, F14, F13, not_289_out, not_290_out, OP5, OP4, not_291_out, not_292_out);
  and and_51 (and_51_out, not_293_out, not_294_out, not_295_out, F13, not_296_out, not_297_out, OP5, OP4, not_298_out, not_299_out);
  and and_52 (and_52_out, not_300_out, not_301_out, not_302_out, F13, F12, not_303_out, OP5, OP4, not_304_out, not_305_out);
  and and_53 (and_53_out, not_306_out, not_307_out, not_308_out, not_309_out, not_310_out, OP4, not_311_out, not_312_out);
  and and_54 (and_54_out, F14, F13, F12, not_313_out, not_314_out, OP4, not_315_out, not_316_out);
  and and_55 (and_55_out, F14, F13, not_317_out, not_318_out, not_319_out, OP4, not_320_out, not_321_out);
  and and_56 (and_56_out, F14, not_322_out, not_323_out, not_324_out, not_325_out, OP4, not_326_out, not_327_out);
  and and_57 (and_57_out, not_328_out, F13, not_329_out, not_330_out, not_331_out, OP4, not_332_out, not_333_out);
  and and_58 (and_58_out, not_334_out, not_335_out, not_336_out, not_337_out, F12, not_338_out, not_339_out, OP4, not_340_out, not_341_out);
  and and_59 (and_59_out, not_342_out, not_343_out, F14, not_344_out, F12, not_345_out, not_346_out, OP4, not_347_out, not_348_out);
  and and_60 (and_60_out, F30, not_349_out, F14, not_350_out, F12, not_351_out, not_352_out, OP4, not_353_out, not_354_out);
  and and_61 (and_61_out, not_355_out, F13, not_356_out, not_357_out, not_358_out, not_359_out, not_360_out, not_361_out);
  and and_62 (and_62_out, not_362_out, F13, not_363_out, not_364_out, OP5, not_365_out, not_366_out, not_367_out);
  and and_63 (and_63_out, not_368_out, not_369_out, not_370_out, OP6, OP5, not_371_out, not_372_out, not_373_out);
  and and_64 (and_64_out, not_374_out, not_375_out, F12, OP6, OP5, not_376_out, not_377_out, not_378_out);
  and and_65 (and_65_out, not_379_out, not_380_out, not_381_out, OP6, OP5, not_382_out, not_383_out, OP2);
  and and_66 (and_66_out, F14, F13, not_384_out, OP6, OP5, OP4, not_385_out, not_386_out);
  and and_67 (and_67_out, F14, F13, F12, OP6, OP5, OP4, not_387_out, not_388_out);
  and and_68 (and_68_out, not_389_out, not_390_out, F14, not_391_out, F12, not_392_out, OP5, OP4, not_393_out, not_394_out);
  and and_69 (and_69_out, not_395_out, F13, F12, not_396_out, not_397_out, OP4, not_398_out, not_399_out);
  and and_70 (and_70_out, not_400_out, not_401_out, F12, not_402_out, OP5, not_403_out, not_404_out, not_405_out);
  and and_71 (and_71_out, F14, not_406_out, F12, OP6, OP5, not_407_out, not_408_out, not_409_out);
  and and_72 (and_72_out, not_410_out, not_411_out, not_412_out, not_413_out, not_414_out, not_415_out, OP5, OP4, not_416_out, not_417_out);
  and and_73 (and_73_out, F30, not_418_out, not_419_out, not_420_out, not_421_out, not_422_out, OP5, OP4, not_423_out, not_424_out);
  and and_74 (and_74_out, not_425_out, not_426_out, F14, F13, F12, not_427_out, OP5, OP4, not_428_out, not_429_out);
  and and_75 (and_75_out, not_430_out, not_431_out, F14, F13, not_432_out, not_433_out, OP5, OP4, not_434_out, not_435_out);
  and and_76 (and_76_out, not_436_out, not_437_out, not_438_out, F13, not_439_out, not_440_out, OP5, OP4, not_441_out, not_442_out);
  and and_77 (and_77_out, not_443_out, not_444_out, not_445_out, F13, F12, not_446_out, OP5, OP4, not_447_out, not_448_out);
  and and_78 (and_78_out, not_449_out, F13, not_450_out, not_451_out, OP5, not_452_out, not_453_out, not_454_out);
  and and_79 (and_79_out, not_455_out, not_456_out, not_457_out, OP6, OP5, not_458_out, not_459_out, not_460_out);
  and and_80 (and_80_out, not_461_out, not_462_out, F12, OP6, OP5, not_463_out, not_464_out, not_465_out);
  and and_81 (and_81_out, not_466_out, not_467_out, F14, not_468_out, F12, not_469_out, OP5, OP4, not_470_out, not_471_out);
  and and_82 (and_82_out, not_472_out, not_473_out, F12, not_474_out, OP5, not_475_out, not_476_out, not_477_out);
  and and_83 (and_83_out, F14, not_478_out, F12, OP6, OP5, not_479_out, not_480_out, not_481_out);
  and and_84 (CSRRSI, F14, F13, not_482_out, OP6, OP5, OP4, not_483_out, not_484_out);
  and and_85 (CSRRCI, F14, F13, F12, OP6, OP5, OP4, not_485_out, not_486_out);
  or or_1 (MemWrite, and_2_out, and_3_out);
  or or_2 (S_Type, and_37_out, and_38_out);
  or or_3 (ALU_SRC, and_4_out, and_5_out, and_6_out, and_7_out, and_8_out, and_9_out, and_10_out, and_11_out, and_12_out, and_13_out, and_14_out, and_15_out, and_16_out);
  or or_4 (RegWrite, and_17_out, and_18_out, and_19_out, and_20_out, and_21_out, and_22_out, and_23_out, and_24_out, and_25_out, and_26_out, and_27_out, and_28_out, and_29_out, and_30_out, and_31_out, and_32_out, and_33_out, and_34_out, and_35_out);
  or or_5 (rs2_used, and_72_out, and_73_out, and_74_out, and_75_out, and_76_out, and_77_out, and_78_out, and_79_out, and_80_out, and_81_out, and_82_out, and_83_out);
  or or_6 (rs1_used, and_47_out, and_48_out, and_49_out, and_50_out, and_51_out, and_52_out, and_53_out, and_54_out, and_55_out, and_56_out, and_57_out, and_58_out, and_59_out, and_60_out, and_61_out, and_62_out, and_63_out, and_64_out, and_65_out, and_66_out, and_67_out, and_68_out, and_69_out, and_70_out, and_71_out);
endmodule

// ALU
module ALU (
  input  [31:0] X,
  input  [31:0] Y,
  input  [3:0] AluOP,
  output out_4,
  output Equal,
  output out_6,
  output [31:0] Result,
  output [31:0] Result_2
);

  wire [0:0] comparator_1_lt, comparator_2_lt;
  wire [31:0] adder_1_out, AND_out, divider_1_out, divider_1_rem, multiplier_1_cout, multiplier_1_out,
       NOR_out, OR_out, shifter_1_out, shifter_2_out, shifter_3_out, subtractor_1_out, XOR_out;

  assign AND_out = X & Y;  // AND_Gate AND, 32 bits wide
  assign OR_out = X | Y;  // OR_Gate OR, 32 bits wide
  Shifter #(.width(32), .shift("ll")) shifter_1 (.in(X), .\dist (Y[4:0]), .out(shifter_1_out));
  Shifter #(.width(32), .shift("ar")) shifter_2 (.in(X), .\dist (Y[4:0]), .out(shifter_2_out));
  Shifter #(.width(32), .shift("lr")) shifter_3 (.in(X), .\dist (Y[4:0]), .out(shifter_3_out));
  Multiplier #(.width(32)) multiplier_1 (.a(X), .b(Y), .out(multiplier_1_out), .cout(multiplier_1_cout));  // open: cin
  Divider #(.width(32)) divider_1 (.a(X), .b(Y), .out(divider_1_out), .rem(divider_1_rem));  // open: upper
  Adder #(.width(32)) adder_1 (.a(X), .b(Y), .out(adder_1_out));  // open: cin, cout
  Subtractor #(.width(32)) subtractor_1 (.a(X), .b(Y), .out(subtractor_1_out));  // open: bin, bout
  assign XOR_out = X ^ Y;  // XOR_Gate XOR, 32 bits wide
  assign NOR_out = ~(X | Y);  // NOR_Gate NOR, 32 bits wide
  Comparator #(.width(32), .mode("twosComplement")) comparator_1 (
    .a(X), .b(Y), .eq(Equal), .lt(comparator_1_lt[0]));  // open: gt
  Comparator #(.width(32), .mode("unsigned")) comparator_2 (.a(X), .b(Y), .lt(comparator_2_lt[0]));  // open: gt, eq
  Multiplexer #(.select(4), .width(32), .disabled("Z"), .enable("false")) multiplexer_1 (
    .in0(shifter_1_out), .in1(shifter_2_out), .in2(shifter_3_out), .in3(multiplier_1_out),
    .in4(divider_1_out), .in5(adder_1_out), .in6(subtractor_1_out), .in7(AND_out), .in8(OR_out),
    .in9(XOR_out), .in10(NOR_out), .in11({{31{1'b0}}, comparator_1_lt[0]}),
    .in12({{31{1'b0}}, comparator_2_lt[0]}), .in13({32{1'b0}}), .in14({32{1'b0}}), .in15({32{1'b0}}),
    .out(Result), .sel(AluOP));
  Multiplexer #(.select(4), .width(32), .disabled("Z"), .enable("false")) multiplexer_2 (
    .in0({32{1'b0}}), .in1({32{1'b0}}), .in2({32{1'b0}}), .in3(multiplier_1_cout), .in4(divider_1_rem),
    .in5({32{1'b0}}), .in6({32{1'b0}}), .in7({32{1'b0}}), .in8({32{1'b0}}), .in9({32{1'b0}}),
    .in10({32{1'b0}}), .in11({32{1'b0}}), .in12({32{1'b0}}), .in13({32{1'b0}}), .in14({32{1'b0}}),
    .in15({32{1'b0}}), .out(Result_2), .sel(AluOP));
  Multiplexer #(.select(4), .width(1), .disabled("Z"), .enable("false")) multiplexer_3 (
    .in0(1'b0), .in1(1'b0), .in2(1'b0), .in3(1'b0), .in4(1'b0), .in5(1'b0), .in6(1'b0), .in7(1'b0),
    .in8(1'b0), .in9(1'b0), .in10(1'b0), .in11(comparator_1_lt[0]), .in12(comparator_2_lt[0]), .in13(1'b0),
    .in14(1'b0), .in15(1'b0), .out(out_6), .sel(AluOP));
  not not_1 (out_4, out_6);

  // Other names for the same wires on the sheet: Result2[31:0] = Result_2; S[3:0] = AluOP; tunnel = out_6;
  //   tunnel_t = out_4

  // Notes on the sheet:
  //   不要改变此引脚区域内容，也不要改变ALU封装形式
  //   输入引脚
  //   输出引脚
endmodule

module Regifile (
  input  [31:0] Din,
  input  Clk,
  input  WE,
  input  [4:0] R1_num,
  input  [4:0] W_num,
  input  [4:0] R2_num,
  output [31:0] R1,
  output [31:0] R2
);

  // RegisterFile registerfile_1: pin names not known; wires that end beside it: Din, Clk, WE, W_num, R1_num, R2_num, R1, R2
endmodule

module \理想流水线  (
  output RegWrite,
  output MemWrite,
  output [31:0] IF_PC,
  output [31:0] ID_PC,
  output [31:0] EX_PC,
  output [31:0] M_PC,
  output [31:0] WB_PC,
  output [31:0] RDin,
  output [31:0] MDin,
  output [31:0] LedData
);

  wire ALU, alu_1_equal, alu_1_out_4, and_3_out, and_4_out, and_5_out, and_6_out, BGE, CLK, clock_1_out,
       comparator_1_eq, comparator_1_lt, comparator_2_eq, d_ff_1_q, ecall, EX_ecall, EX_halt, ex_mem_1_alu_2,
       ex_mem_1_halt_2, ex_mem_1_jal_2, ex_mem_1_jalr_2, ex_mem_1_memtoreg_2, ex_mem_1_regwrite_2,
       ex_mem_1_sltiu_2, Go, halt, id_ex_1_alusrc_2, id_ex_1_beq_2, id_ex_1_bge_2, id_ex_1_bne_2,
       id_ex_1_jal_2, id_ex_1_memtoreg_2, id_ex_1_menwrite, id_ex_1_regwrite_2, id_ex_1_sh_2,
       id_ex_1_sltiu_2, IR1, IR2, IR3, MEM_SH, mem_wb_1_halt_2, mem_wb_1_jal_2, mem_wb_1_jalr_2, nand_1_out,
       not_1_out, not_2_out, not_3_out, or_3_out, RST, SH, SLTIU, SRL, W1, W2, W3, WB_ALU, WB_SLTIU,
       \单周期硬布线控制器_1_alu_src , \单周期硬布线控制器_1_beq , \单周期硬布线控制器_1_bne , \单周期硬布线控制器_1_jal , \单周期硬布线控制器_1_jalr ,
       \单周期硬布线控制器_1_memtoreg , \单周期硬布线控制器_1_memwrite , \单周期硬布线控制器_1_regwrite , \单周期硬布线控制器_1_s_type ,
       \单周期硬布线控制器_1_uret ;
  wire [1:0] id_ex_1_jalr_2, mem_wb_1_memtoreg_2;
  wire [3:0] id_ex_1_alu_op_2, RAM_Sel, \单周期硬布线控制器_1_alu_op ;
  wire [3:1] multiplexer_9_out;
  wire [4:0] ex_mem_1_rd_2, id_ex_1_rd_2, multiplexer_2_out, multiplexer_3_out, WB_rd;
  wire [11:0] multiplexer_4_out;
  wire [12:0] CNT_num;
  wire [15:0] \LoadUse次数 , \总周期数 , \插入气泡数 , \无条件分支数 , \条件分支成功数 ;
  wire [31:0] adder_2_out, adder_3_out, Alu_add, and_1_out, bit_extender_1_out, bit_extender_2_out,
       bit_extender_3_out, Branch_add, EX_IR, ex_mem_1_pc_4_2, EX_R1, EX_R2, id_ex_1_imm1_2, id_ex_1_imm2b_2,
       id_ex_1_imm2j_2, id_ex_1_pc_4_2, ID_IR, if_id_1_pc_4_2, IF_IR, MEM_ALUresult, MEM_IR, MEM_R2,
       mem_wb_1_aluresult_2, mem_wb_1_pc_4_2, mem_wb_1_readdata_2, mips_ram_1_p8, multiplexer_1_out,
       multiplexer_5_out, multiplexer_11_out, multiplexer_13_out, PC_4, regifile_1_r1, regifile_1_r2,
       shifter_1_out, shifter_2_out, shifter_3_out, WB_IR;

  Button \u_总复位  (.out(RST));
  Button _1 (.out(IR1));
  Button _2 (.out(IR2));
  Button _3 (.out(IR3));
  // Probe on \总周期数 
  // Probe on \总周期数 
  Button \u_继续运行  (.out(Go));
  LED #(.active("true")) led_1 (.in(W1));
  LED #(.active("true")) led_2 (.in(W2));
  LED #(.active("true")) led_3 (.in(W3));
  Hex_Digit_Display hex_digit_display_1 (.value(LedData[31:28]));  // open: dp
  // Probe on IF_PC[19:0]
  // RiscV_Probe riscv_probe_1: pin names not known; wires that end beside it: IF_IR
  assign and_1_out = Alu_add & 32'hfffffffe;  // AND_Gate and_1, 32 bits wide
  Hex_Digit_Display hex_digit_display_2 (.value(LedData[23:20]));  // open: dp
  Hex_Digit_Display hex_digit_display_3 (.value(LedData[27:24]));  // open: dp
  // Probe on ID_PC[19:0]
  // RiscV_Probe riscv_probe_2: pin names not known; wires that end beside it: ID_IR
  Multiplexer #(.select(2), .width(32), .disabled("Z"), .enable("false")) multiplexer_1 (
    .in0(PC_4), .in1(and_1_out), .in2(Branch_add), .out(multiplexer_1_out), .sel(id_ex_1_jalr_2));  // open: in3
  Hex_Digit_Display hex_digit_display_4 (.value(LedData[15:12]));  // open: dp
  Hex_Digit_Display hex_digit_display_5 (.value(LedData[19:16]));  // open: dp
  not not_1 (not_1_out, halt);
  Hex_Digit_Display hex_digit_display_6 (.value(LedData[11:8]));  // open: dp
  Hex_Digit_Display hex_digit_display_7 (.value(LedData[7:4]));  // open: dp
  // Probe on EX_PC[19:0]
  // RiscV_Probe riscv_probe_3: pin names not known; wires that end beside it: EX_IR
  Register #(.width(32), .trigger("rising"), .Select("low")) PC (
    .D(multiplexer_1_out), .en(not_1_out), .Q(IF_PC), .clk(CLK), .clr(RST));
  Hex_Digit_Display hex_digit_display_8 (.value(LedData[3:0]));  // open: dp
  Adder #(.width(32)) adder_1 (.a(IF_PC), .b(32'h4), .out(PC_4), .cin(1'b0));  // open: cout
  // Probe on \总周期数 
  // Probe on M_PC[19:0]
  // RiscV_Probe riscv_probe_4: pin names not known; wires that end beside it: MEM_IR
  // Probe on \总周期数 
  // Probe on \无条件分支数 
  // Probe on \条件分支成功数 
  // Probe on \插入气泡数 
  // Probe on \LoadUse次数 
  not not_2 (not_2_out, halt);
  // Probe on IF_PC[11:0]
  // Probe on WB_PC[19:0]
  // RiscV_Probe riscv_probe_5: pin names not known; wires that end beside it: WB_IR
  // RiscV_Probe riscv_probe_6: pin names not known; wires that end beside it: IF_IR, PC_4
  ROM #(.addrWidth(10), .dataWidth(32), .Select("high")) rom_1 (.addr(IF_PC[11:2]), .data(IF_IR));
  Counter #(.width(16), .max('hffff), .ongoal("wrap"), .trigger("rising"), .behavior("new")) counter_1 (
    .count(not_2_out), .Q(\总周期数 ), .clk(CLK));  // open: load, D, carry, clr, preset, down
  // Probe on EX_PC[11:0]
  // Probe on ID_PC[11:0]
  // Probe on M_PC[11:0]
  D_Flip_Flop #(.trigger("high"), .Pre_Clr_Positions("LEGACY"), .NegatePresetClear("false"), .enable("true"), .NewFFLayout("false")) d_ff_1 (.Q(d_ff_1_q));  // open: clk, D, Qn, preset, en, reset
  // Probe on 13'h4
  IF_ID if_id_1 (
    .IR(IF_IR), .PC(IF_PC), .PC_4(PC_4), .IR_2(ID_IR), .PC_2(ID_PC), .PC_4_2(if_id_1_pc_4_2), .reset(RST),
    .BranchTaken(1'b0), .en(1'b1), .clk(CLK));  // open: PredictJump, PredictJump_2
  // Probe on WB_PC[11:0]
  Comparator #(.width(13), .mode("twosComplement")) comparator_1 (
    .a(CNT_num), .b(13'h4), .eq(comparator_1_eq), .lt(comparator_1_lt));  // open: gt
  Clock #(.highDuration(1), .lowDuration(1)) clock_1 (.out(clock_1_out));
  nand nand_1 (nand_1_out, d_ff_1_q, comparator_1_eq);
  Counter #(.width(13), .max('h1fff), .ongoal("stay"), .trigger("rising"), .behavior("old")) counter_2 (
    .count(comparator_1_lt), .Q(CNT_num), .clk(clock_1_out));  // open: load, D, carry, clr, preset
  \单周期硬布线控制器  \u_单周期硬布线控制器_1  (
    .Funct({ID_IR[30], ID_IR[25], ID_IR[14:12]}), .OP(ID_IR[6:2]), .ALU_OP(\单周期硬布线控制器_1_alu_op ),
    .MemToReg(\单周期硬布线控制器_1_memtoreg ), .MemWrite(\单周期硬布线控制器_1_memwrite ), .ALU_SRC(\单周期硬布线控制器_1_alu_src ),
    .RegWrite(\单周期硬布线控制器_1_regwrite ), .ecall(ecall), .S_type(\单周期硬布线控制器_1_s_type ),
    .Jalr(\单周期硬布线控制器_1_jalr ), .Beq(\单周期硬布线控制器_1_beq ), .JAL(\单周期硬布线控制器_1_jal ), .Bne(\单周期硬布线控制器_1_bne ),
    .in_3(ID_IR[21]), .uret(\单周期硬布线控制器_1_uret ), .SRL(SRL), .SLTIU(SLTIU), .SH(SH), .BGE(BGE));  // open: rs1_used, rs2_used, CSRRSI, CSRRCI
  assign CLK = nand_1_out ? clock_1_out : 1'bz;  // Controlled_Buffer controlled_buffer_1
  Multiplexer #(.select(1), .width(5), .disabled("Z"), .enable("false")) multiplexer_2 (
    .in0(ID_IR[19:15]), .in1(5'b10001), .out(multiplexer_2_out), .sel(ecall));
  Multiplexer #(.select(1), .width(5), .disabled("Z"), .enable("false")) multiplexer_3 (
    .in0(ID_IR[24:20]), .in1(5'b01010), .out(multiplexer_3_out), .sel(ecall));
  assign bit_extender_1_out = {{20{ID_IR[31]}}, {ID_IR[31], ID_IR[7], ID_IR[30:25], ID_IR[11:8]}};  // Bit_Extender bit_extender_1
  assign bit_extender_2_out = {{12{ID_IR[31]}}, {ID_IR[31], ID_IR[19:12], ID_IR[20], ID_IR[30:21]}};  // Bit_Extender bit_extender_2
  Pull_Resistor #(.pull(1)) pull_resistor_1 (.node(CLK));
  Multiplexer #(.select(1), .width(12), .disabled("Z"), .enable("false")) multiplexer_4 (
    .in0(ID_IR[31:20]), .in1({ID_IR[31:25], ID_IR[11:7]}), .out(multiplexer_4_out), .sel(\单周期硬布线控制器_1_s_type ));
  assign bit_extender_3_out = {{20{multiplexer_4_out[11]}}, multiplexer_4_out};  // Bit_Extender bit_extender_3
  Regifile regifile_1 (
    .Din(RDin), .Clk(CLK), .R1(regifile_1_r1), .R2(regifile_1_r2), .WE(RegWrite), .W_num(WB_rd),
    .R1_num(multiplexer_2_out), .R2_num(multiplexer_3_out));
  ID_EX id_ex_1 (
    .Beq(\单周期硬布线控制器_1_beq ), .Bne(\单周期硬布线控制器_1_bne ), .MemToReg(\单周期硬布线控制器_1_memtoreg ),
    .MemWrite(\单周期硬布线控制器_1_memwrite ), .AluSrc(\单周期硬布线控制器_1_alu_src ), .RegWrite(\单周期硬布线控制器_1_regwrite ),
    .SType(\单周期硬布线控制器_1_s_type ), .ecall(ecall), .Jal(\单周期硬布线控制器_1_jal ), .Jalr(\单周期硬布线控制器_1_jalr ),
    .SLTIU(SLTIU), .SH(SH), .BGE(BGE), .ALU_OP(\单周期硬布线控制器_1_alu_op ), .rd(ID_IR[11:7]), .R1(regifile_1_r1),
    .R2(regifile_1_r2), .imm1(bit_extender_3_out), .IR(ID_IR), .PC(ID_PC), .PC_4(if_id_1_pc_4_2),
    .Beq_2(id_ex_1_beq_2), .Bne_2(id_ex_1_bne_2), .MemToReg_2(id_ex_1_memtoreg_2),
    .MenWrite(id_ex_1_menwrite), .AluSrc_2(id_ex_1_alusrc_2), .RegWrite_2(id_ex_1_regwrite_2),
    .ecall_2(EX_ecall), .Jal_2(id_ex_1_jal_2), .Jalr_2(id_ex_1_jalr_2[0]), .SLTIU_2(id_ex_1_sltiu_2),
    .SH_2(id_ex_1_sh_2), .BGE_2(id_ex_1_bge_2), .ALU_OP_2(id_ex_1_alu_op_2), .rd_2(id_ex_1_rd_2),
    .R1_2(EX_R1), .R2_2(EX_R2), .imm1_2(id_ex_1_imm1_2), .IR_2(EX_IR), .PC_2(EX_PC), .PC_4_2(id_ex_1_pc_4_2),
    .Reset(RST), .Flush(1'b0), .en(1'b1), .clk(CLK), .imm2j(bit_extender_2_out), .imm2j_2(id_ex_1_imm2j_2),
    .imm2b(bit_extender_1_out), .imm2b_2(id_ex_1_imm2b_2));  // open: RS1_Forward, RS2_Forward, SType_2, RS1_Forward_2, RS2_Forward_2, URET, URET_2, PredictJump, PredictJump_2
  Shifter #(.width(32), .shift("ll")) shifter_1 (.in(id_ex_1_imm2b_2), .\dist (5'b00001), .out(shifter_1_out));
  Shifter #(.width(32), .shift("ll")) shifter_2 (.in(id_ex_1_imm2j_2), .\dist (5'b00001), .out(shifter_2_out));
  Comparator #(.width(32), .mode("twosComplement")) comparator_2 (
    .a(EX_R1), .b(32'h22), .eq(comparator_2_eq));  // open: gt, lt
  Multiplexer #(.select(1), .width(32), .disabled("Z"), .enable("false")) multiplexer_5 (
    .in0(EX_R2), .in1(id_ex_1_imm1_2), .out(multiplexer_5_out), .sel(id_ex_1_alusrc_2));
  Adder #(.width(32)) adder_2 (.a(shifter_1_out), .b(EX_PC), .out(adder_2_out));  // open: cin, cout
  Adder #(.width(32)) adder_3 (.a(shifter_2_out), .b(EX_PC), .out(adder_3_out));  // open: cin, cout
  and and_2 (EX_halt, EX_ecall, not_3_out);
  not not_3 (not_3_out, comparator_2_eq);
  Register #(.width(32), .trigger("rising"), .Select("low")) PC_2 (
    .D(EX_R2), .en(and_3_out), .Q(LedData), .clk(CLK));  // open: clr
  and and_3 (and_3_out, comparator_2_eq, EX_ecall);
  or or_1 (id_ex_1_jalr_2[1], id_ex_1_jal_2, and_5_out, and_4_out, and_6_out);
  and and_4 (and_4_out, ~alu_1_equal, id_ex_1_bne_2);  // AND_Gate
  and and_5 (and_5_out, id_ex_1_beq_2, alu_1_equal);
  ALU alu_1 (
    .X(EX_R1), .Y(multiplexer_5_out), .AluOP(id_ex_1_alu_op_2), .Equal(alu_1_equal), .Result(Alu_add),
    .out_4(alu_1_out_4), .out_6(ALU));  // open: Result_2
  Multiplexer #(.select(1), .width(32), .disabled("Z"), .enable("false")) multiplexer_6 (
    .in0(adder_2_out), .in1(adder_3_out), .out(Branch_add), .sel(id_ex_1_jal_2));
  and and_6 (and_6_out, id_ex_1_bge_2, alu_1_out_4);
  EX_MEM ex_mem_1 (
    .Jal(id_ex_1_jal_2), .Jalr(id_ex_1_jalr_2[0]), .MemToReg(id_ex_1_memtoreg_2),
    .MemWrite(id_ex_1_menwrite), .RegWrite(id_ex_1_regwrite_2), .Halt(EX_halt), .SLTIU(id_ex_1_sltiu_2),
    .SH(id_ex_1_sh_2), .ALU(ALU), .rd(id_ex_1_rd_2), .result(Alu_add), .WriteData(EX_R2), .IR(EX_IR),
    .PC(EX_PC), .PC_4(id_ex_1_pc_4_2), .Jal_2(ex_mem_1_jal_2), .Jalr_2(ex_mem_1_jalr_2),
    .MemToReg_2(ex_mem_1_memtoreg_2), .MemWrite_2(MemWrite), .RegWrite_2(ex_mem_1_regwrite_2),
    .Halt_2(ex_mem_1_halt_2), .SLTIU_2(ex_mem_1_sltiu_2), .SH_2(MEM_SH), .ALU_2(ex_mem_1_alu_2),
    .rd_2(ex_mem_1_rd_2), .result_2(MEM_ALUresult), .Writedata_2(MEM_R2), .IR_2(MEM_IR), .PC_2(M_PC),
    .PC_4_2(ex_mem_1_pc_4_2), .reset(RST), .en(1'b1), .clk(CLK));  // open: URET, URET_2
  Multiplexer #(.select(1), .width(32), .disabled("Z"), .enable("false")) multiplexer_7 (
    .in0(MEM_R2), .in1(shifter_3_out), .out(MDin), .sel(MEM_ALUresult[1]));
  Shifter #(.width(32), .shift("ll")) shifter_3 (.in(MEM_R2), .\dist (5'b10000), .out(shifter_3_out));
  // MIPS_RAM mips_ram_1: pin names not known; wires that end beside it: MEM_ALUresult[11:2], MDin, MemWrite, RAM_Sel, CLK, 1'b1, RST, mips_ram_1_p8
  Multiplexer #(.select(1), .width(4), .disabled("Z"), .enable("false")) multiplexer_8 (
    .in0(4'b1111), .in1({{2{multiplexer_9_out[3]}}, {2{multiplexer_9_out[1]}}}), .out(RAM_Sel), .sel(MEM_SH));
  Multiplexer #(.select(1), .width(1), .disabled("Z"), .enable("false")) multiplexer_9 (
    .in0(1'b1), .in1(1'b0), .out(multiplexer_9_out[1]), .sel(MEM_ALUresult[1]));
  MEM_WB mem_wb_1 (
    .Jal(ex_mem_1_jal_2), .Jalr(ex_mem_1_jalr_2), .MemToReg(ex_mem_1_memtoreg_2),
    .RegWrite(ex_mem_1_regwrite_2), .Halt(ex_mem_1_halt_2), .rd(ex_mem_1_rd_2), .AluResult(MEM_ALUresult),
    .ReadData(mips_ram_1_p8), .IR(MEM_IR), .PC(M_PC), .PC_4(ex_mem_1_pc_4_2), .Jal_2(mem_wb_1_jal_2),
    .Jalr_2(mem_wb_1_jalr_2), .MemToReg_2(mem_wb_1_memtoreg_2[0]), .RegWrite_2(RegWrite),
    .Halt_2(mem_wb_1_halt_2), .rd_2(WB_rd), .AluResult_2(mem_wb_1_aluresult_2),
    .Readdata_2(mem_wb_1_readdata_2), .IR_2(WB_IR), .PC_2(WB_PC), .PC_4_2(mem_wb_1_pc_4_2), .reset(RST),
    .en(1'b1), .clk(CLK), .SLTIU(ex_mem_1_sltiu_2), .SLTIU_2(WB_SLTIU), .ALU(ex_mem_1_alu_2), .ALU_2(WB_ALU));  // open: URET, URET_2, SH, SH_2
  Multiplexer #(.select(1), .width(1), .disabled("Z"), .enable("false")) multiplexer_10 (
    .in0(1'b0), .in1(1'b1), .out(multiplexer_9_out[3]), .sel(MEM_ALUresult[1]));
  or or_2 (mem_wb_1_memtoreg_2[1], mem_wb_1_jal_2, mem_wb_1_jalr_2);
  Multiplexer #(.select(2), .width(32), .disabled("Z"), .enable("false")) multiplexer_11 (
    .in0(mem_wb_1_aluresult_2), .in1(mem_wb_1_readdata_2), .in2(mem_wb_1_pc_4_2), .out(multiplexer_11_out),
    .sel(mem_wb_1_memtoreg_2));  // open: in3
  or or_3 (or_3_out, mem_wb_1_halt_2, halt);
  D_Flip_Flop #(.trigger("falling"), .Pre_Clr_Positions("ABOVE_BELOW"), .NegatePresetClear("false"), .enable("false"), .NewFFLayout("true")) d_ff_2 (
    .clk(CLK), .D(or_3_out), .Q(halt), .reset(Go));  // open: Qn, preset
  Multiplexer #(.select(1), .width(32), .disabled("Z"), .enable("false")) multiplexer_12 (
    .in0(multiplexer_11_out), .in1(multiplexer_13_out), .out(RDin), .sel(WB_SLTIU));
  Multiplexer #(.select(1), .width(32), .disabled("Z"), .enable("false")) multiplexer_13 (
    .in0({32{1'b0}}), .in1(32'h1), .out(multiplexer_13_out), .sel(WB_ALU));

  // Other names for the same wires on the sheet: MEM_PC[31:0] = M_PC; WB_RegWrite = RegWrite

  // Notes on the sheet:
  //   中断源
  //   时空图监测，可删除
  //   中断等待指示
  //   数码管输出
  //   指令存储器
  //   指令探针
  //   contents of rom_1 (hex, n*v repeats v):
  //   413 493 913 993 46413 14e493 296913 39e993 842023 942223 1242423 1342623 a00893 493 913 993 73
  //   控制位
  //   流水调试日志用
  //   暂停节拍，不能为0
  //   用这个时钟源需要去掉电路中的其他时钟源
  //   rs1
  //   rs2
  //   imm-i
  //   rd
  //   ctrl+k关闭时钟连续运行，将控制位置零，进入单步调试模式调试
  //   戳工具置1进入计数暂停模式，ctrl+k时钟自动运行到对应节拍暂停
  //   JAL
  //   JALR
  //   URET
  //   imm-j
  //   beq/bne
  //   jal
  //   rd
  //   可计数暂停的时钟源
  //   Beq
  //   Bne
  //   MemToReg
  //   MemWrite
  //   AluOP
  //   AluSrcB
  //   RegWrite
  //   S_type
  //   为方便自动评测，需要输出流水线各段保存的PC值，注意是PC不是PC+4，另外ID段寄存器写入信息，Mem段内存写入信息也要输出
  //   Beq
  //   Jal
  //   Jalr
  //   Bne
  //   数据存储器
endmodule
module \气泡流水线  (
  output RegWrite,
  output MemWrite,
  output [31:0] IF_PC,
  output [31:0] ID_PC,
  output [31:0] EX_PC,
  output [31:0] M_PC,
  output [31:0] WB_PC,
  output [31:0] RDin,
  output [31:0] MDin,
  output [31:0] LedData
);

  wire ALU, alu_1_equal, alu_1_out_4, and_2_out, and_3_out, and_4_out, and_5_out, and_6_out, and_7_out,
       and_9_out, and_10_out, and_11_out, and_12_out, BGE, CLK, clock_1_out, comparator_1_eq,
       comparator_1_lt, comparator_2_eq, d_ff_1_q, ecall, EX_ecall, EX_halt, ex_mem_1_alu_2, ex_mem_1_halt_2,
       ex_mem_1_jal_2, ex_mem_1_jalr_2, ex_mem_1_memtoreg_2, ex_mem_1_regwrite_2, ex_mem_1_sltiu_2, Go, halt,
       id_ex_1_alusrc_2, id_ex_1_beq_2, id_ex_1_bge_2, id_ex_1_bne_2, id_ex_1_jal_2, id_ex_1_memtoreg_2,
       id_ex_1_menwrite, id_ex_1_regwrite_2, id_ex_1_sh_2, id_ex_1_sltiu_2, IR1, IR2, IR3, MEM_SH,
       mem_wb_1_halt_2, mem_wb_1_jal_2, mem_wb_1_jalr_2, multiplexer_2_out, multiplexer_6_out,
       multiplexer_9_out, nand_1_out, not_1_out, not_2_out, not_3_out, not_4_out, not_5_out, not_6_out,
       or_1_out, or_3_out, or_7_out, RST, SH, SLTIU, SRL, stall, W1, W2, W3, WB_ALU, WB_SLTIU,
       \单周期硬布线控制器_1_alu_src , \单周期硬布线控制器_1_beq , \单周期硬布线控制器_1_bne , \单周期硬布线控制器_1_jal , \单周期硬布线控制器_1_jalr ,
       \单周期硬布线控制器_1_memtoreg , \单周期硬布线控制器_1_memwrite , \单周期硬布线控制器_1_regwrite , \单周期硬布线控制器_1_rs1_used ,
       \单周期硬布线控制器_1_rs2_used , \单周期硬布线控制器_1_s_type , \单周期硬布线控制器_1_uret , \无条件分支 , \条件分支 , \气泡处理逻辑_1_flush ;
  wire [1:0] id_ex_1_jalr_2, mem_wb_1_memtoreg_2;
  wire [3:0] id_ex_1_alu_op_2, RAM_Sel, \单周期硬布线控制器_1_alu_op ;
  wire [3:1] multiplexer_12_out;
  wire [4:0] ex_mem_1_rd_2, id_ex_1_rd_2, multiplexer_3_out, multiplexer_4_out, WB_rd;
  wire [11:0] multiplexer_5_out;
  wire [12:0] CNT_num;
  wire [15:0] \LoadUse次数 , \总周期数 , \插入气泡数 , \无条件分支数 , \条件分支成功数 ;
  wire [31:0] adder_2_out, adder_3_out, Alu_add, and_1_out, bit_extender_1_out, bit_extender_2_out,
       bit_extender_3_out, Branch_add, EX_IR, ex_mem_1_pc_4_2, EX_R1, EX_R2, id_ex_1_imm1_2, id_ex_1_imm2b_2,
       id_ex_1_imm2j_2, id_ex_1_pc_4_2, ID_IR, if_id_1_pc_4_2, IF_IR, MEM_ALUresult, MEM_IR, MEM_R2,
       mem_wb_1_aluresult_2, mem_wb_1_pc_4_2, mem_wb_1_readdata_2, mips_ram_1_p8, multiplexer_1_out,
       multiplexer_7_out, multiplexer_14_out, multiplexer_16_out, PC_4, regifile_1_r1, regifile_1_r2,
       shifter_1_out, shifter_2_out, shifter_3_out, WB_IR;

  Button \u_总复位  (.out(RST));
  Button _1 (.out(IR1));
  Button _2 (.out(IR2));
  Button _3 (.out(IR3));
  // Probe on \总周期数 
  // Probe on \总周期数 
  Button \u_继续运行  (.out(Go));
  LED #(.active("true")) led_1 (.in(W1));
  LED #(.active("true")) led_2 (.in(W2));
  LED #(.active("true")) led_3 (.in(W3));
  Hex_Digit_Display hex_digit_display_1 (.value(LedData[31:28]));  // open: dp
  // Probe on IF_PC[19:0]
  // RiscV_Probe riscv_probe_1: pin names not known; wires that end beside it: IF_IR
  Hex_Digit_Display hex_digit_display_2 (.value(LedData[23:20]));  // open: dp
  Hex_Digit_Display hex_digit_display_3 (.value(LedData[27:24]));  // open: dp
  // Probe on ID_PC[19:0]
  // RiscV_Probe riscv_probe_2: pin names not known; wires that end beside it: ID_IR
  Hex_Digit_Display hex_digit_display_4 (.value(LedData[15:12]));  // open: dp
  Hex_Digit_Display hex_digit_display_5 (.value(LedData[19:16]));  // open: dp
  Hex_Digit_Display hex_digit_display_6 (.value(LedData[11:8]));  // open: dp
  Hex_Digit_Display hex_digit_display_7 (.value(LedData[7:4]));  // open: dp
  // Probe on EX_PC[19:0]
  // RiscV_Probe riscv_probe_3: pin names not known; wires that end beside it: EX_IR
  Hex_Digit_Display hex_digit_display_8 (.value(LedData[3:0]));  // open: dp
  // Probe on \总周期数 
  // Probe on M_PC[19:0]
  // RiscV_Probe riscv_probe_4: pin names not known; wires that end beside it: MEM_IR
  // Probe on \总周期数 
  // Probe on \无条件分支数 
  // Probe on \条件分支成功数 
  // Probe on \插入气泡数 
  // Probe on \LoadUse次数 
  assign and_1_out = Alu_add & 32'hfffffffe;  // AND_Gate and_1, 32 bits wide
  not not_1 (not_1_out, stall);
  not not_2 (not_2_out, halt);
  // Probe on IF_PC[11:0]
  // Probe on WB_PC[19:0]
  // RiscV_Probe riscv_probe_5: pin names not known; wires that end beside it: WB_IR
  \气泡处理逻辑  \u_气泡处理逻辑_1  (
    .BranchTaken(or_3_out), .IR(ID_IR), .ecall(ecall), .rs1_used(\单周期硬布线控制器_1_rs1_used ),
    .EX_RegWrite(id_ex_1_regwrite_2), .rs2_used(\单周期硬布线控制器_1_rs2_used ), .MEM_RegWrite(ex_mem_1_regwrite_2),
    .EX_rd(id_ex_1_rd_2), .MEM_rd(ex_mem_1_rd_2), .stall(stall), .flush(\气泡处理逻辑_1_flush ));
  Multiplexer #(.select(2), .width(32), .disabled("Z"), .enable("false")) multiplexer_1 (
    .in0(PC_4), .in1(and_1_out), .in2(Branch_add), .out(multiplexer_1_out), .sel(id_ex_1_jalr_2));  // open: in3
  and and_2 (and_2_out, not_1_out, not_2_out);
  // Probe on EX_PC[11:0]
  // Probe on ID_PC[11:0]
  // Probe on M_PC[11:0]
  D_Flip_Flop #(.trigger("high"), .Pre_Clr_Positions("LEGACY"), .NegatePresetClear("false"), .enable("true"), .NewFFLayout("false")) d_ff_1 (.Q(d_ff_1_q));  // open: clk, D, Qn, preset, en, reset
  // Probe on 13'h451
  Register #(.width(32), .trigger("rising"), .Select("low")) PC (
    .D(multiplexer_1_out), .en(and_2_out), .Q(IF_PC), .clk(CLK), .clr(RST));
  // Probe on WB_PC[11:0]
  Comparator #(.width(13), .mode("twosComplement")) comparator_1 (
    .a(CNT_num), .b(13'h451), .eq(comparator_1_eq), .lt(comparator_1_lt));  // open: gt
  Clock #(.highDuration(1), .lowDuration(1)) clock_1 (.out(clock_1_out));
  Adder #(.width(32)) adder_1 (.a(IF_PC), .b(32'h4), .out(PC_4), .cin(1'b0));  // open: cout
  nand nand_1 (nand_1_out, d_ff_1_q, comparator_1_eq);
  Counter #(.width(13), .max('h1fff), .ongoal("stay"), .trigger("rising"), .behavior("old")) counter_1 (
    .count(comparator_1_lt), .Q(CNT_num), .clk(clock_1_out));  // open: load, D, carry, clr, preset
  assign CLK = nand_1_out ? clock_1_out : 1'bz;  // Controlled_Buffer controlled_buffer_1
  not not_3 (not_3_out, halt);
  Pull_Resistor #(.pull(1)) pull_resistor_1 (.node(CLK));
  // RiscV_Probe riscv_probe_6: pin names not known; wires that end beside it: IF_IR, PC_4
  ROM #(.addrWidth(10), .dataWidth(32), .Select("high")) rom_1 (.addr(IF_PC[11:2]), .data(IF_IR));
  Counter #(.width(16), .max('hffff), .ongoal("wrap"), .trigger("rising"), .behavior("new")) counter_2 (
    .count(not_3_out), .Q(\总周期数 ), .clk(CLK));  // open: load, D, carry, clr, preset, down
  or or_1 (or_1_out, id_ex_1_jalr_2[1], id_ex_1_jalr_2[0]);
  and and_3 (and_3_out, ~stall, ~halt);  // AND_Gate
  IF_ID if_id_1 (
    .IR(IF_IR), .PC(IF_PC), .PC_4(PC_4), .IR_2(ID_IR), .PC_2(ID_PC), .PC_4_2(if_id_1_pc_4_2), .reset(RST),
    .BranchTaken(or_1_out), .en(and_3_out), .clk(CLK));  // open: PredictJump, PredictJump_2
  Multiplexer #(.select(1), .width(1), .disabled("Z"), .enable("false")) multiplexer_2 (
    .in0(and_4_out), .in1(1'b0), .out(multiplexer_2_out), .sel(CLK));
  and and_4 (and_4_out, \无条件分支 , CLK);
  Counter #(.width(16), .max('hffff), .ongoal("wrap"), .trigger("rising"), .behavior("old")) counter_3 (
    .count(1'b1), .Q(\无条件分支数 ), .clk(multiplexer_2_out), .clr(RST));  // open: load, D, carry, preset
  \单周期硬布线控制器  \u_单周期硬布线控制器_1  (
    .Funct({ID_IR[30], ID_IR[25], ID_IR[14:12]}), .OP(ID_IR[6:2]), .ALU_OP(\单周期硬布线控制器_1_alu_op ),
    .MemToReg(\单周期硬布线控制器_1_memtoreg ), .MemWrite(\单周期硬布线控制器_1_memwrite ), .ALU_SRC(\单周期硬布线控制器_1_alu_src ),
    .RegWrite(\单周期硬布线控制器_1_regwrite ), .ecall(ecall), .S_type(\单周期硬布线控制器_1_s_type ),
    .Jalr(\单周期硬布线控制器_1_jalr ), .Beq(\单周期硬布线控制器_1_beq ), .JAL(\单周期硬布线控制器_1_jal ), .Bne(\单周期硬布线控制器_1_bne ),
    .in_3(ID_IR[21]), .uret(\单周期硬布线控制器_1_uret ), .SRL(SRL), .SLTIU(SLTIU), .SH(SH), .BGE(BGE),
    .rs1_used(\单周期硬布线控制器_1_rs1_used ), .rs2_used(\单周期硬布线控制器_1_rs2_used ));  // open: CSRRSI, CSRRCI
  assign bit_extender_1_out = {{20{ID_IR[31]}}, {ID_IR[31], ID_IR[7], ID_IR[30:25], ID_IR[11:8]}};  // Bit_Extender bit_extender_1
  assign bit_extender_2_out = {{12{ID_IR[31]}}, {ID_IR[31], ID_IR[19:12], ID_IR[20], ID_IR[30:21]}};  // Bit_Extender bit_extender_2
  Multiplexer #(.select(1), .width(5), .disabled("Z"), .enable("false")) multiplexer_3 (
    .in0(ID_IR[19:15]), .in1(5'b10001), .out(multiplexer_3_out), .sel(ecall));
  Multiplexer #(.select(1), .width(5), .disabled("Z"), .enable("false")) multiplexer_4 (
    .in0(ID_IR[24:20]), .in1(5'b01010), .out(multiplexer_4_out), .sel(ecall));
  Multiplexer #(.select(1), .width(12), .disabled("Z"), .enable("false")) multiplexer_5 (
    .in0(ID_IR[31:20]), .in1({ID_IR[31:25], ID_IR[11:7]}), .out(multiplexer_5_out), .sel(\单周期硬布线控制器_1_s_type ));
  assign bit_extender_3_out = {{20{multiplexer_5_out[11]}}, multiplexer_5_out};  // Bit_Extender bit_extender_3
  not not_4 (not_4_out, CLK);
  and and_5 (and_5_out, \条件分支 , CLK);
  ID_EX id_ex_1 (
    .Beq(\单周期硬布线控制器_1_beq ), .Bne(\单周期硬布线控制器_1_bne ), .MemToReg(\单周期硬布线控制器_1_memtoreg ),
    .MemWrite(\单周期硬布线控制器_1_memwrite ), .AluSrc(\单周期硬布线控制器_1_alu_src ), .RegWrite(\单周期硬布线控制器_1_regwrite ),
    .SType(\单周期硬布线控制器_1_s_type ), .ecall(ecall), .Jal(\单周期硬布线控制器_1_jal ), .Jalr(\单周期硬布线控制器_1_jalr ),
    .SLTIU(SLTIU), .SH(SH), .BGE(BGE), .ALU_OP(\单周期硬布线控制器_1_alu_op ), .rd(ID_IR[11:7]), .R1(regifile_1_r1),
    .R2(regifile_1_r2), .imm1(bit_extender_3_out), .IR(ID_IR), .PC(ID_PC), .PC_4(if_id_1_pc_4_2),
    .Beq_2(id_ex_1_beq_2), .Bne_2(id_ex_1_bne_2), .MemToReg_2(id_ex_1_memtoreg_2),
    .MenWrite(id_ex_1_menwrite), .AluSrc_2(id_ex_1_alusrc_2), .RegWrite_2(id_ex_1_regwrite_2),
    .ecall_2(EX_ecall), .Jal_2(id_ex_1_jal_2), .Jalr_2(id_ex_1_jalr_2[0]), .SLTIU_2(id_ex_1_sltiu_2),
    .SH_2(id_ex_1_sh_2), .BGE_2(id_ex_1_bge_2), .ALU_OP_2(id_ex_1_alu_op_2), .rd_2(id_ex_1_rd_2),
    .R1_2(EX_R1), .R2_2(EX_R2), .imm1_2(id_ex_1_imm1_2), .IR_2(EX_IR), .PC_2(EX_PC), .PC_4_2(id_ex_1_pc_4_2),
    .Reset(RST), .Flush(\气泡处理逻辑_1_flush ), .en(not_5_out), .clk(CLK), .imm2j(bit_extender_2_out),
    .imm2j_2(id_ex_1_imm2j_2), .imm2b(bit_extender_1_out), .imm2b_2(id_ex_1_imm2b_2));  // open: RS1_Forward, RS2_Forward, SType_2, RS1_Forward_2, RS2_Forward_2, URET, URET_2, PredictJump, PredictJump_2
  Regifile regifile_1 (
    .Din(RDin), .Clk(not_4_out), .R1(regifile_1_r1), .R2(regifile_1_r2), .WE(RegWrite), .W_num(WB_rd),
    .R1_num(multiplexer_3_out), .R2_num(multiplexer_4_out));
  not not_5 (not_5_out, halt);
  Counter #(.width(16), .max('hffff), .ongoal("wrap"), .trigger("rising"), .behavior("old")) counter_4 (
    .count(1'b1), .Q(\条件分支成功数 ), .clk(multiplexer_6_out), .clr(RST));  // open: load, D, carry, preset
  Multiplexer #(.select(1), .width(1), .disabled("Z"), .enable("false")) multiplexer_6 (
    .in0(and_5_out), .in1(1'b0), .out(multiplexer_6_out), .sel(CLK));
  or or_2 (\无条件分支 , id_ex_1_jalr_2[0], id_ex_1_jal_2);
  Shifter #(.width(32), .shift("ll")) shifter_1 (.in(id_ex_1_imm2b_2), .\dist (5'b00001), .out(shifter_1_out));
  Shifter #(.width(32), .shift("ll")) shifter_2 (.in(id_ex_1_imm2j_2), .\dist (5'b00001), .out(shifter_2_out));
  Comparator #(.width(32), .mode("twosComplement")) comparator_2 (
    .a(EX_R1), .b(32'h22), .eq(comparator_2_eq));  // open: gt, lt
  Multiplexer #(.select(1), .width(32), .disabled("Z"), .enable("false")) multiplexer_7 (
    .in0(EX_R2), .in1(id_ex_1_imm1_2), .out(multiplexer_7_out), .sel(id_ex_1_alusrc_2));
  Adder #(.width(32)) adder_2 (.a(shifter_1_out), .b(EX_PC), .out(adder_2_out));  // open: cin, cout
  Adder #(.width(32)) adder_3 (.a(shifter_2_out), .b(EX_PC), .out(adder_3_out));  // open: cin, cout
  not not_6 (not_6_out, comparator_2_eq);
  Register #(.width(32), .trigger("rising"), .Select("low")) PC_2 (
    .D(EX_R2), .en(and_6_out), .Q(LedData), .clk(CLK));  // open: clr
  and and_6 (and_6_out, comparator_2_eq, EX_ecall);
  or or_3 (or_3_out, id_ex_1_jalr_2[0], id_ex_1_jalr_2[1]);
  or or_4 (id_ex_1_jalr_2[1], id_ex_1_jal_2, and_7_out, and_10_out, and_9_out);
  and and_7 (and_7_out, id_ex_1_beq_2, alu_1_equal);
  ALU alu_1 (
    .X(EX_R1), .Y(multiplexer_7_out), .AluOP(id_ex_1_alu_op_2), .Equal(alu_1_equal), .Result(Alu_add),
    .out_4(alu_1_out_4), .out_6(ALU));  // open: Result_2
  Multiplexer #(.select(1), .width(32), .disabled("Z"), .enable("false")) multiplexer_8 (
    .in0(adder_2_out), .in1(adder_3_out), .out(Branch_add), .sel(id_ex_1_jal_2));
  and and_8 (EX_halt, EX_ecall, not_6_out);
  or or_5 (\条件分支 , and_7_out, and_10_out, and_9_out);
  and and_9 (and_9_out, id_ex_1_bge_2, alu_1_out_4);
  and and_10 (and_10_out, ~alu_1_equal, id_ex_1_bne_2);  // AND_Gate
  Counter #(.width(16), .max('hffff), .ongoal("wrap"), .trigger("rising"), .behavior("old")) counter_5 (
    .count(1'b1), .Q(\插入气泡数 ), .clk(multiplexer_9_out), .clr(RST));  // open: load, D, carry, preset
  Multiplexer #(.select(1), .width(1), .disabled("Z"), .enable("false")) multiplexer_9 (
    .in0(and_11_out), .in1(1'b0), .out(multiplexer_9_out), .sel(CLK));
  and and_11 (and_11_out, and_12_out, CLK);
  and and_12 (and_12_out, ~halt, stall);  // AND_Gate
  EX_MEM ex_mem_1 (
    .Jal(id_ex_1_jal_2), .Jalr(id_ex_1_jalr_2[0]), .MemToReg(id_ex_1_memtoreg_2),
    .MemWrite(id_ex_1_menwrite), .RegWrite(id_ex_1_regwrite_2), .Halt(EX_halt), .SLTIU(id_ex_1_sltiu_2),
    .SH(id_ex_1_sh_2), .ALU(ALU), .rd(id_ex_1_rd_2), .result(Alu_add), .WriteData(EX_R2), .IR(EX_IR),
    .PC(EX_PC), .PC_4(id_ex_1_pc_4_2), .Jal_2(ex_mem_1_jal_2), .Jalr_2(ex_mem_1_jalr_2),
    .MemToReg_2(ex_mem_1_memtoreg_2), .MemWrite_2(MemWrite), .RegWrite_2(ex_mem_1_regwrite_2),
    .Halt_2(ex_mem_1_halt_2), .SLTIU_2(ex_mem_1_sltiu_2), .SH_2(MEM_SH), .ALU_2(ex_mem_1_alu_2),
    .rd_2(ex_mem_1_rd_2), .result_2(MEM_ALUresult), .Writedata_2(MEM_R2), .IR_2(MEM_IR), .PC_2(M_PC),
    .PC_4_2(ex_mem_1_pc_4_2), .reset(RST), .en(not_5_out), .clk(CLK));  // open: URET, URET_2
  Shifter #(.width(32), .shift("ll")) shifter_3 (.in(MEM_R2), .\dist (5'b10000), .out(shifter_3_out));
  Multiplexer #(.select(1), .width(32), .disabled("Z"), .enable("false")) multiplexer_10 (
    .in0(MEM_R2), .in1(shifter_3_out), .out(MDin), .sel(MEM_ALUresult[1]));
  // MIPS_RAM mips_ram_1: pin names not known; wires that end beside it: MEM_ALUresult[11:2], MDin, MemWrite, RAM_Sel, CLK, 1'b1, RST, mips_ram_1_p8
  Multiplexer #(.select(1), .width(4), .disabled("Z"), .enable("false")) multiplexer_11 (
    .in0(4'b1111), .in1({{2{multiplexer_12_out[3]}}, {2{multiplexer_12_out[1]}}}), .out(RAM_Sel), .sel(MEM_SH));
  Multiplexer #(.select(1), .width(1), .disabled("Z"), .enable("false")) multiplexer_12 (
    .in0(1'b1), .in1(1'b0), .out(multiplexer_12_out[1]), .sel(MEM_ALUresult[1]));
  Multiplexer #(.select(1), .width(1), .disabled("Z"), .enable("false")) multiplexer_13 (
    .in0(1'b0), .in1(1'b1), .out(multiplexer_12_out[3]), .sel(MEM_ALUresult[1]));
  MEM_WB mem_wb_1 (
    .Jal(ex_mem_1_jal_2), .Jalr(ex_mem_1_jalr_2), .MemToReg(ex_mem_1_memtoreg_2),
    .RegWrite(ex_mem_1_regwrite_2), .Halt(ex_mem_1_halt_2), .rd(ex_mem_1_rd_2), .AluResult(MEM_ALUresult),
    .ReadData(mips_ram_1_p8), .IR(MEM_IR), .PC(M_PC), .PC_4(ex_mem_1_pc_4_2), .Jal_2(mem_wb_1_jal_2),
    .Jalr_2(mem_wb_1_jalr_2), .MemToReg_2(mem_wb_1_memtoreg_2[0]), .RegWrite_2(RegWrite),
    .Halt_2(mem_wb_1_halt_2), .rd_2(WB_rd), .AluResult_2(mem_wb_1_aluresult_2),
    .Readdata_2(mem_wb_1_readdata_2), .IR_2(WB_IR), .PC_2(WB_PC), .PC_4_2(mem_wb_1_pc_4_2), .reset(RST),
    .en(not_5_out), .clk(CLK), .SLTIU(ex_mem_1_sltiu_2), .SLTIU_2(WB_SLTIU), .ALU(ex_mem_1_alu_2),
    .ALU_2(WB_ALU));  // open: URET, URET_2, SH, SH_2
  or or_6 (mem_wb_1_memtoreg_2[1], mem_wb_1_jal_2, mem_wb_1_jalr_2);
  Multiplexer #(.select(2), .width(32), .disabled("Z"), .enable("false")) multiplexer_14 (
    .in0(mem_wb_1_aluresult_2), .in1(mem_wb_1_readdata_2), .in2(mem_wb_1_pc_4_2), .out(multiplexer_14_out),
    .sel(mem_wb_1_memtoreg_2));  // open: in3
  or or_7 (or_7_out, mem_wb_1_halt_2, halt);
  D_Flip_Flop #(.trigger("falling"), .Pre_Clr_Positions("ABOVE_BELOW"), .NegatePresetClear("false"), .enable("false"), .NewFFLayout("true")) d_ff_2 (
    .clk(CLK), .D(or_7_out), .Q(halt), .reset(Go));  // open: Qn, preset
  Multiplexer #(.select(1), .width(32), .disabled("Z"), .enable("false")) multiplexer_15 (
    .in0(multiplexer_14_out), .in1(multiplexer_16_out), .out(RDin), .sel(WB_SLTIU));
  Multiplexer #(.select(1), .width(32), .disabled("Z"), .enable("false")) multiplexer_16 (
    .in0({32{1'b0}}), .in1(32'h1), .out(multiplexer_16_out), .sel(WB_ALU));

  // Other names for the same wires on the sheet: MEM_PC[31:0] = M_PC; WB_RegWrite = RegWrite

  // Notes on the sheet:
  //   中断源
  //   时空图监测，可删除
  //   中断等待指示
  //   数码管输出
  //   控制位
  //   流水调试日志用
  //   暂停节拍，不能为0
  //   戳工具置1进入计数暂停模式，ctrl+k时钟自动运行到对应节拍暂停
  //   ctrl+k关闭时钟连续运行，将控制位置零，进入单步调试模式调试
  //   可计数暂停的时钟源
  //   指令存储器
  //   contents of rom_1 (hex, n*v repeats v):
  //   100493 100006f 100493 200913 300993 100006f 100493 200913 300993 100006f 100493 200913 300993
  //   100006f 100493 200913 300993 3a0000ef 100413 100493 1f49493 900533 2200893 73 24d493 48463 fedff06f
  //   900533 2200893 73 100493 249493 900533 2200893 73 48463 fedff06f 100493 1f49493 900533 2200893 73
  //   4034d493 900533 2200893 73 4044d493 900533 2200893 73 4044d493 900533 2200893 73 4044d493 900533
  //   2200893 73 4044d493 900533 2200893 73 4044d493 900533 2200893 73 4044d493 900533 2200893 73 4044d493
  //   900533 2200893 73 100413 1f41993 41f9d993 433 c00913 300b13 140413 f47413 800293 100313 499993
  //   89e9b3 1300533 2200893 73 406282b3 fe0294e3 140413 f00f93 1f47433 1c41413 800293 100313 49d993
  //   89e9b3 1300533 2200893 73 406282b3 fe0294e3 1c45413 406b0b33 b0463 f95ff06f 2b3 fff2c293 829293
  //   ff2e293 500533 2200893 73 fff00413 493 84a023 140413 448493 84a023 140413 448493 84a023 140413
  //   448493 84a023 140413 448493 84a023 140413 448493 84a023 140413 448493 84a023 140413 448493 84a023
  //   140413 448493 84a023 140413 448493 84a023 140413 448493 84a023 140413 448493 84a023 140413 448493
  //   84a023 140413 448493 84a023 140413 448493 84a023 140413 448493 84a023 140413 448493 140413 433
  //   3c00493 42983 4aa03 149a2b3 28663 134a023 1442023 ffc48493 fe9412e3 800533 2200893 73 440413 3c00493
  //   fc9416e3 3200893 73 100293 300313 800493 849493 7648493 1449493 900533 2200893 73 800e13 54d4b3
  //   64d4b3 900533 2200893 73 fffe0e13 fe0e14e3 a00893 73 fff00293 313 1900413 841413 9700493 940533
  //   2200893 73 5484b3 494b313 fe0306e3 a00893 73 313 2000e13 100493 100913 931023 900533 2200893 73
  //   12484b3 230313 fffe0e13 fe0e12e3 1000e13 313 32483 900533 2200893 73 430313 fffe0e13 fe0e14e3 a00893
  //   73 f00493 900533 2200893 73 fff48493 fe04d8e3 a00893 73 a00893 73 413 140413 800533 2200893 73
  //   240413 800533 2200893 73 340413 800533 2200893 73 440413 800533 2200893 73 540413 800533 2200893 73
  //   640413 800533 2200893 73 740413 800533 2200893 73 840413 800533 2200893 2200893 73 8067
  //   指令探针
  //   为方便自动评测，需要输出流水线各段保存的PC值，注意是PC不是PC+4，另外ID段寄存器写入信息，Mem段内存写入信息也要输出
  //   JAL
  //   JALR
  //   URET
  //   rs1
  //   rs2
  //   imm-i
  //   rd
  //   imm-j
  //   beq/bne
  //   jal
  //   rd
  //   Beq
  //   Bne
  //   MemToReg
  //   MemWrite
  //   AluOP
  //   AluSrcB
  //   RegWrite
  //   S_type
  //   Beq
  //   Jal
  //   Jalr
  //   Bne
  //   数据存储器
endmodule

module \重定向流水线  (
  output RegWrite,
  output MemWrite,
  output [31:0] IF_PC,
  output [31:0] ID_PC,
  output [31:0] EX_PC,
  output [31:0] M_PC,
  output [31:0] WB_PC,
  output [31:0] RDin,
  output [31:0] MDin,
  output [31:0] LedData
);

  wire alu_1_equal, alu_1_out_4, alu_1_out_6, and_2_out, and_3_out, and_4_out, and_5_out, and_6_out,
       and_7_out, and_9_out, and_10_out, and_11_out, and_12_out, and_13_out, BGE, CLK, clock_1_out,
       comparator_1_eq, comparator_1_lt, comparator_2_eq, d_ff_1_q, ecall, EX_ecall, EX_halt, ex_mem_1_alu_2,
       ex_mem_1_halt_2, ex_mem_1_jal_2, ex_mem_1_jalr_2, ex_mem_1_memtoreg_2, ex_mem_1_regwrite_2,
       ex_mem_1_sltiu_2, flush, Go, halt, id_ex_1_alusrc_2, id_ex_1_beq_2, id_ex_1_bge_2, id_ex_1_bne_2,
       id_ex_1_jal_2, id_ex_1_memtoreg_2, id_ex_1_menwrite, id_ex_1_regwrite_2, id_ex_1_sh_2,
       id_ex_1_sltiu_2, IR1, IR2, IR3, MEM_SH, mem_wb_1_halt_2, mem_wb_1_jal_2, mem_wb_1_jalr_2,
       multiplexer_2_out, multiplexer_6_out, multiplexer_11_out, multiplexer_12_out, nand_1_out, not_1_out,
       not_2_out, not_3_out, not_4_out, not_5_out, not_6_out, or_1_out, or_3_out, or_7_out, RST, SH, SLTIU,
       SRL, stall, W1, W2, W3, WB_ALU, WB_SLTIU, \单周期硬布线控制器_1_alu_src , \单周期硬布线控制器_1_beq , \单周期硬布线控制器_1_bne ,
       \单周期硬布线控制器_1_jal , \单周期硬布线控制器_1_jalr , \单周期硬布线控制器_1_memtoreg , \单周期硬布线控制器_1_memwrite ,
       \单周期硬布线控制器_1_regwrite , \单周期硬布线控制器_1_rs1_used , \单周期硬布线控制器_1_rs2_used , \单周期硬布线控制器_1_s_type ,
       \单周期硬布线控制器_1_uret , \无条件分支 , \条件分支 ;
  wire [1:0] id_ex_1_jalr_2, id_ex_1_rs1_forward_2, id_ex_1_rs2_forward_2, mem_wb_1_memtoreg_2,
       \重定向处理逻辑_1_rs1_forward , \重定向处理逻辑_1_rs2_forward ;
  wire [3:0] id_ex_1_alu_op_2, RAM_Sel, \单周期硬布线控制器_1_alu_op ;
  wire [3:1] multiplexer_15_out;
  wire [4:0] ex_mem_1_rd_2, id_ex_1_rd_2, multiplexer_3_out, multiplexer_4_out, WB_rd;
  wire [11:0] multiplexer_5_out;
  wire [12:0] CNT_num;
  wire [15:0] \LoadUse次数 , \总周期数 , \插入气泡数 , \无条件分支数 , \条件分支成功数 ;
  wire [31:0] adder_2_out, adder_3_out, Alu_add, and_1_out, bit_extender_1_out, bit_extender_2_out,
       bit_extender_3_out, Branch_add, EX_IR, ex_mem_1_pc_4_2, EX_R1, EX_R2, id_ex_1_imm1_2, id_ex_1_imm2b_2,
       id_ex_1_imm2j_2, id_ex_1_pc_4_2, id_ex_1_r1_2, id_ex_1_r2_2, ID_IR, if_id_1_pc_4_2, IF_IR,
       MEM_ALUresult, MEM_IR, MEM_R2, mem_wb_1_aluresult_2, mem_wb_1_pc_4_2, mem_wb_1_readdata_2,
       mips_ram_1_p8, multiplexer_1_out, multiplexer_9_out, multiplexer_17_out, multiplexer_19_out, PC_4,
       regifile_1_r1, regifile_1_r2, shifter_1_out, shifter_2_out, shifter_3_out, WB_IR;

  Button \u_总复位  (.out(RST));
  Button _1 (.out(IR1));
  Button _2 (.out(IR2));
  Button _3 (.out(IR3));
  // Probe on \总周期数 
  // Probe on \总周期数 
  Button \u_继续运行  (.out(Go));
  LED #(.active("true")) led_1 (.in(W1));
  LED #(.active("true")) led_2 (.in(W2));
  LED #(.active("true")) led_3 (.in(W3));
  Hex_Digit_Display hex_digit_display_1 (.value(LedData[31:28]));  // open: dp
  // Probe on IF_PC[19:0]
  // RiscV_Probe riscv_probe_1: pin names not known; wires that end beside it: IF_IR
  Hex_Digit_Display hex_digit_display_2 (.value(LedData[23:20]));  // open: dp
  Hex_Digit_Display hex_digit_display_3 (.value(LedData[27:24]));  // open: dp
  // Probe on ID_PC[19:0]
  // RiscV_Probe riscv_probe_2: pin names not known; wires that end beside it: ID_IR
  Hex_Digit_Display hex_digit_display_4 (.value(LedData[19:16]));  // open: dp
  Hex_Digit_Display hex_digit_display_5 (.value(LedData[15:12]));  // open: dp
  Hex_Digit_Display hex_digit_display_6 (.value(LedData[11:8]));  // open: dp
  Hex_Digit_Display hex_digit_display_7 (.value(LedData[7:4]));  // open: dp
  // Probe on EX_PC[19:0]
  // RiscV_Probe riscv_probe_3: pin names not known; wires that end beside it: EX_IR
  Hex_Digit_Display hex_digit_display_8 (.value(LedData[3:0]));  // open: dp
  // Probe on \总周期数 
  // Probe on M_PC[19:0]
  // RiscV_Probe riscv_probe_4: pin names not known; wires that end beside it: MEM_IR
  // Probe on \总周期数 
  // Probe on \无条件分支数 
  // Probe on \条件分支成功数 
  // Probe on \插入气泡数 
  // Probe on \LoadUse次数 
  \重定向处理逻辑  \u_重定向处理逻辑_1  (
    .IR(ID_IR), .BranchTaken(or_3_out), .EX_MemToReg(id_ex_1_memtoreg_2), .ecall(ecall),
    .rs1_used(\单周期硬布线控制器_1_rs1_used ), .EX_RegWrite(id_ex_1_regwrite_2), .rs2_used(\单周期硬布线控制器_1_rs2_used ),
    .MEM_RegWrite(ex_mem_1_regwrite_2), .EX_rd(id_ex_1_rd_2), .MEM_rd(ex_mem_1_rd_2), .stall(stall),
    .flush(flush), .rs1_Forward(\重定向处理逻辑_1_rs1_forward ), .rs2_Forward(\重定向处理逻辑_1_rs2_forward ));
  assign and_1_out = Alu_add & 32'hfffffffe;  // AND_Gate and_1, 32 bits wide
  not not_1 (not_1_out, stall);
  not not_2 (not_2_out, halt);
  // Probe on IF_PC[11:0]
  // Probe on WB_PC[19:0]
  // RiscV_Probe riscv_probe_5: pin names not known; wires that end beside it: WB_IR
  Multiplexer #(.select(2), .width(32), .disabled("Z"), .enable("false")) multiplexer_1 (
    .in0(PC_4), .in1(and_1_out), .in2(Branch_add), .out(multiplexer_1_out), .sel(id_ex_1_jalr_2));  // open: in3
  and and_2 (and_2_out, not_1_out, not_2_out);
  // Probe on ID_PC[11:0]
  // Probe on EX_PC[11:0]
  // Probe on M_PC[11:0]
  D_Flip_Flop #(.trigger("high"), .Pre_Clr_Positions("LEGACY"), .NegatePresetClear("false"), .enable("true"), .NewFFLayout("false")) d_ff_1 (.Q(d_ff_1_q));  // open: clk, D, Qn, preset, en, reset
  // Probe on 13'h27b
  Register #(.width(32), .trigger("rising"), .Select("low")) PC (
    .D(multiplexer_1_out), .en(and_2_out), .Q(IF_PC), .clk(CLK), .clr(RST));
  // Probe on WB_PC[11:0]
  Comparator #(.width(13), .mode("twosComplement")) comparator_1 (
    .a(CNT_num), .b(13'h27b), .eq(comparator_1_eq), .lt(comparator_1_lt));  // open: gt
  Clock #(.highDuration(1), .lowDuration(1)) clock_1 (.out(clock_1_out));
  Adder #(.width(32)) adder_1 (.a(IF_PC), .b(32'h4), .out(PC_4), .cin(1'b0));  // open: cout
  nand nand_1 (nand_1_out, d_ff_1_q, comparator_1_eq);
  Counter #(.width(13), .max('h1fff), .ongoal("stay"), .trigger("rising"), .behavior("old")) counter_1 (
    .count(comparator_1_lt), .Q(CNT_num), .clk(clock_1_out));  // open: load, D, carry, clr, preset
  assign CLK = nand_1_out ? clock_1_out : 1'bz;  // Controlled_Buffer controlled_buffer_1
  not not_3 (not_3_out, halt);
  Pull_Resistor #(.pull(1)) pull_resistor_1 (.node(CLK));
  // RiscV_Probe riscv_probe_6: pin names not known; wires that end beside it: IF_IR, PC_4
  ROM #(.addrWidth(10), .dataWidth(32), .Select("high")) rom_1 (.addr(IF_PC[11:2]), .data(IF_IR));
  Counter #(.width(16), .max('hffff), .ongoal("wrap"), .trigger("rising"), .behavior("new")) counter_2 (
    .count(not_3_out), .Q(\总周期数 ), .clk(CLK));  // open: load, D, carry, clr, preset, down
  or or_1 (or_1_out, id_ex_1_jalr_2[1], id_ex_1_jalr_2[0]);
  and and_3 (and_3_out, ~stall, ~halt);  // AND_Gate
  IF_ID if_id_1 (
    .IR(IF_IR), .PC(IF_PC), .PC_4(PC_4), .IR_2(ID_IR), .PC_2(ID_PC), .PC_4_2(if_id_1_pc_4_2), .reset(RST),
    .BranchTaken(or_1_out), .en(and_3_out), .clk(CLK));  // open: PredictJump, PredictJump_2
  Multiplexer #(.select(1), .width(1), .disabled("Z"), .enable("false")) multiplexer_2 (
    .in0(and_4_out), .in1(1'b0), .out(multiplexer_2_out), .sel(CLK));
  and and_4 (and_4_out, \无条件分支 , CLK);
  Counter #(.width(16), .max('hffff), .ongoal("wrap"), .trigger("rising"), .behavior("old")) counter_3 (
    .count(1'b1), .Q(\无条件分支数 ), .clk(multiplexer_2_out), .clr(RST));  // open: load, D, carry, preset
  \单周期硬布线控制器  \u_单周期硬布线控制器_1  (
    .Funct({ID_IR[30], ID_IR[25], ID_IR[14:12]}), .OP(ID_IR[6:2]), .ALU_OP(\单周期硬布线控制器_1_alu_op ),
    .MemToReg(\单周期硬布线控制器_1_memtoreg ), .MemWrite(\单周期硬布线控制器_1_memwrite ), .ALU_SRC(\单周期硬布线控制器_1_alu_src ),
    .RegWrite(\单周期硬布线控制器_1_regwrite ), .ecall(ecall), .S_type(\单周期硬布线控制器_1_s_type ),
    .Jalr(\单周期硬布线控制器_1_jalr ), .Beq(\单周期硬布线控制器_1_beq ), .JAL(\单周期硬布线控制器_1_jal ), .Bne(\单周期硬布线控制器_1_bne ),
    .in_3(ID_IR[21]), .uret(\单周期硬布线控制器_1_uret ), .SRL(SRL), .SLTIU(SLTIU), .SH(SH), .BGE(BGE),
    .rs1_used(\单周期硬布线控制器_1_rs1_used ), .rs2_used(\单周期硬布线控制器_1_rs2_used ));  // open: CSRRSI, CSRRCI
  assign bit_extender_1_out = {{20{ID_IR[31]}}, {ID_IR[31], ID_IR[7], ID_IR[30:25], ID_IR[11:8]}};  // Bit_Extender bit_extender_1
  assign bit_extender_2_out = {{12{ID_IR[31]}}, {ID_IR[31], ID_IR[19:12], ID_IR[20], ID_IR[30:21]}};  // Bit_Extender bit_extender_2
  Multiplexer #(.select(1), .width(5), .disabled("Z"), .enable("false")) multiplexer_3 (
    .in0(ID_IR[19:15]), .in1(5'b10001), .out(multiplexer_3_out), .sel(ecall));
  Multiplexer #(.select(1), .width(5), .disabled("Z"), .enable("false")) multiplexer_4 (
    .in0(ID_IR[24:20]), .in1(5'b01010), .out(multiplexer_4_out), .sel(ecall));
  Multiplexer #(.select(1), .width(12), .disabled("Z"), .enable("false")) multiplexer_5 (
    .in0(ID_IR[31:20]), .in1({ID_IR[31:25], ID_IR[11:7]}), .out(multiplexer_5_out), .sel(\单周期硬布线控制器_1_s_type ));
  assign bit_extender_3_out = {{20{multiplexer_5_out[11]}}, multiplexer_5_out};  // Bit_Extender bit_extender_3
  not not_4 (not_4_out, CLK);
  and and_5 (and_5_out, \条件分支 , CLK);
  ID_EX id_ex_1 (
    .Beq(\单周期硬布线控制器_1_beq ), .Bne(\单周期硬布线控制器_1_bne ), .MemToReg(\单周期硬布线控制器_1_memtoreg ),
    .MemWrite(\单周期硬布线控制器_1_memwrite ), .AluSrc(\单周期硬布线控制器_1_alu_src ), .RegWrite(\单周期硬布线控制器_1_regwrite ),
    .SType(\单周期硬布线控制器_1_s_type ), .ecall(ecall), .Jal(\单周期硬布线控制器_1_jal ), .Jalr(\单周期硬布线控制器_1_jalr ),
    .SLTIU(SLTIU), .SH(SH), .BGE(BGE), .ALU_OP(\单周期硬布线控制器_1_alu_op ), .rd(ID_IR[11:7]), .R1(regifile_1_r1),
    .R2(regifile_1_r2), .imm1(bit_extender_3_out), .IR(ID_IR), .PC(ID_PC), .PC_4(if_id_1_pc_4_2),
    .RS1_Forward(\重定向处理逻辑_1_rs1_forward ), .RS2_Forward(\重定向处理逻辑_1_rs2_forward ), .Beq_2(id_ex_1_beq_2),
    .Bne_2(id_ex_1_bne_2), .MemToReg_2(id_ex_1_memtoreg_2), .MenWrite(id_ex_1_menwrite),
    .AluSrc_2(id_ex_1_alusrc_2), .RegWrite_2(id_ex_1_regwrite_2), .ecall_2(EX_ecall), .Jal_2(id_ex_1_jal_2),
    .Jalr_2(id_ex_1_jalr_2[0]), .SLTIU_2(id_ex_1_sltiu_2), .SH_2(id_ex_1_sh_2), .BGE_2(id_ex_1_bge_2),
    .ALU_OP_2(id_ex_1_alu_op_2), .rd_2(id_ex_1_rd_2), .R1_2(id_ex_1_r1_2), .R2_2(id_ex_1_r2_2),
    .imm1_2(id_ex_1_imm1_2), .IR_2(EX_IR), .PC_2(EX_PC), .PC_4_2(id_ex_1_pc_4_2),
    .RS1_Forward_2(id_ex_1_rs1_forward_2), .RS2_Forward_2(id_ex_1_rs2_forward_2), .Reset(RST), .Flush(flush),
    .en(not_5_out), .clk(CLK), .imm2j(bit_extender_2_out), .imm2j_2(id_ex_1_imm2j_2),
    .imm2b(bit_extender_1_out), .imm2b_2(id_ex_1_imm2b_2));  // open: SType_2, URET, URET_2, PredictJump, PredictJump_2
  Regifile regifile_1 (
    .Din(RDin), .Clk(not_4_out), .R1(regifile_1_r1), .R2(regifile_1_r2), .WE(RegWrite), .W_num(WB_rd),
    .R1_num(multiplexer_3_out), .R2_num(multiplexer_4_out));
  not not_5 (not_5_out, halt);
  Counter #(.width(16), .max('hffff), .ongoal("wrap"), .trigger("rising"), .behavior("old")) counter_4 (
    .count(1'b1), .Q(\条件分支成功数 ), .clk(multiplexer_6_out), .clr(RST));  // open: load, D, carry, preset
  Multiplexer #(.select(1), .width(1), .disabled("Z"), .enable("false")) multiplexer_6 (
    .in0(and_5_out), .in1(1'b0), .out(multiplexer_6_out), .sel(CLK));
  or or_2 (\无条件分支 , id_ex_1_jalr_2[0], id_ex_1_jal_2);
  Multiplexer #(.select(2), .width(32), .disabled("Z"), .enable("false")) multiplexer_7 (
    .in0(id_ex_1_r1_2), .in1(RDin), .in2(MEM_ALUresult), .out(EX_R1), .sel(id_ex_1_rs1_forward_2));  // open: in3
  Multiplexer #(.select(2), .width(32), .disabled("Z"), .enable("false")) multiplexer_8 (
    .in0(id_ex_1_r2_2), .in1(RDin), .in2(MEM_ALUresult), .out(EX_R2), .sel(id_ex_1_rs2_forward_2));  // open: in3
  Shifter #(.width(32), .shift("ll")) shifter_1 (.in(id_ex_1_imm2b_2), .\dist (5'b00001), .out(shifter_1_out));
  Shifter #(.width(32), .shift("ll")) shifter_2 (.in(id_ex_1_imm2j_2), .\dist (5'b00001), .out(shifter_2_out));
  Comparator #(.width(32), .mode("twosComplement")) comparator_2 (
    .a(EX_R1), .b(32'h22), .eq(comparator_2_eq));  // open: gt, lt
  Multiplexer #(.select(1), .width(32), .disabled("Z"), .enable("false")) multiplexer_9 (
    .in0(EX_R2), .in1(id_ex_1_imm1_2), .out(multiplexer_9_out), .sel(id_ex_1_alusrc_2));
  Adder #(.width(32)) adder_2 (.a(shifter_1_out), .b(EX_PC), .out(adder_2_out));  // open: cin, cout
  Adder #(.width(32)) adder_3 (.a(shifter_2_out), .b(EX_PC), .out(adder_3_out));  // open: cin, cout
  not not_6 (not_6_out, comparator_2_eq);
  Register #(.width(32), .trigger("rising"), .Select("low")) PC_2 (
    .D(EX_R2), .en(and_6_out), .Q(LedData), .clk(CLK));  // open: clr
  and and_6 (and_6_out, comparator_2_eq, EX_ecall);
  or or_3 (or_3_out, id_ex_1_jalr_2[0], id_ex_1_jalr_2[1]);
  or or_4 (id_ex_1_jalr_2[1], id_ex_1_jal_2, and_7_out, and_10_out, and_9_out);
  and and_7 (and_7_out, id_ex_1_beq_2, alu_1_equal);
  ALU alu_1 (
    .X(EX_R1), .Y(multiplexer_9_out), .AluOP(id_ex_1_alu_op_2), .Equal(alu_1_equal), .Result(Alu_add),
    .out_4(alu_1_out_4), .out_6(alu_1_out_6));  // open: Result_2
  Multiplexer #(.select(1), .width(32), .disabled("Z"), .enable("false")) multiplexer_10 (
    .in0(adder_2_out), .in1(adder_3_out), .out(Branch_add), .sel(id_ex_1_jal_2));
  and and_8 (EX_halt, EX_ecall, not_6_out);
  or or_5 (\条件分支 , and_7_out, and_10_out, and_9_out);
  and and_9 (and_9_out, id_ex_1_bge_2, alu_1_out_4);
  and and_10 (and_10_out, ~alu_1_equal, id_ex_1_bne_2);  // AND_Gate
  Counter #(.width(16), .max('hffff), .ongoal("wrap"), .trigger("rising"), .behavior("old")) counter_5 (
    .count(1'b1), .Q(\插入气泡数 ), .clk(multiplexer_11_out), .clr(RST));  // open: load, D, carry, preset
  Multiplexer #(.select(1), .width(1), .disabled("Z"), .enable("false")) multiplexer_11 (
    .in0(and_11_out), .in1(1'b0), .out(multiplexer_11_out), .sel(CLK));
  and and_11 (and_11_out, and_12_out, CLK);
  and and_12 (and_12_out, ~halt, flush);  // AND_Gate
  EX_MEM ex_mem_1 (
    .Jal(id_ex_1_jal_2), .Jalr(id_ex_1_jalr_2[0]), .MemToReg(id_ex_1_memtoreg_2),
    .MemWrite(id_ex_1_menwrite), .RegWrite(id_ex_1_regwrite_2), .Halt(EX_halt), .SLTIU(id_ex_1_sltiu_2),
    .SH(id_ex_1_sh_2), .ALU(alu_1_out_6), .rd(id_ex_1_rd_2), .result(Alu_add), .WriteData(EX_R2), .IR(EX_IR),
    .PC(EX_PC), .PC_4(id_ex_1_pc_4_2), .Jal_2(ex_mem_1_jal_2), .Jalr_2(ex_mem_1_jalr_2),
    .MemToReg_2(ex_mem_1_memtoreg_2), .MemWrite_2(MemWrite), .RegWrite_2(ex_mem_1_regwrite_2),
    .Halt_2(ex_mem_1_halt_2), .SLTIU_2(ex_mem_1_sltiu_2), .SH_2(MEM_SH), .ALU_2(ex_mem_1_alu_2),
    .rd_2(ex_mem_1_rd_2), .result_2(MEM_ALUresult), .Writedata_2(MEM_R2), .IR_2(MEM_IR), .PC_2(M_PC),
    .PC_4_2(ex_mem_1_pc_4_2), .reset(RST), .en(not_5_out), .clk(CLK));  // open: URET, URET_2
  and and_13 (and_13_out, stall, CLK);
  Shifter #(.width(32), .shift("ll")) shifter_3 (.in(MEM_R2), .\dist (5'b10000), .out(shifter_3_out));
  Counter #(.width(16), .max('hffff), .ongoal("wrap"), .trigger("rising"), .behavior("old")) counter_6 (
    .count(1'b1), .Q(\LoadUse次数 ), .clk(multiplexer_12_out), .clr(RST));  // open: load, D, carry, preset
  Multiplexer #(.select(1), .width(1), .disabled("Z"), .enable("false")) multiplexer_12 (
    .in0(and_13_out), .in1(1'b0), .out(multiplexer_12_out), .sel(CLK));
  Multiplexer #(.select(1), .width(32), .disabled("Z"), .enable("false")) multiplexer_13 (
    .in0(MEM_R2), .in1(shifter_3_out), .out(MDin), .sel(MEM_ALUresult[1]));
  // MIPS_RAM mips_ram_1: pin names not known; wires that end beside it: MEM_ALUresult[11:2], MDin, MemWrite, RAM_Sel, CLK, 1'b1, RST, mips_ram_1_p8
  Multiplexer #(.select(1), .width(4), .disabled("Z"), .enable("false")) multiplexer_14 (
    .in0(4'b1111), .in1({{2{multiplexer_15_out[3]}}, {2{multiplexer_15_out[1]}}}), .out(RAM_Sel), .sel(MEM_SH));
  Multiplexer #(.select(1), .width(1), .disabled("Z"), .enable("false")) multiplexer_15 (
    .in0(1'b1), .in1(1'b0), .out(multiplexer_15_out[1]), .sel(MEM_ALUresult[1]));
  Multiplexer #(.select(1), .width(1), .disabled("Z"), .enable("false")) multiplexer_16 (
    .in0(1'b0), .in1(1'b1), .out(multiplexer_15_out[3]), .sel(MEM_ALUresult[1]));
  MEM_WB mem_wb_1 (
    .Jal(ex_mem_1_jal_2), .Jalr(ex_mem_1_jalr_2), .MemToReg(ex_mem_1_memtoreg_2),
    .RegWrite(ex_mem_1_regwrite_2), .Halt(ex_mem_1_halt_2), .rd(ex_mem_1_rd_2), .AluResult(MEM_ALUresult),
    .ReadData(mips_ram_1_p8), .IR(MEM_IR), .PC(M_PC), .PC_4(ex_mem_1_pc_4_2), .Jal_2(mem_wb_1_jal_2),
    .Jalr_2(mem_wb_1_jalr_2), .MemToReg_2(mem_wb_1_memtoreg_2[0]), .RegWrite_2(RegWrite),
    .Halt_2(mem_wb_1_halt_2), .rd_2(WB_rd), .AluResult_2(mem_wb_1_aluresult_2),
    .Readdata_2(mem_wb_1_readdata_2), .IR_2(WB_IR), .PC_2(WB_PC), .PC_4_2(mem_wb_1_pc_4_2), .reset(RST),
    .en(not_5_out), .clk(CLK), .SLTIU(ex_mem_1_sltiu_2), .SLTIU_2(WB_SLTIU), .ALU(ex_mem_1_alu_2),
    .ALU_2(WB_ALU));  // open: URET, URET_2, SH, SH_2
  or or_6 (mem_wb_1_memtoreg_2[1], mem_wb_1_jal_2, mem_wb_1_jalr_2);
  Multiplexer #(.select(2), .width(32), .disabled("Z"), .enable("false")) multiplexer_17 (
    .in0(mem_wb_1_aluresult_2), .in1(mem_wb_1_readdata_2), .in2(mem_wb_1_pc_4_2), .out(multiplexer_17_out),
    .sel(mem_wb_1_memtoreg_2));  // open: in3
  or or_7 (or_7_out, mem_wb_1_halt_2, halt);
  D_Flip_Flop #(.trigger("falling"), .Pre_Clr_Positions("ABOVE_BELOW"), .NegatePresetClear("false"), .enable("false"), .NewFFLayout("true")) d_ff_2 (
    .clk(CLK), .D(or_7_out), .Q(halt), .reset(Go));  // open: Qn, preset
  Multiplexer #(.select(1), .width(32), .disabled("Z"), .enable("false")) multiplexer_18 (
    .in0(multiplexer_17_out), .in1(multiplexer_19_out), .out(RDin), .sel(WB_SLTIU));
  Multiplexer #(.select(1), .width(32), .disabled("Z"), .enable("false")) multiplexer_19 (
    .in0({32{1'b0}}), .in1(32'h1), .out(multiplexer_19_out), .sel(WB_ALU));

  // Other names for the same wires on the sheet: MEM_PC[31:0] = M_PC; WB_RegWrite = RegWrite

  // Notes on the sheet:
  //   中断源
  //   时空图监测，可删除
  //   中断等待指示
  //   数码管输出
  //   控制位
  //   流水调试日志用
  //   暂停节拍，不能为0
  //   戳工具置1进入计数暂停模式，ctrl+k时钟自动运行到对应节拍暂停
  //   ctrl+k关闭时钟连续运行，将控制位置零，进入单步调试模式调试
  //   可计数暂停的时钟源
  //   指令存储器
  //   contents of rom_1 (hex, n*v repeats v):
  //   100493 100006f 100493 200913 300993 100006f 100493 200913 300993 100006f 100493 200913 300993
  //   100006f 100493 200913 300993 3a0000ef 100413 100493 1f49493 900533 2200893 73 24d493 48463 fedff06f
  //   900533 2200893 73 100493 249493 900533 2200893 73 48463 fedff06f 100493 1f49493 900533 2200893 73
  //   4034d493 900533 2200893 73 4044d493 900533 2200893 73 4044d493 900533 2200893 73 4044d493 900533
  //   2200893 73 4044d493 900533 2200893 73 4044d493 900533 2200893 73 4044d493 900533 2200893 73 4044d493
  //   900533 2200893 73 100413 1f41993 41f9d993 433 c00913 300b13 140413 f47413 800293 100313 499993
  //   89e9b3 1300533 2200893 73 406282b3 fe0294e3 140413 f00f93 1f47433 1c41413 800293 100313 49d993
  //   89e9b3 1300533 2200893 73 406282b3 fe0294e3 1c45413 406b0b33 b0463 f95ff06f 2b3 fff2c293 829293
  //   ff2e293 500533 2200893 73 fff00413 493 84a023 140413 448493 84a023 140413 448493 84a023 140413
  //   448493 84a023 140413 448493 84a023 140413 448493 84a023 140413 448493 84a023 140413 448493 84a023
  //   140413 448493 84a023 140413 448493 84a023 140413 448493 84a023 140413 448493 84a023 140413 448493
  //   84a023 140413 448493 84a023 140413 448493 84a023 140413 448493 84a023 140413 448493 140413 433
  //   3c00493 42983 4aa03 149a2b3 28663 134a023 1442023 ffc48493 fe9412e3 800533 2200893 73 440413 3c00493
  //   fc9416e3 3200893 73 100293 300313 800493 849493 7648493 1449493 900533 2200893 73 800e13 54d4b3
  //   64d4b3 900533 2200893 73 fffe0e13 fe0e14e3 a00893 73 fff00293 313 1900413 841413 9700493 940533
  //   2200893 73 5484b3 494b313 fe0306e3 a00893 73 313 2000e13 100493 100913 931023 900533 2200893 73
  //   12484b3 230313 fffe0e13 fe0e12e3 1000e13 313 32483 900533 2200893 73 430313 fffe0e13 fe0e14e3 a00893
  //   73 f00493 900533 2200893 73 fff48493 fe04d8e3 a00893 73 a00893 73 413 140413 800533 2200893 73
  //   240413 800533 2200893 73 340413 800533 2200893 73 440413 800533 2200893 73 540413 800533 2200893 73
  //   640413 800533 2200893 73 740413 800533 2200893 73 840413 800533 2200893 2200893 73 8067
  //   指令探针
  //   为方便自动评测，需要输出流水线各段保存的PC值，注意是PC不是PC+4，另外ID段寄存器写入信息，Mem段内存写入信息也要输出
  //   JAL
  //   JALR
  //   URET
  //   rs1
  //   rs2
  //   imm-i
  //   imm-j
  //   rd
  //   beq/bne
  //   jal
  //   rd
  //   Beq
  //   Bne
  //   MemToReg
  //   MemWrite
  //   AluOP
  //   AluSrcB
  //   RegWrite
  //   S_type
  //   Beq
  //   Jal
  //   Jalr
  //   Bne
  //   数据存储器
endmodule

module \中断按键参考电路  (
  input  \同步清零信号 ,
  output \与中断屏蔽位与 
);

  wire \_1号中断_out , and_1_out, clock_1_out, d_ff_1_q, or_1_out, or_2_out;

  Clock #(.highDuration(1), .lowDuration(1)) clock_1 (.out(clock_1_out));
  Button \_1号中断  (.out(\_1号中断_out ));
  LED #(.active("true")) \_1号中断等待指示灯  (.in(or_1_out));
  or or_1 (or_1_out, \与中断屏蔽位与 , d_ff_1_q);
  D_Flip_Flop #(.trigger("rising"), .Pre_Clr_Positions("LEGACY"), .NegatePresetClear("false"), .enable("true"), .NewFFLayout("false")) d_ff_1 (
    .clk(\_1号中断_out ), .D(1'b1), .Q(d_ff_1_q), .reset(\与中断屏蔽位与 ));  // open: Qn, preset, en
  or or_2 (or_2_out, d_ff_1_q, \与中断屏蔽位与 );
  and and_1 (and_1_out, or_2_out, ~\同步清零信号 );  // AND_Gate
  D_Flip_Flop #(.trigger("rising"), .Pre_Clr_Positions("LEGACY"), .NegatePresetClear("false"), .enable("true"), .NewFFLayout("false")) IR1 (
    .clk(clock_1_out), .D(and_1_out), .Q(\与中断屏蔽位与 ));  // open: Qn, preset, en, reset

  // Notes on the sheet:
  //   中断信号采样参考电路
  //   Reset 
endmodule

module \单周期_单级中断  (
  input  IR1,
  input  IR2,
  input  IR3,
  output RegWrite,
  output MemWrite,
  output [31:0] PC,
  output [31:0] IR,
  output [31:0] RDin,
  output [31:0] MDin,
  output [31:0] LedData
);

  wire ALU, ALU_t, ALU_t_t, and_2_out, and_3_out, and_4_out, and_5_out, and_6_out, and_7_out, and_8_out,
       and_9_out, Beq, BGE, Bne, clear1, clear2, clear3, CLK, clock_1_out, comparator_1_eq, comparator_2_eq,
       comparator_3_eq, comparator_4_eq, comparator_5_eq, comparator_6_eq, comparator_6_lt, d_ff_1_q,
       d_ff_2_q, d_ff_3_q, d_ff_4_q, ecall, Go, halt, IE, INT, INTRequest, IR1_q, IR1_t, IR2_q, IR2_t, IR3_q,
       IR3_t, IRA, IRB, IRC, JAL, JALR, mips_ram_1_p7, nand_1_out, not_1_out, not_2_out, not_3_out, or_1_out,
       or_5_out, or_6_out, or_7_out, or_8_out, riscv_probe_1_p2, RST, SH, SLTIU, URET, W1, W2, W3,
       \单周期硬布线控制器_1_alu_src , \单周期硬布线控制器_1_s_type ;
  wire [1:0] INTnum, priority_encoder_1_out, register_1_q, \单周期硬布线控制器_1_memtoreg ;
  wire [3:0] RAM_Sel, \单周期硬布线控制器_1_alu_op ;
  wire [3:1] multiplexer_14_out;
  wire [4:0] multiplexer_4_out, multiplexer_5_out;
  wire [11:0] multiplexer_8_out;
  wire [12:0] CNT_num;
  wire [15:0] \总周期数 ;
  wire [31:0] ALUresult, and_1_out, B_ADD, bit_extender_1_out, bit_extender_2_out, bit_extender_3_out,
       INT_PC, JAL_ADD, mips_ram_1_p8, multiplexer_2_out, multiplexer_3_out, multiplexer_7_out,
       multiplexer_9_out, multiplexer_11_out, PC_4, R2, regifile_1_r1, RET_PC, Scene, shifter_1_out,
       shifter_2_out, shifter_3_out;

  Button \u_继续运行  (.out(Go));
  Button _1 ();  // open: out
  Button _2 ();  // open: out
  Button _3 ();  // open: out
  LED #(.active("true")) led_1 (.in(W1));
  LED #(.active("true")) led_2 (.in(W2));
  LED #(.active("true")) led_3 (.in(W3));
  Hex_Digit_Display hex_digit_display_1 (.value(LedData[31:28]));  // open: dp
  Comparator #(.width(16), .mode("twosComplement")) comparator_1 (
    .a(16'h23b), .b(\总周期数 ), .eq(comparator_1_eq));  // open: gt, lt
  Comparator #(.width(16), .mode("twosComplement")) comparator_2 (
    .a(\总周期数 ), .b(16'h1), .eq(comparator_2_eq));  // open: gt, lt
  Comparator #(.width(16), .mode("twosComplement")) comparator_3 (
    .a(\总周期数 ), .b(16'h4), .eq(comparator_3_eq));  // open: gt, lt
  Comparator #(.width(16), .mode("twosComplement")) comparator_4 (
    .a(\总周期数 ), .b(16'h7), .eq(comparator_4_eq));  // open: gt, lt
  Hex_Digit_Display hex_digit_display_2 (.value(LedData[23:20]));  // open: dp
  Hex_Digit_Display hex_digit_display_3 (.value(LedData[27:24]));  // open: dp
  or or_1 (or_1_out, comparator_1_eq, comparator_2_eq);
  assign IRA = or_1_out ? ~CLK : 1'bz;  // Controlled_Inverter controlled_inverter_1
  assign IRB = comparator_3_eq ? ~CLK : 1'bz;  // Controlled_Inverter controlled_inverter_2
  assign IRC = comparator_4_eq ? ~CLK : 1'bz;  // Controlled_Inverter controlled_inverter_3
  assign and_1_out = 32'hfffffffe & ALUresult;  // AND_Gate and_1, 32 bits wide
  Hex_Digit_Display hex_digit_display_4 (.value(LedData[15:12]));  // open: dp
  Hex_Digit_Display hex_digit_display_5 (.value(LedData[19:16]));  // open: dp
  Pull_Resistor #(.pull(0)) pull_resistor_1 (.node(IRA));
  Pull_Resistor #(.pull(0)) pull_resistor_2 (.node(IRB));
  Pull_Resistor #(.pull(0)) pull_resistor_3 (.node(IRC));
  Multiplexer #(.select(2), .width(32), .disabled("Z"), .enable("false")) multiplexer_1 (
    .in0(PC_4), .in1(and_1_out), .in2(JAL_ADD), .in3(B_ADD), .out(Scene), .sel(priority_encoder_1_out));
  or or_2 (W1, IR1_q, d_ff_1_q);
  or or_3 (W2, IR2_q, d_ff_2_q);
  or or_4 (W3, IR3_q, d_ff_3_q);
  Hex_Digit_Display hex_digit_display_6 (.value(LedData[11:8]));  // open: dp
  Hex_Digit_Display hex_digit_display_7 (.value(LedData[7:4]));  // open: dp
  // Probe on \总周期数 
  Priority_Encoder #(.select(2), .disabled(0)) priority_encoder_1 (
    .in0(1'b1), .in1(JALR), .in2(JAL), .in3(or_5_out), .out(priority_encoder_1_out));  // open: gs, en_out, en_in
  Multiplexer #(.select(1), .width(32), .disabled("Z"), .enable("false")) multiplexer_2 (
    .in0(Scene), .in1(RET_PC), .out(multiplexer_2_out), .sel(URET));
  D_Flip_Flop #(.trigger("rising"), .Pre_Clr_Positions("LEGACY"), .NegatePresetClear("false"), .enable("true"), .NewFFLayout("false")) d_ff_1 (
    .clk(IR1_t), .D(1'b1), .Q(d_ff_1_q), .reset(IR1_q));  // open: Qn, preset, en
  D_Flip_Flop #(.trigger("rising"), .Pre_Clr_Positions("LEGACY"), .NegatePresetClear("false"), .enable("true"), .NewFFLayout("false")) d_ff_2 (
    .clk(IR2_t), .D(1'b1), .Q(d_ff_2_q), .reset(IR2_q));  // open: Qn, preset, en
  D_Flip_Flop #(.trigger("rising"), .Pre_Clr_Positions("LEGACY"), .NegatePresetClear("false"), .enable("true"), .NewFFLayout("false")) d_ff_3 (
    .clk(IR3_t), .D(1'b1), .Q(d_ff_3_q), .reset(IR3_q));  // open: Qn, preset, en
  Hex_Digit_Display hex_digit_display_8 (.value(LedData[3:0]));  // open: dp
  or or_5 (or_5_out, and_2_out, and_3_out, and_4_out);
  Multiplexer #(.select(1), .width(32), .disabled("Z"), .enable("false")) multiplexer_3 (
    .in0(multiplexer_2_out), .in1(INT_PC), .out(multiplexer_3_out), .sel(INT));
  or or_6 (or_6_out, d_ff_1_q, IR1_q);
  or or_7 (or_7_out, d_ff_2_q, IR2_q);
  or or_8 (or_8_out, d_ff_3_q, IR3_q);
  and and_2 (and_2_out, Beq, ALU_t);
  and and_3 (and_3_out, ~ALU_t, Bne);  // AND_Gate
  and and_4 (and_4_out, BGE, ALU_t_t);
  Register #(.width(32), .trigger("rising"), .Select("low")) u_PC (
    .D(multiplexer_3_out), .en(not_1_out), .Q(PC), .clk(CLK), .clr(RST));
  not not_1 (not_1_out, halt);
  and and_5 (and_5_out, or_6_out, ~clear1);  // AND_Gate
  and and_6 (and_6_out, or_7_out, ~clear2);  // AND_Gate
  and and_7 (and_7_out, or_8_out, ~clear3);  // AND_Gate
  or or_9 (IR1_t, IR1, IRA);
  Button button_1 (.out(RST));
  D_Flip_Flop #(.trigger("rising"), .Pre_Clr_Positions("LEGACY"), .NegatePresetClear("false"), .enable("true"), .NewFFLayout("false")) u_IR1 (
    .clk(CLK), .D(and_5_out), .Q(IR1_q));  // open: Qn, preset, en, reset
  D_Flip_Flop #(.trigger("rising"), .Pre_Clr_Positions("LEGACY"), .NegatePresetClear("false"), .enable("true"), .NewFFLayout("false")) u_IR2 (
    .clk(CLK), .D(and_6_out), .Q(IR2_q));  // open: Qn, preset, en, reset
  D_Flip_Flop #(.trigger("rising"), .Pre_Clr_Positions("LEGACY"), .NegatePresetClear("false"), .enable("true"), .NewFFLayout("false")) u_IR3 (
    .clk(CLK), .D(and_7_out), .Q(IR3_q));  // open: Qn, preset, en, reset
  or or_10 (IR2_t, IR2, IRB);
  Adder #(.width(32)) adder_1 (.a(PC), .b(32'h4), .out(PC_4), .cin(1'b0));  // open: cout
  // RiscV_Probe riscv_probe_1: pin names not known; wires that end beside it: IR, riscv_probe_1_p2
  ROM #(.addrWidth(10), .dataWidth(32), .Select("high")) rom_1 (.addr(PC[11:2]), .data(IR));
  or or_11 (IR3_t, IR3, IRC);
  Priority_Encoder #(.select(2), .disabled("Z")) priority_encoder_2 (
    .in0(IR1_q), .in1(IR2_q), .in2(IR3_q), .out(INTnum), .gs(INTRequest));  // open: in3, en_out, en_in
  \单周期硬布线控制器  \u_单周期硬布线控制器_1  (
    .Funct({IR[30], IR[25], IR[14:12]}), .OP(IR[6:2]), .ALU_OP(\单周期硬布线控制器_1_alu_op ),
    .MemToReg(\单周期硬布线控制器_1_memtoreg [0]), .MemWrite(MemWrite), .ALU_SRC(\单周期硬布线控制器_1_alu_src ),
    .RegWrite(RegWrite), .ecall(ecall), .S_type(\单周期硬布线控制器_1_s_type ), .Jalr(JALR), .Beq(Beq), .JAL(JAL),
    .Bne(Bne), .in_3(IR[21]), .uret(URET), .SRL(riscv_probe_1_p2), .SLTIU(SLTIU), .SH(SH), .BGE(BGE));  // open: rs1_used, rs2_used, CSRRSI, CSRRCI
  Multiplexer #(.select(1), .width(5), .disabled("Z"), .enable("false")) multiplexer_4 (
    .in0(IR[19:15]), .in1(5'b10001), .out(multiplexer_4_out), .sel(ecall));
  Multiplexer #(.select(1), .width(5), .disabled("Z"), .enable("false")) multiplexer_5 (
    .in0(IR[24:20]), .in1(5'b01010), .out(multiplexer_5_out), .sel(ecall));
  assign bit_extender_1_out = {{20{IR[31]}}, {IR[31], IR[7], IR[30:25], IR[11:8]}};  // Bit_Extender bit_extender_1
  assign bit_extender_2_out = {{12{IR[31]}}, {IR[31], IR[19:12], IR[20], IR[30:21]}};  // Bit_Extender bit_extender_2
  Multiplexer #(.select(1), .width(32), .disabled("Z"), .enable("false")) multiplexer_6 (
    .in0(multiplexer_11_out), .in1(multiplexer_7_out), .out(RDin), .sel(SLTIU));
  Multiplexer #(.select(1), .width(32), .disabled("Z"), .enable("false")) multiplexer_7 (
    .in0({32{1'b0}}), .in1(32'h1), .out(multiplexer_7_out), .sel(ALU));
  assign bit_extender_3_out = {{20{multiplexer_8_out[11]}}, multiplexer_8_out};  // Bit_Extender bit_extender_3
  Multiplexer #(.select(1), .width(12), .disabled("Z"), .enable("false")) multiplexer_8 (
    .in0(IR[31:20]), .in1({IR[31:25], IR[11:7]}), .out(multiplexer_8_out), .sel(\单周期硬布线控制器_1_s_type ));
  Shifter #(.width(32), .shift("ll")) shifter_1 (.in(bit_extender_1_out), .\dist (5'b00001), .out(shifter_1_out));
  Shifter #(.width(32), .shift("ll")) shifter_2 (.in(bit_extender_2_out), .\dist (5'b00001), .out(shifter_2_out));
  Regifile regifile_1 (
    .Din(RDin), .Clk(CLK), .R1(regifile_1_r1), .R2(R2), .WE(RegWrite), .W_num(IR[11:7]),
    .R1_num(multiplexer_4_out), .R2_num(multiplexer_5_out));
  Adder #(.width(32)) adder_2 (.a(PC), .b(shifter_1_out), .out(B_ADD), .cin(1'b0));  // open: cout
  Adder #(.width(32)) adder_3 (.a(PC), .b(shifter_2_out), .out(JAL_ADD), .cin(1'b0));  // open: cout
  Multiplexer #(.select(1), .width(32), .disabled("Z"), .enable("false")) multiplexer_9 (
    .in0(R2), .in1(bit_extender_3_out), .out(multiplexer_9_out), .sel(\单周期硬布线控制器_1_alu_src ));
  D_Flip_Flop #(.trigger("high"), .Pre_Clr_Positions("LEGACY"), .NegatePresetClear("false"), .enable("true"), .NewFFLayout("false")) d_ff_4 (.Q(d_ff_4_q));  // open: clk, D, Qn, preset, en, reset
  // Probe on 13'hc
  ALU alu_1 (
    .X(regifile_1_r1), .Y(multiplexer_9_out), .AluOP(\单周期硬布线控制器_1_alu_op ), .Equal(ALU_t),
    .Result(ALUresult), .out_4(ALU_t_t), .out_6(ALU));  // open: Result_2
  Comparator #(.width(32), .mode("twosComplement")) comparator_5 (
    .a(regifile_1_r1), .b(32'h22), .eq(comparator_5_eq));  // open: gt, lt
  not not_2 (not_2_out, comparator_5_eq);
  and and_8 (and_8_out, comparator_5_eq, ecall);
  Comparator #(.width(13), .mode("twosComplement")) comparator_6 (
    .a(CNT_num), .b(13'hc), .eq(comparator_6_eq), .lt(comparator_6_lt));  // open: gt
  Clock #(.highDuration(1), .lowDuration(1)) clock_1 (.out(clock_1_out));
  // Probe on \单周期硬布线控制器_1_alu_op 
  D_Flip_Flop #(.trigger("falling"), .Pre_Clr_Positions("ABOVE_BELOW"), .NegatePresetClear("false"), .enable("true"), .NewFFLayout("true")) d_ff_5 (
    .clk(CLK), .D(not_2_out), .Q(halt), .en(ecall), .reset(Go));  // open: Qn, preset
  Register #(.width(32), .trigger("rising"), .Select("low")) PC_2 (
    .D(R2), .en(and_8_out), .Q(LedData), .clk(CLK));  // open: clr
  Counter #(.width(13), .max('h1fff), .ongoal("stay"), .trigger("rising"), .behavior("old")) counter_1 (
    .count(comparator_6_lt), .Q(CNT_num), .clk(clock_1_out));  // open: load, D, carry, clr, preset
  not not_3 (not_3_out, halt);
  nand nand_1 (nand_1_out, d_ff_4_q, comparator_6_eq);
  Counter #(.width(16), .max('hffff), .ongoal("wrap"), .trigger("rising"), .behavior("new")) counter_2 (
    .count(not_3_out), .Q(\总周期数 ), .clk(CLK));  // open: load, D, carry, clr, preset, down
  assign CLK = nand_1_out ? clock_1_out : 1'bz;  // Controlled_Buffer controlled_buffer_1
  Pull_Resistor #(.pull(1)) pull_resistor_4 (.node(CLK));
  Register #(.width(2), .trigger("rising"), .Select("low")) register_1 (
    .D(INTnum), .en(INT), .Q(register_1_q), .clk(CLK));  // open: clr
  // MIPS_RAM mips_ram_1: pin names not known; wires that end beside it: ALUresult[11:2], MDin, MemWrite, RAM_Sel, CLK, 1'b1, mips_ram_1_p7, mips_ram_1_p8
  Button button_2 (.out(mips_ram_1_p7));
  and and_9 (and_9_out, INTRequest, ~URET);  // AND_Gate
  Multiplexer #(.select(2), .width(32), .disabled("Z"), .enable("false")) multiplexer_10 (
    .in0(32'h30ac), .in1(32'h3150), .in2(32'h31f4), .out(INT_PC), .sel(INTnum));  // open: in3
  and and_10 (INT, INTRequest, ~IE);  // AND_Gate
  Demultiplexer #(.select(2), .width(1), .tristate("false"), .disabled("Z"), .enable("false")) demultiplexer_1 (
    .out0(clear1), .out1(clear2), .out2(clear3), .in(URET), .sel(register_1_q));  // open: out3
  D_Flip_Flop #(.trigger("rising"), .Pre_Clr_Positions("LEGACY"), .NegatePresetClear("false"), .enable("true"), .NewFFLayout("false")) d_ff_6 (
    .clk(CLK), .D(and_9_out), .Q(IE));  // open: Qn, preset, en, reset
  Register #(.width(32), .trigger("rising"), .Select("low")) register_2 (
    .D(Scene), .en(INT), .Q(RET_PC), .clk(CLK));  // open: clr
  or or_12 (\单周期硬布线控制器_1_memtoreg [1], JAL, JALR);
  Multiplexer #(.select(2), .width(32), .disabled("Z"), .enable("false")) multiplexer_11 (
    .in0(ALUresult), .in1(mips_ram_1_p8), .in2(PC_4), .out(multiplexer_11_out), .sel(\单周期硬布线控制器_1_memtoreg ));  // open: in3
  Multiplexer #(.select(1), .width(32), .disabled("Z"), .enable("false")) multiplexer_12 (
    .in0(R2), .in1(shifter_3_out), .out(MDin), .sel(ALUresult[1]));
  Shifter #(.width(32), .shift("ll")) shifter_3 (.in(R2), .\dist (5'b10000), .out(shifter_3_out));
  Multiplexer #(.select(1), .width(4), .disabled("Z"), .enable("false")) multiplexer_13 (
    .in0(4'b1111), .in1({{2{multiplexer_14_out[3]}}, {2{multiplexer_14_out[1]}}}), .out(RAM_Sel), .sel(SH));
  Multiplexer #(.select(1), .width(1), .disabled("Z"), .enable("false")) multiplexer_14 (
    .in0(1'b1), .in1(1'b0), .out(multiplexer_14_out[1]), .sel(ALUresult[1]));
  Multiplexer #(.select(1), .width(1), .disabled("Z"), .enable("false")) multiplexer_15 (
    .in0(1'b0), .in1(1'b1), .out(multiplexer_14_out[3]), .sel(ALUresult[1]));

  // Other names for the same wires on the sheet: JALR_ADD[31:0] = ALUresult

  // Notes on the sheet:
  //   中断源
  //   中断等待指示
  //   总复位信号应将除ROM以外所有存储组件全部清零
  //   单级中断测试信号模拟器
  //   数码管输出
  //   数码管输出应该用寄存器锁存，否则显示数据只能一闪而过
  //   Reset 
  //   Reset 
  //   Reset 
  //   指令存储器
  //   指令探针
  //   contents of rom_1 (hex, n*v repeats v):
  //   7d000113 100413 1f41993 41f9d993 433 c00913 800b13 140413 f47413 800293 100313 499993 89e9b3 1300533
  //   2200893 73 406282b3 fe0294e3 140413 f00f93 1f47433 1c41413 800293 100313 49d993 89e9b3 1300533
  //   2200893 73 406282b3 fe0294e3 1c45413 406b0b33 b0463 f95ff06f 2b3 fff2c293 1029293 fff2e293 500533
  //   2200893 73 f5dff06f 1112023 410113 a12023 410113 812023 410113 1312023 410113 1412023 410113 1512023
  //   410113 1612023 410113 100b13 300a13 100a93 1600433 441413 14469b3 1300533 2200893 73 fe0416e3
  //   415a0a33 fe0a10e3 ffc10113 12b03 ffc10113 12a83 ffc10113 12a03 ffc10113 12983 ffc10113 12403
  //   ffc10113 12503 ffc10113 12883 200073 1112023 410113 a12023 410113 812023 410113 1312023 410113
  //   1412023 410113 1512023 410113 1612023 410113 200b13 300a13 100a93 1600433 441413 14469b3 1300533
  //   2200893 73 fe0416e3 415a0a33 fe0a10e3 ffc10113 12b03 ffc10113 12a83 ffc10113 12a03 ffc10113 12983
  //   ffc10113 12403 ffc10113 12503 ffc10113 12883 200073 1112023 410113 a12023 410113 812023 410113
  //   1312023 410113 1412023 410113 1512023 410113 1612023 410113 300b13 300a13 100a93 1600433 441413
  //   14469b3 1300533 2200893 73 fe0416e3 415a0a33 fe0a10e3 ffc10113 12b03 ffc10113 12a83 ffc10113 12a03
  //   ffc10113 12983 ffc10113 12403 ffc10113 12503 ffc10113 12883 200073
  //   rs1
  //   rs2
  //   指令字
  //   rd
  //   imm-i
  //   rd
  //   JAL
  //   JALR
  //   URET
  //   SRL
  //   imm-j
  //   beq/bne
  //   jal
  //   Beq
  //   Bne
  //   MemToReg
  //   MemWrite
  //   AluOP
  //   AluSrcB
  //   RegWrite
  //   S_type
  //   为方便自动评测，需要输出PC，IR，寄存器堆写如数据RDin
  //   RAM写使能MemWrite、RAM写入数据MDin等信号
  //   SignImm
  //   控制位
  //   暂停节拍，不能为0
  //   戳工具置1进入计数暂停模式，ctrl+k时钟自动运行到对应节拍暂停
  //   ctrl+k关闭时钟连续运行，将控制位置零，进入单步调试模式调试
  //   可计数暂停的时钟源
  //   数据存储器
endmodule

module \单周期_多级中断  (
  input  IR1,
  input  IR2,
  input  IR3,
  output RegWrite,
  output MemWrite,
  output [31:0] PC,
  output [31:0] IR,
  output [31:0] RDin,
  output [31:0] MDin,
  output [31:0] LedData
);

  wire ALU, ALU_t, ALU_t_t, and_2_out, and_3_out, and_4_out, and_5_out, and_6_out, and_7_out, and_8_out,
       and_9_out, and_10_out, and_12_out, and_13_out, and_14_out, and_15_out, Beq, BGE, Bne, button_2_out,
       clear1, clear2, clear3, CLK, clock_1_out, comparator_1_eq, comparator_2_eq, comparator_3_eq,
       comparator_4_eq, comparator_5_eq, comparator_6_eq, comparator_6_lt, comparator_7_eq, comparator_9_lt,
       CSRRCI, CSRRSI, d_ff_1_q, d_ff_2_q, d_ff_3_q, d_ff_4_q, decoder_1_out1, decoder_1_out2,
       decoder_1_out3, decoder_2_out1, decoder_2_out2, decoder_2_out3, ecall, Go, halt, IE, in, INT,
       INTRequest, IR1_q, IR1_t, IR2_q, IR2_t, IR3_q, IR3_t, IRA, IRB, IRC, JAL, JALR, nand_1_out, not_1_out,
       not_2_out, not_3_out, not_4_out, or_1_out, or_2_out, or_6_out, or_7_out, or_8_out, or_11_out,
       or_13_out, or_15_out, or_16_out, or_17_out, RST, SH, SLTIU, URET, W1, W2, W3, \单周期硬布线控制器_1_alu_src ,
       \单周期硬布线控制器_1_s_type ;
  wire [1:0] adder_4_out, count, CUR_IRnum, IRnum, multiplexer_11_out, priority_encoder_1_out, Qnum,
       register_4_q, register_5_q, register_6_q, \单周期硬布线控制器_1_memtoreg ;
  wire [3:0] RAM_Sel, \单周期硬布线控制器_1_alu_op ;
  wire [3:1] multiplexer_17_out;
  wire [4:0] multiplexer_6_out, multiplexer_7_out;
  wire [11:0] multiplexer_8_out;
  wire [12:0] CNT_num;
  wire [15:0] \总周期数 ;
  wire [31:0] ALUresult, and_1_out, B_ADD, bit_extender_1_out, bit_extender_2_out, bit_extender_3_out,
       counter_3_q, INT_PC, JAL_ADD, mips_ram_1_p8, multiplexer_2_out, multiplexer_3_out, multiplexer_10_out,
       multiplexer_12_out, multiplexer_14_out, PC_4, R2, regifile_1_r1, register_1_q, register_2_q,
       register_3_q, RET_PC, Scene, shifter_1_out, shifter_2_out, shifter_3_out;

  Button \u_继续运行  (.out(Go));
  Button _1 ();  // open: out
  Button _2 ();  // open: out
  Button _3 ();  // open: out
  LED #(.active("true")) led_1 (.in(W1));
  LED #(.active("true")) led_2 (.in(W2));
  LED #(.active("true")) led_3 (.in(W3));
  Hex_Digit_Display hex_digit_display_1 (.value(LedData[31:28]));  // open: dp
  Comparator #(.width(16), .mode("twosComplement")) comparator_1 (
    .a(\总周期数 ), .b(16'h7), .eq(comparator_1_eq));  // open: gt, lt
  Comparator #(.width(16), .mode("twosComplement")) comparator_2 (
    .a(\总周期数 ), .b(16'h241), .eq(comparator_2_eq));  // open: gt, lt
  // Probe on RET_PC
  // Probe on Scene
  Hex_Digit_Display hex_digit_display_2 (.value(LedData[27:24]));  // open: dp
  Hex_Digit_Display hex_digit_display_3 (.value(LedData[23:20]));  // open: dp
  Comparator #(.width(16), .mode("twosComplement")) comparator_3 (
    .a(16'h258), .b(\总周期数 ), .eq(comparator_3_eq));  // open: gt, lt
  or or_1 (or_1_out, comparator_3_eq, comparator_4_eq);
  Comparator #(.width(16), .mode("twosComplement")) comparator_4 (
    .a(\总周期数 ), .b(16'h1), .eq(comparator_4_eq));  // open: gt, lt
  Comparator #(.width(16), .mode("twosComplement")) comparator_5 (
    .a(\总周期数 ), .b(16'h4), .eq(comparator_5_eq));  // open: gt, lt
  or or_2 (or_2_out, comparator_1_eq, comparator_2_eq);
  // Probe on INT_PC
  // Probe on PC
  Hex_Digit_Display hex_digit_display_4 (.value(LedData[15:12]));  // open: dp
  Hex_Digit_Display hex_digit_display_5 (.value(LedData[19:16]));  // open: dp
  Pull_Resistor #(.pull(0)) pull_resistor_1 (.node(IRA));
  assign IRA = or_1_out ? ~CLK : 1'bz;  // Controlled_Inverter controlled_inverter_1
  Pull_Resistor #(.pull(0)) pull_resistor_2 (.node(IRB));
  assign IRB = comparator_5_eq ? ~CLK : 1'bz;  // Controlled_Inverter controlled_inverter_2
  Pull_Resistor #(.pull(0)) pull_resistor_3 (.node(IRC));
  assign IRC = or_2_out ? ~CLK : 1'bz;  // Controlled_Inverter controlled_inverter_3
  or or_3 (W1, IR1_q, d_ff_1_q);
  or or_4 (W2, IR2_q, d_ff_2_q);
  or or_5 (W3, IR3_q, d_ff_3_q);
  Hex_Digit_Display hex_digit_display_6 (.value(LedData[7:4]));  // open: dp
  Hex_Digit_Display hex_digit_display_7 (.value(LedData[11:8]));  // open: dp
  // Probe on \总周期数 
  D_Flip_Flop #(.trigger("rising"), .Pre_Clr_Positions("LEGACY"), .NegatePresetClear("false"), .enable("true"), .NewFFLayout("false")) d_ff_1 (
    .clk(IR1_t), .D(1'b1), .Q(d_ff_1_q), .reset(IR1_q));  // open: Qn, preset, en
  D_Flip_Flop #(.trigger("rising"), .Pre_Clr_Positions("LEGACY"), .NegatePresetClear("false"), .enable("true"), .NewFFLayout("false")) d_ff_2 (
    .clk(IR2_t), .D(1'b1), .Q(d_ff_2_q), .reset(IR2_q));  // open: Qn, preset, en
  D_Flip_Flop #(.trigger("rising"), .Pre_Clr_Positions("LEGACY"), .NegatePresetClear("false"), .enable("true"), .NewFFLayout("false")) d_ff_3 (
    .clk(IR3_t), .D(1'b1), .Q(d_ff_3_q), .reset(IR3_q));  // open: Qn, preset, en
  Hex_Digit_Display hex_digit_display_8 (.value(LedData[3:0]));  // open: dp
  or or_6 (or_6_out, d_ff_1_q, IR1_q);
  or or_7 (or_7_out, d_ff_2_q, IR2_q);
  or or_8 (or_8_out, d_ff_3_q, IR3_q);
  assign and_1_out = 32'hfffffffe & ALUresult;  // AND_Gate and_1, 32 bits wide
  and and_2 (and_2_out, or_6_out, ~clear1);  // AND_Gate
  and and_3 (and_3_out, or_7_out, ~clear2);  // AND_Gate
  and and_4 (and_4_out, or_8_out, ~clear3);  // AND_Gate
  or or_9 (IR1_t, IR1, IRA);
  Multiplexer #(.select(2), .width(32), .disabled("Z"), .enable("false")) multiplexer_1 (
    .in0(PC_4), .in1(and_1_out), .in2(JAL_ADD), .in3(B_ADD), .out(Scene), .sel(priority_encoder_1_out));
  D_Flip_Flop #(.trigger("rising"), .Pre_Clr_Positions("LEGACY"), .NegatePresetClear("false"), .enable("true"), .NewFFLayout("false")) u_IR1 (
    .clk(CLK), .D(and_2_out), .Q(IR1_q));  // open: Qn, preset, en, reset
  D_Flip_Flop #(.trigger("rising"), .Pre_Clr_Positions("LEGACY"), .NegatePresetClear("false"), .enable("true"), .NewFFLayout("false")) u_IR2 (
    .clk(CLK), .D(and_3_out), .Q(IR2_q));  // open: Qn, preset, en, reset
  D_Flip_Flop #(.trigger("rising"), .Pre_Clr_Positions("LEGACY"), .NegatePresetClear("false"), .enable("true"), .NewFFLayout("false")) u_IR3 (
    .clk(CLK), .D(and_4_out), .Q(IR3_q));  // open: Qn, preset, en, reset
  or or_10 (IR2_t, IR2, IRB);
  Priority_Encoder #(.select(2), .disabled(0)) priority_encoder_1 (
    .in0(1'b1), .in1(JALR), .in2(JAL), .in3(or_11_out), .out(priority_encoder_1_out));  // open: gs, en_out, en_in
  Multiplexer #(.select(1), .width(32), .disabled("Z"), .enable("false")) multiplexer_2 (
    .in0(Scene), .in1(RET_PC), .out(multiplexer_2_out), .sel(URET));
  Decoder #(.select(2), .tristate("false"), .disabled("Z"), .enable("false")) decoder_1 (
    .out1(decoder_1_out1), .out2(decoder_1_out2), .out3(decoder_1_out3), .sel(IRnum));  // open: out0
  or or_11 (or_11_out, and_8_out, and_9_out, and_10_out);
  // Probe on multiplexer_3_out
  Multiplexer #(.select(1), .width(32), .disabled("Z"), .enable("false")) multiplexer_3 (
    .in0(multiplexer_2_out), .in1(INT_PC), .out(multiplexer_3_out), .sel(INT));
  not not_1 (not_1_out, halt);
  Demultiplexer #(.select(2), .width(1), .tristate("false"), .disabled("Z"), .enable("false")) demultiplexer_1 (
    .out1(clear1), .out2(clear2), .out3(clear3), .in(URET), .sel(IRnum));  // open: out0
  and and_5 (and_5_out, INT, decoder_1_out1);
  and and_6 (and_6_out, INT, decoder_1_out2);
  and and_7 (and_7_out, INT, decoder_1_out3);
  or or_12 (IR3_t, IR3, IRC);
  Button button_1 (.out(RST));
  and and_8 (and_8_out, Beq, ALU_t);
  and and_9 (and_9_out, ~ALU_t, Bne);  // AND_Gate
  and and_10 (and_10_out, BGE, ALU_t_t);
  Register #(.width(32), .trigger("rising"), .Select("low")) u_PC (
    .D(multiplexer_3_out), .en(not_1_out), .Q(PC), .clk(CLK), .clr(RST));
  Priority_Encoder #(.select(2), .disabled("Z")) priority_encoder_2 (
    .in0(1'b1), .in1(IR1_q), .in2(IR2_q), .in3(IR3_q), .out(IRnum), .gs(INTRequest));  // open: en_out, en_in
  Adder #(.width(32)) adder_1 (.a(PC), .b(32'h4), .out(PC_4), .cin(1'b0));  // open: cout
  Multiplexer #(.select(2), .width(32), .disabled("Z"), .enable("false")) multiplexer_4 (
    .in0(Scene), .in1(32'h30ac), .in2(32'h3158), .in3(32'h3204), .out(INT_PC), .sel(IRnum));
  and and_11 (INT, IE, in, INTRequest);
  // RiscV_Probe riscv_probe_1: pin names not known; wires that end beside it: IR
  Register #(.width(32), .trigger("rising"), .Select("low")) register_1 (
    .D(Scene), .en(and_5_out), .Q(register_1_q), .clk(CLK));  // open: clr
  Register #(.width(32), .trigger("rising"), .Select("low")) register_2 (
    .D(Scene), .en(and_6_out), .Q(register_2_q), .clk(CLK));  // open: clr
  Register #(.width(32), .trigger("rising"), .Select("low")) register_3 (
    .D(Scene), .en(and_7_out), .Q(register_3_q), .clk(CLK));  // open: clr
  ROM #(.addrWidth(10), .dataWidth(32), .Select("high")) rom_1 (.addr(PC[11:2]), .data(IR));
  Multiplexer #(.select(2), .width(32), .disabled("Z"), .enable("false")) multiplexer_5 (
    .in1(register_1_q), .in2(register_2_q), .in3(register_3_q), .out(RET_PC), .sel(CUR_IRnum));  // open: in0
  \单周期硬布线控制器  \u_单周期硬布线控制器_1  (
    .Funct({IR[30], IR[25], IR[14:12]}), .OP(IR[6:2]), .ALU_OP(\单周期硬布线控制器_1_alu_op ),
    .MemToReg(\单周期硬布线控制器_1_memtoreg [0]), .MemWrite(MemWrite), .ALU_SRC(\单周期硬布线控制器_1_alu_src ),
    .RegWrite(RegWrite), .ecall(ecall), .S_type(\单周期硬布线控制器_1_s_type ), .Jalr(JALR), .Beq(Beq), .JAL(JAL),
    .Bne(Bne), .in_3(IR[21]), .uret(URET), .SLTIU(SLTIU), .SH(SH), .BGE(BGE), .CSRRSI(CSRRSI), .CSRRCI(CSRRCI));  // open: SRL, rs1_used, rs2_used
  Decoder #(.select(2), .tristate("false"), .disabled("Z"), .enable("false")) decoder_2 (
    .out1(decoder_2_out1), .out2(decoder_2_out2), .out3(decoder_2_out3), .sel(Qnum));  // open: out0
  Multiplexer #(.select(1), .width(5), .disabled("Z"), .enable("false")) multiplexer_6 (
    .in0(IR[19:15]), .in1(5'b10001), .out(multiplexer_6_out), .sel(ecall));
  Multiplexer #(.select(1), .width(5), .disabled("Z"), .enable("false")) multiplexer_7 (
    .in0(IR[24:20]), .in1(5'b01010), .out(multiplexer_7_out), .sel(ecall));
  Multiplexer #(.select(1), .width(12), .disabled("Z"), .enable("false")) multiplexer_8 (
    .in0(IR[31:20]), .in1({IR[31:25], IR[11:7]}), .out(multiplexer_8_out), .sel(\单周期硬布线控制器_1_s_type ));
  assign bit_extender_1_out = {{20{IR[31]}}, {IR[31], IR[7], IR[30:25], IR[11:8]}};  // Bit_Extender bit_extender_1
  Shifter #(.width(32), .shift("ll")) shifter_1 (.in(bit_extender_1_out), .\dist (5'b00001), .out(shifter_1_out));
  assign bit_extender_2_out = {{12{IR[31]}}, {IR[31], IR[19:12], IR[20], IR[30:21]}};  // Bit_Extender bit_extender_2
  Shifter #(.width(32), .shift("ll")) shifter_2 (.in(bit_extender_2_out), .\dist (5'b00001), .out(shifter_2_out));
  Multiplexer #(.select(1), .width(32), .disabled("Z"), .enable("false")) multiplexer_9 (
    .in0(multiplexer_14_out), .in1(multiplexer_10_out), .out(RDin), .sel(SLTIU));
  Multiplexer #(.select(1), .width(32), .disabled("Z"), .enable("false")) multiplexer_10 (
    .in0({32{1'b0}}), .in1(32'h1), .out(multiplexer_10_out), .sel(ALU));
  Multiplexer #(.select(1), .width(2), .disabled("Z"), .enable("false")) multiplexer_11 (
    .in0(2'b11), .in1(2'b01), .out(multiplexer_11_out), .sel(INT));
  D_Flip_Flop #(.trigger("high"), .Pre_Clr_Positions("LEGACY"), .NegatePresetClear("false"), .enable("true"), .NewFFLayout("false")) d_ff_4 (.Q(d_ff_4_q));  // open: clk, D, Qn, preset, en, reset
  // Probe on 13'hcd
  Regifile regifile_1 (
    .Din(RDin), .Clk(CLK), .R1(regifile_1_r1), .R2(R2), .WE(RegWrite), .W_num(IR[11:7]),
    .R1_num(multiplexer_6_out), .R2_num(multiplexer_7_out));
  assign bit_extender_3_out = {{20{multiplexer_8_out[11]}}, multiplexer_8_out};  // Bit_Extender bit_extender_3
  and and_12 (and_12_out, decoder_2_out1, INT);
  and and_13 (and_13_out, decoder_2_out2, INT);
  and and_14 (and_14_out, decoder_2_out3, INT);
  Comparator #(.width(13), .mode("twosComplement")) comparator_6 (
    .a(CNT_num), .b(13'hcd), .eq(comparator_6_eq), .lt(comparator_6_lt));  // open: gt
  Clock #(.highDuration(1), .lowDuration(1)) clock_1 (.out(clock_1_out));
  Adder #(.width(32)) adder_2 (.a(PC), .b(shifter_1_out), .out(B_ADD), .cin(1'b0));  // open: cout
  Adder #(.width(32)) adder_3 (.a(PC), .b(shifter_2_out), .out(JAL_ADD), .cin(1'b0));  // open: cout
  Adder #(.width(2)) adder_4 (.a(count), .b(multiplexer_11_out), .out(adder_4_out), .cin(1'b0));  // open: cout
  Counter #(.width(13), .max('h1fff), .ongoal("stay"), .trigger("rising"), .behavior("old")) counter_1 (
    .count(comparator_6_lt), .Q(CNT_num), .clk(clock_1_out));  // open: load, D, carry, clr, preset
  Register #(.width(2), .trigger("rising"), .Select("low")) register_4 (
    .D(IRnum), .en(and_12_out), .Q(register_4_q), .clk(CLK));  // open: clr
  Register #(.width(2), .trigger("rising"), .Select("low")) register_5 (
    .D(IRnum), .en(and_13_out), .Q(register_5_q), .clk(CLK));  // open: clr
  Register #(.width(2), .trigger("rising"), .Select("low")) register_6 (
    .D(IRnum), .en(and_14_out), .Q(register_6_q), .clk(CLK));  // open: clr
  or or_13 (or_13_out, INT, URET);
  nand nand_1 (nand_1_out, d_ff_4_q, comparator_6_eq);
  Multiplexer #(.select(1), .width(32), .disabled("Z"), .enable("false")) multiplexer_12 (
    .in0(R2), .in1(bit_extender_3_out), .out(multiplexer_12_out), .sel(\单周期硬布线控制器_1_alu_src ));
  Comparator #(.width(32), .mode("twosComplement")) comparator_7 (
    .a(regifile_1_r1), .b(32'h22), .eq(comparator_7_eq));  // open: gt, lt
  Register #(.width(2), .trigger("rising"), .Select("low")) register_7 (
    .D(adder_4_out), .en(or_13_out), .Q(count), .clk(CLK));  // open: clr
  assign CLK = nand_1_out ? clock_1_out : 1'bz;  // Controlled_Buffer controlled_buffer_1
  Pull_Resistor #(.pull(1)) pull_resistor_4 (.node(CLK));
  // Probe on \单周期硬布线控制器_1_alu_op 
  ALU alu_1 (
    .X(regifile_1_r1), .Y(multiplexer_12_out), .AluOP(\单周期硬布线控制器_1_alu_op ), .Equal(ALU_t),
    .Result(ALUresult), .out_4(ALU_t_t), .out_6(ALU));  // open: Result_2
  not not_2 (not_2_out, comparator_7_eq);
  Register #(.width(32), .trigger("rising"), .Select("low")) PC_2 (
    .D(R2), .en(and_15_out), .Q(LedData), .clk(CLK));  // open: clr
  and and_15 (and_15_out, comparator_7_eq, ecall);
  D_Flip_Flop #(.trigger("falling"), .Pre_Clr_Positions("ABOVE_BELOW"), .NegatePresetClear("false"), .enable("true"), .NewFFLayout("true")) d_ff_5 (
    .clk(CLK), .D(not_2_out), .Q(halt), .en(ecall), .reset(Go));  // open: Qn, preset
  Multiplexer #(.select(2), .width(2), .disabled("Z"), .enable("false")) multiplexer_13 (
    .in0(2'b00), .in1(register_4_q), .in2(register_5_q), .in3(register_6_q), .out(CUR_IRnum), .sel(count));
  Adder #(.width(2)) adder_5 (.a(count), .b(2'b01), .out(Qnum), .cin(1'b0));  // open: cout
  not not_3 (not_3_out, halt);
  Counter #(.width(16), .max('hffff), .ongoal("wrap"), .trigger("rising"), .behavior("new")) counter_2 (
    .count(not_3_out), .Q(\总周期数 ), .clk(CLK));  // open: load, D, carry, clr, preset, down
  Button button_2 (.out(button_2_out));
  Comparator #(.width(2), .mode("unsigned")) comparator_8 (.a(CUR_IRnum), .b(IRnum), .lt(in));  // open: gt, eq
  // MIPS_RAM mips_ram_1: pin names not known; wires that end beside it: ALUresult[11:2], MDin, MemWrite, RAM_Sel, CLK, 1'b1, button_2_out, mips_ram_1_p8
  or or_14 (\单周期硬布线控制器_1_memtoreg [1], JAL, JALR);
  Counter #(.width(32), .max('hffffffff), .ongoal("wrap"), .trigger("rising"), .behavior("new")) counter_3 (
    .Q(counter_3_q), .clk(CLK));  // open: load, D, count, carry, clr, preset, down
  Multiplexer #(.select(2), .width(32), .disabled("Z"), .enable("false")) multiplexer_14 (
    .in0(ALUresult), .in1(mips_ram_1_p8), .in2(PC_4), .out(multiplexer_14_out), .sel(\单周期硬布线控制器_1_memtoreg ));  // open: in3
  not not_4 (not_4_out, or_15_out);
  or or_15 (or_15_out, INT, CSRRCI);
  or or_16 (or_16_out, CSRRCI, CSRRSI);
  or or_17 (or_17_out, or_16_out, comparator_9_lt, INT, URET);
  Comparator #(.width(32), .mode("twosComplement")) comparator_9 (
    .a(counter_3_q), .b(32'h2), .lt(comparator_9_lt));  // open: gt, eq
  Register #(.width(1), .trigger("rising"), .Select("low")) register_8 (
    .D(not_4_out), .en(or_17_out), .Q(IE), .clk(CLK));  // open: clr
  Shifter #(.width(32), .shift("ll")) shifter_3 (.in(R2), .\dist (5'b10000), .out(shifter_3_out));
  Multiplexer #(.select(1), .width(32), .disabled("Z"), .enable("false")) multiplexer_15 (
    .in0(R2), .in1(shifter_3_out), .out(MDin), .sel(ALUresult[1]));
  Multiplexer #(.select(1), .width(4), .disabled("Z"), .enable("false")) multiplexer_16 (
    .in0(4'b1111), .in1({{2{multiplexer_17_out[3]}}, {2{multiplexer_17_out[1]}}}), .out(RAM_Sel), .sel(SH));
  Multiplexer #(.select(1), .width(1), .disabled("Z"), .enable("false")) multiplexer_17 (
    .in0(1'b1), .in1(1'b0), .out(multiplexer_17_out[1]), .sel(ALUresult[1]));
  Multiplexer #(.select(1), .width(1), .disabled("Z"), .enable("false")) multiplexer_18 (
    .in0(1'b0), .in1(1'b1), .out(multiplexer_17_out[3]), .sel(ALUresult[1]));

  // Other names for the same wires on the sheet: JALR_ADD[31:0] = ALUresult

  // Notes on the sheet:
  //   中断源
  //   中断等待指示
  //   总复位信号应将除ROM以外所有存储组件全部清零
  //   多级中断测试信号模拟器
  //   数码管输出
  //   数码管输出应该用寄存器锁存，否则显示数据只能一闪而过
  //   Reset 
  //   Reset 
  //   Reset 
  //   指令存储器
  //   为方便自动评测，需要输出PC，IR，寄存器堆写如数据RDin
  //   指令探针
  //   指令字
  //   contents of rom_1 (hex, n*v repeats v):
  //   7d000113 100413 1f41993 41f9d993 433 c00913 800b13 140413 f47413 800293 100313 499993 89e9b3 1300533
  //   2200893 73 406282b3 fe0294e3 140413 f00f93 1f47433 1c41413 800293 100313 49d993 89e9b3 1300533
  //   2200893 73 406282b3 fe0294e3 1c45413 406b0b33 b0463 f95ff06f 2b3 fff2c293 1029293 fff2e293 500533
  //   2200893 73 f5dff06f 1112023 410113 a12023 410113 812023 410113 1312023 410113 1412023 410113 1512023
  //   410113 1612023 410113 40e073 100b13 300a13 100a93 1600433 441413 14469b3 1300533 2200893 73 fe0416e3
  //   415a0a33 fe0a10e3 40f073 ffc10113 12b03 ffc10113 12a83 ffc10113 12a03 ffc10113 12983 ffc10113 12403
  //   ffc10113 12503 ffc10113 12883 200073 1112023 410113 a12023 410113 812023 410113 1312023 410113
  //   1412023 410113 1512023 410113 1612023 410113 40e073 200b13 300a13 100a93 1600433 441413 14469b3
  //   1300533 2200893 73 fe0416e3 415a0a33 fe0a10e3 40f073 ffc10113 12b03 ffc10113 12a83 ffc10113 12a03
  //   ffc10113 12983 ffc10113 12403 ffc10113 12503 ffc10113 12883 200073 1112023 410113 a12023 410113
  //   812023 410113 1312023 410113 1412023 410113 1512023 410113 1612023 410113 40e073 300b13 300a13
  //   100a93 1600433 441413 14469b3 1300533 2200893 73 fe0416e3 415a0a33 fe0a10e3 40f073 ffc10113 12b03
  //   ffc10113 12a83 ffc10113 12a03 ffc10113 12983 ffc10113 12403 ffc10113 12503 ffc10113 12883 200073
  //   RAM写使能MemWrite、RAM写入数据MDin等信号
  //   JAL
  //   JALR
  //   URET
  //   rs1
  //   rs2
  //   rd
  //   imm-i
  //   rd
  //   imm-j
  //   beq/bne
  //   jal
  //   Beq
  //   Bne
  //   MemToReg
  //   MemWrite
  //   AluOP
  //   AluSrcB
  //   RegWrite
  //   S_type
  //   控制位
  //   暂停节拍，不能为0
  //   SignImm
  //   戳工具置1进入计数暂停模式，ctrl+k时钟自动运行到对应节拍暂停
  //   ctrl+k关闭时钟连续运行，将控制位置零，进入单步调试模式调试
  //   可计数暂停的时钟源
  //   数据存储器
endmodule
module \流水线中断  (
  output RegWrite,
  output MemWrite,
  output [31:0] IF_PC,
  output [31:0] ID_PC,
  output [31:0] EX_PC,
  output [31:0] M_PC,
  output [31:0] WB_PC,
  output [31:0] RDin,
  output [31:0] MDin,
  output [31:0] LedData
);

  wire alu_1_equal, alu_1_out_4, alu_1_out_6, and_2_out, and_3_out, and_4_out, and_8_out, and_10_out,
       and_11_out, and_12_out, and_14_out, and_16_out, and_17_out, and_18_out, and_19_out, and_20_out,
       and_21_out, and_22_out, BGE, BranchTaken, BranchTaken_before_1, BranchTaken_before_2, clear1, clear2,
       clear3, CLK, clock_1_out, comparator_1_eq, comparator_1_lt, comparator_2_eq, comparator_3_eq,
       comparator_4_eq, d_ff_1_q, d_ff_2_q, d_ff_3_q, d_ff_4_q, decoder_1_out1, decoder_1_out2,
       decoder_1_out3, ecall, EX_ecall, EX_halt, ex_mem_1_alu_2, ex_mem_1_halt_2, ex_mem_1_jal_2,
       ex_mem_1_jalr_2, ex_mem_1_memtoreg_2, ex_mem_1_regwrite_2, ex_mem_1_sltiu_2, EX_URET, flush, Go, halt,
       id_ex_1_alusrc_2, id_ex_1_beq_2, id_ex_1_bge_2, id_ex_1_bne_2, id_ex_1_jal_2, id_ex_1_memtoreg_2,
       id_ex_1_menwrite, id_ex_1_regwrite_2, id_ex_1_sh_2, id_ex_1_sltiu_2, ID_URET, IE, IF_URET, INT,
       INTRequest, IR1, IR1_q, IR2, IR2_q, IR3, IR3_q, LoadUse, LoadUse_before_1, MEM_SH, MEM_URET,
       mem_wb_1_halt_2, mem_wb_1_jal_2, mem_wb_1_jalr_2, multiplexer_5_out, multiplexer_10_out,
       multiplexer_14_out, multiplexer_16_out, nand_1_out, not_1_out, not_2_out, not_3_out, not_4_out,
       not_5_out, not_6_out, or_4_out, or_5_out, or_6_out, or_7_out, or_13_out, RST, SH, SLTIU, SRL, W1, W2,
       W3, WB_ALU, WB_SLTIU, WB_URET, \单周期硬布线控制器_1_alu_src , \单周期硬布线控制器_1_beq , \单周期硬布线控制器_1_bne ,
       \单周期硬布线控制器_1_jal , \单周期硬布线控制器_1_jalr , \单周期硬布线控制器_1_memtoreg , \单周期硬布线控制器_1_memwrite ,
       \单周期硬布线控制器_1_regwrite , \单周期硬布线控制器_1_rs1_used , \单周期硬布线控制器_1_rs2_used , \单周期硬布线控制器_1_s_type , \无条件分支 ,
       \条件分支 ;
  wire [1:0] id_ex_1_jalr_2, id_ex_1_rs1_forward_2, id_ex_1_rs2_forward_2, INTnum, mem_wb_1_memtoreg_2,
       register_3_q, \重定向处理逻辑_1_rs1_forward , \重定向处理逻辑_1_rs2_forward ;
  wire [3:0] id_ex_1_alu_op_2, RAM_Sel, \单周期硬布线控制器_1_alu_op ;
  wire [3:1] multiplexer_19_out;
  wire [4:0] ex_mem_1_rd_2, id_ex_1_rd_2, multiplexer_7_out, multiplexer_8_out, WB_rd;
  wire [11:0] multiplexer_9_out;
  wire [12:0] CNT_num;
  wire [15:0] \LoadUse次数 , \总周期数 , \插入气泡数 , \无条件分支数 , \条件分支成功数 ;
  wire [31:0] adder_2_out, adder_3_out, Alu_add, and_1_out, bit_extender_1_out, bit_extender_2_out,
       bit_extender_3_out, Branch_add, EX_IR, ex_mem_1_pc_4_2, EX_R1, EX_R2, id_ex_1_imm1_2, id_ex_1_imm2b_2,
       id_ex_1_imm2j_2, id_ex_1_pc_4_2, id_ex_1_r1_2, id_ex_1_r2_2, ID_IR, if_id_1_pc_4_2, IF_IR, INT_PC,
       MEM_ALUresult, MEM_IR, MEM_R2, mem_wb_1_aluresult_2, mem_wb_1_pc_4_2, mem_wb_1_readdata_2,
       mips_ram_1_p8, multiplexer_2_out, multiplexer_3_out, multiplexer_4_out, multiplexer_13_out,
       multiplexer_21_out, multiplexer_22_out, PC_4, regifile_1_r1, regifile_1_r2, RET_PC, Scene,
       shifter_1_out, shifter_2_out, shifter_3_out, WB_IR;

  Button \u_总复位  (.out(RST));
  Button _1 (.out(IR1));
  Button _2 (.out(IR2));
  Button _3 (.out(IR3));
  // Probe on \总周期数 
  // Probe on \总周期数 
  Button \u_继续运行  (.out(Go));
  LED #(.active("true")) led_1 (.in(W1));
  LED #(.active("true")) led_2 (.in(W2));
  LED #(.active("true")) led_3 (.in(W3));
  Hex_Digit_Display hex_digit_display_1 (.value(LedData[31:28]));  // open: dp
  // Probe on IF_PC[19:0]
  // RiscV_Probe riscv_probe_1: pin names not known; wires that end beside it: IF_IR
  Hex_Digit_Display hex_digit_display_2 (.value(LedData[27:24]));  // open: dp
  Hex_Digit_Display hex_digit_display_3 (.value(LedData[23:20]));  // open: dp
  // Probe on ID_PC[19:0]
  // RiscV_Probe riscv_probe_2: pin names not known; wires that end beside it: ID_IR
  Hex_Digit_Display hex_digit_display_4 (.value(LedData[15:12]));  // open: dp
  Hex_Digit_Display hex_digit_display_5 (.value(LedData[19:16]));  // open: dp
  Hex_Digit_Display hex_digit_display_6 (.value(LedData[11:8]));  // open: dp
  Hex_Digit_Display hex_digit_display_7 (.value(LedData[7:4]));  // open: dp
  // Probe on EX_PC[19:0]
  // RiscV_Probe riscv_probe_3: pin names not known; wires that end beside it: EX_IR
  Hex_Digit_Display hex_digit_display_8 (.value(LedData[3:0]));  // open: dp
  or or_1 (W1, IR1_q, d_ff_1_q);
  or or_2 (W2, IR2_q, d_ff_2_q);
  or or_3 (W3, IR3_q, d_ff_3_q);
  Register #(.width(1), .trigger("rising"), .Select("low")) register_1 (
    .D(BranchTaken), .Q(BranchTaken_before_1), .clk(CLK), .clr(RST));  // open: en
  Register #(.width(1), .trigger("rising"), .Select("low")) register_2 (
    .D(LoadUse), .Q(LoadUse_before_1), .clk(CLK), .clr(RST));  // open: en
  // Probe on \总周期数 
  // Probe on M_PC[19:0]
  // RiscV_Probe riscv_probe_4: pin names not known; wires that end beside it: MEM_IR
  D_Flip_Flop #(.trigger("rising"), .Pre_Clr_Positions("LEGACY"), .NegatePresetClear("false"), .enable("true"), .NewFFLayout("false")) d_ff_1 (
    .clk(IR1), .D(1'b1), .Q(d_ff_1_q), .reset(IR1_q));  // open: Qn, preset, en
  D_Flip_Flop #(.trigger("rising"), .Pre_Clr_Positions("LEGACY"), .NegatePresetClear("false"), .enable("true"), .NewFFLayout("false")) d_ff_2 (
    .clk(IR2), .D(1'b1), .Q(d_ff_2_q), .reset(IR2_q));  // open: Qn, preset, en
  D_Flip_Flop #(.trigger("rising"), .Pre_Clr_Positions("LEGACY"), .NegatePresetClear("false"), .enable("true"), .NewFFLayout("false")) d_ff_3 (
    .clk(IR3), .D(1'b1), .Q(d_ff_3_q), .reset(IR3_q));  // open: Qn, preset, en
  Register #(.width(2), .trigger("rising"), .Select("low")) register_3 (
    .D(INTnum), .en(INT), .Q(register_3_q), .clk(CLK));  // open: clr
  Multiplexer #(.select(3), .width(32), .disabled("Z"), .enable("false")) multiplexer_1 (
    .in0(EX_PC), .in1(IF_PC), .in2(ID_PC), .in4(ID_PC), .out(Scene),
    .sel({LoadUse_before_1, BranchTaken_before_2, BranchTaken_before_1}));  // open: in3, in5, in6, in7
  // Probe on \总周期数 
  // Probe on \无条件分支数 
  // Probe on \条件分支成功数 
  // Probe on \插入气泡数 
  // Probe on \LoadUse次数 
  or or_4 (or_4_out, d_ff_1_q, IR1_q);
  or or_5 (or_5_out, d_ff_2_q, IR2_q);
  or or_6 (or_6_out, d_ff_3_q, IR3_q);
  Decoder #(.select(2), .tristate("false"), .disabled("Z"), .enable("false")) decoder_1 (
    .out1(decoder_1_out1), .out2(decoder_1_out2), .out3(decoder_1_out3), .sel(register_3_q));  // open: out0
  // Probe on IF_PC[11:0]
  // Probe on WB_PC[19:0]
  // RiscV_Probe riscv_probe_5: pin names not known; wires that end beside it: WB_IR
  assign and_1_out = Alu_add & 32'hfffffffe;  // AND_Gate and_1, 32 bits wide
  and and_2 (and_2_out, or_4_out, ~clear1);  // AND_Gate
  and and_3 (and_3_out, or_5_out, ~clear2);  // AND_Gate
  and and_4 (and_4_out, or_6_out, ~clear3);  // AND_Gate
  and and_5 (clear1, decoder_1_out1, IF_URET);
  and and_6 (clear2, decoder_1_out2, IF_URET);
  and and_7 (clear3, decoder_1_out3, IF_URET);
  Register #(.width(1), .trigger("rising"), .Select("low")) register_4 (
    .D(BranchTaken_before_1), .Q(BranchTaken_before_2), .clk(CLK), .clr(RST));  // open: en
  // Probe on EX_PC[11:0]
  // Probe on ID_PC[11:0]
  \重定向处理逻辑  \u_重定向处理逻辑_1  (
    .IR(ID_IR), .BranchTaken(BranchTaken), .EX_MemToReg(id_ex_1_memtoreg_2), .ecall(ecall),
    .rs1_used(\单周期硬布线控制器_1_rs1_used ), .EX_RegWrite(id_ex_1_regwrite_2), .rs2_used(\单周期硬布线控制器_1_rs2_used ),
    .MEM_RegWrite(ex_mem_1_regwrite_2), .EX_rd(id_ex_1_rd_2), .MEM_rd(ex_mem_1_rd_2), .stall(LoadUse),
    .flush(flush), .rs1_Forward(\重定向处理逻辑_1_rs1_forward ), .rs2_Forward(\重定向处理逻辑_1_rs2_forward ));
  not not_1 (not_1_out, LoadUse);
  and and_8 (and_8_out, not_1_out, not_2_out);
  not not_2 (not_2_out, halt);
  D_Flip_Flop #(.trigger("rising"), .Pre_Clr_Positions("LEGACY"), .NegatePresetClear("false"), .enable("true"), .NewFFLayout("false")) u_IR1 (
    .clk(CLK), .D(and_2_out), .Q(IR1_q));  // open: Qn, preset, en, reset
  D_Flip_Flop #(.trigger("rising"), .Pre_Clr_Positions("LEGACY"), .NegatePresetClear("false"), .enable("true"), .NewFFLayout("false")) u_IR2 (
    .clk(CLK), .D(and_3_out), .Q(IR2_q));  // open: Qn, preset, en, reset
  D_Flip_Flop #(.trigger("rising"), .Pre_Clr_Positions("LEGACY"), .NegatePresetClear("false"), .enable("true"), .NewFFLayout("false")) u_IR3 (
    .clk(CLK), .D(and_4_out), .Q(IR3_q));  // open: Qn, preset, en, reset
  // Probe on M_PC[11:0]
  D_Flip_Flop #(.trigger("high"), .Pre_Clr_Positions("LEGACY"), .NegatePresetClear("false"), .enable("true"), .NewFFLayout("false")) d_ff_4 (.Q(d_ff_4_q));  // open: clk, D, Qn, preset, en, reset
  // Probe on 13'h27b
  Multiplexer #(.select(2), .width(32), .disabled("Z"), .enable("false")) multiplexer_2 (
    .in0(PC_4), .in1(and_1_out), .in2(Branch_add), .out(multiplexer_2_out), .sel(id_ex_1_jalr_2));  // open: in3
  // Probe on WB_PC[11:0]
  Comparator #(.width(13), .mode("twosComplement")) comparator_1 (
    .a(CNT_num), .b(13'h27b), .eq(comparator_1_eq), .lt(comparator_1_lt));  // open: gt
  Clock #(.highDuration(1), .lowDuration(1)) clock_1 (.out(clock_1_out));
  Multiplexer #(.select(1), .width(32), .disabled("Z"), .enable("false")) multiplexer_3 (
    .in0(multiplexer_2_out), .in1(RET_PC), .out(multiplexer_3_out), .sel(IF_URET));
  nand nand_1 (nand_1_out, d_ff_4_q, comparator_1_eq);
  Counter #(.width(13), .max('h1fff), .ongoal("stay"), .trigger("rising"), .behavior("old")) counter_1 (
    .count(comparator_1_lt), .Q(CNT_num), .clk(clock_1_out));  // open: load, D, carry, clr, preset
  Multiplexer #(.select(1), .width(32), .disabled("Z"), .enable("false")) multiplexer_4 (
    .in0(multiplexer_3_out), .in1(INT_PC), .out(multiplexer_4_out), .sel(INT));
  Register #(.width(32), .trigger("rising"), .Select("low")) PC (
    .D(multiplexer_4_out), .en(and_8_out), .Q(IF_PC), .clk(CLK), .clr(RST));
  Priority_Encoder #(.select(2), .disabled("Z")) priority_encoder_1 (
    .in1(IR1_q), .in2(IR2_q), .in3(IR3_q), .out(INTnum), .gs(INTRequest));  // open: in0, en_out, en_in
  assign CLK = nand_1_out ? clock_1_out : 1'bz;  // Controlled_Buffer controlled_buffer_1
  Adder #(.width(32)) adder_1 (.a(IF_PC), .b(32'h4), .out(PC_4), .cin(1'b0));  // open: cout
  Pull_Resistor #(.pull(1)) pull_resistor_1 (.node(CLK));
  Comparator #(.width(12), .mode("twosComplement")) comparator_2 (
    .a(IF_IR[31:20]), .b(12'h2), .eq(comparator_2_eq));  // open: gt, lt
  Comparator #(.width(5), .mode("twosComplement")) comparator_3 (
    .a(IF_IR[6:2]), .b(5'b11100), .eq(comparator_3_eq));  // open: gt, lt
  and and_9 (IF_URET, comparator_2_eq, comparator_3_eq);
  not not_3 (not_3_out, halt);
  // RiscV_Probe riscv_probe_6: pin names not known; wires that end beside it: IF_IR, PC_4
  ROM #(.addrWidth(10), .dataWidth(32), .Select("high")) rom_1 (.addr(IF_PC[11:2]), .data(IF_IR));
  Counter #(.width(16), .max('hffff), .ongoal("wrap"), .trigger("rising"), .behavior("new")) counter_2 (
    .count(not_3_out), .Q(\总周期数 ), .clk(CLK));  // open: load, D, carry, clr, preset, down
  and and_10 (and_10_out, ~LoadUse, ~halt);  // AND_Gate
  Multiplexer #(.select(1), .width(1), .disabled("Z"), .enable("false")) multiplexer_5 (
    .in0(and_11_out), .in1(1'b0), .out(multiplexer_5_out), .sel(CLK));
  and and_11 (and_11_out, \无条件分支 , CLK);
  or or_7 (or_7_out, id_ex_1_jalr_2[1], id_ex_1_jalr_2[0]);
  IF_ID if_id_1 (
    .IR(IF_IR), .PC(IF_PC), .PC_4(PC_4), .IR_2(ID_IR), .PC_2(ID_PC), .PC_4_2(if_id_1_pc_4_2), .reset(RST),
    .BranchTaken(or_7_out), .en(and_10_out), .clk(CLK));  // open: PredictJump, PredictJump_2
  Counter #(.width(16), .max('hffff), .ongoal("wrap"), .trigger("rising"), .behavior("old")) counter_3 (
    .count(1'b1), .Q(\无条件分支数 ), .clk(multiplexer_5_out), .clr(RST));  // open: load, D, carry, preset
  and and_12 (and_12_out, INTRequest, ~EX_URET);  // AND_Gate
  Multiplexer #(.select(2), .width(32), .disabled("Z"), .enable("false")) multiplexer_6 (
    .in1(32'h30ac), .in2(32'h3150), .in3(32'h31f4), .out(INT_PC), .sel(INTnum));  // open: in0
  \单周期硬布线控制器  \u_单周期硬布线控制器_1  (
    .Funct({ID_IR[30], ID_IR[25], ID_IR[14:12]}), .OP(ID_IR[6:2]), .ALU_OP(\单周期硬布线控制器_1_alu_op ),
    .MemToReg(\单周期硬布线控制器_1_memtoreg ), .MemWrite(\单周期硬布线控制器_1_memwrite ), .ALU_SRC(\单周期硬布线控制器_1_alu_src ),
    .RegWrite(\单周期硬布线控制器_1_regwrite ), .ecall(ecall), .S_type(\单周期硬布线控制器_1_s_type ),
    .Jalr(\单周期硬布线控制器_1_jalr ), .Beq(\单周期硬布线控制器_1_beq ), .JAL(\单周期硬布线控制器_1_jal ), .Bne(\单周期硬布线控制器_1_bne ),
    .in_3(ID_IR[21]), .uret(ID_URET), .SRL(SRL), .SLTIU(SLTIU), .SH(SH), .BGE(BGE),
    .rs1_used(\单周期硬布线控制器_1_rs1_used ), .rs2_used(\单周期硬布线控制器_1_rs2_used ));  // open: CSRRSI, CSRRCI
  D_Flip_Flop #(.trigger("rising"), .Pre_Clr_Positions("LEGACY"), .NegatePresetClear("false"), .enable("true"), .NewFFLayout("false")) d_ff_5 (
    .clk(CLK), .D(and_12_out), .Q(IE));  // open: Qn, preset, en, reset
  and and_13 (INT, INTRequest, ~IE);  // AND_Gate
  Register #(.width(32), .trigger("rising"), .Select("low")) register_5 (
    .D(Scene), .en(INT), .Q(RET_PC), .clk(CLK), .clr(RST));
  Multiplexer #(.select(1), .width(5), .disabled("Z"), .enable("false")) multiplexer_7 (
    .in0(ID_IR[19:15]), .in1(5'b10001), .out(multiplexer_7_out), .sel(ecall));
  Multiplexer #(.select(1), .width(5), .disabled("Z"), .enable("false")) multiplexer_8 (
    .in0(ID_IR[24:20]), .in1(5'b01010), .out(multiplexer_8_out), .sel(ecall));
  assign bit_extender_1_out = {{20{ID_IR[31]}}, {ID_IR[31], ID_IR[7], ID_IR[30:25], ID_IR[11:8]}};  // Bit_Extender bit_extender_1
  assign bit_extender_2_out = {{12{ID_IR[31]}}, {ID_IR[31], ID_IR[19:12], ID_IR[20], ID_IR[30:21]}};  // Bit_Extender bit_extender_2
  Multiplexer #(.select(1), .width(12), .disabled("Z"), .enable("false")) multiplexer_9 (
    .in0(ID_IR[31:20]), .in1({ID_IR[31:25], ID_IR[11:7]}), .out(multiplexer_9_out), .sel(\单周期硬布线控制器_1_s_type ));
  and and_14 (and_14_out, \条件分支 , CLK);
  assign bit_extender_3_out = {{20{multiplexer_9_out[11]}}, multiplexer_9_out};  // Bit_Extender bit_extender_3
  Counter #(.width(16), .max('hffff), .ongoal("wrap"), .trigger("rising"), .behavior("old")) counter_4 (
    .count(1'b1), .Q(\条件分支成功数 ), .clk(multiplexer_10_out), .clr(RST));  // open: load, D, carry, preset
  Multiplexer #(.select(1), .width(1), .disabled("Z"), .enable("false")) multiplexer_10 (
    .in0(and_14_out), .in1(1'b0), .out(multiplexer_10_out), .sel(CLK));
  not not_4 (not_4_out, CLK);
  Regifile regifile_1 (
    .Din(RDin), .Clk(not_4_out), .R1(regifile_1_r1), .R2(regifile_1_r2), .WE(RegWrite), .W_num(WB_rd),
    .R1_num(multiplexer_7_out), .R2_num(multiplexer_8_out));
  ID_EX id_ex_1 (
    .Beq(\单周期硬布线控制器_1_beq ), .Bne(\单周期硬布线控制器_1_bne ), .MemToReg(\单周期硬布线控制器_1_memtoreg ),
    .MemWrite(\单周期硬布线控制器_1_memwrite ), .AluSrc(\单周期硬布线控制器_1_alu_src ), .RegWrite(\单周期硬布线控制器_1_regwrite ),
    .SType(\单周期硬布线控制器_1_s_type ), .ecall(ecall), .Jal(\单周期硬布线控制器_1_jal ), .Jalr(\单周期硬布线控制器_1_jalr ),
    .SLTIU(SLTIU), .SH(SH), .BGE(BGE), .ALU_OP(\单周期硬布线控制器_1_alu_op ), .rd(ID_IR[11:7]), .R1(regifile_1_r1),
    .R2(regifile_1_r2), .imm1(bit_extender_3_out), .IR(ID_IR), .PC(ID_PC), .PC_4(if_id_1_pc_4_2),
    .RS1_Forward(\重定向处理逻辑_1_rs1_forward ), .RS2_Forward(\重定向处理逻辑_1_rs2_forward ), .Beq_2(id_ex_1_beq_2),
    .Bne_2(id_ex_1_bne_2), .MemToReg_2(id_ex_1_memtoreg_2), .MenWrite(id_ex_1_menwrite),
    .AluSrc_2(id_ex_1_alusrc_2), .RegWrite_2(id_ex_1_regwrite_2), .ecall_2(EX_ecall), .Jal_2(id_ex_1_jal_2),
    .Jalr_2(id_ex_1_jalr_2[0]), .SLTIU_2(id_ex_1_sltiu_2), .SH_2(id_ex_1_sh_2), .BGE_2(id_ex_1_bge_2),
    .ALU_OP_2(id_ex_1_alu_op_2), .rd_2(id_ex_1_rd_2), .R1_2(id_ex_1_r1_2), .R2_2(id_ex_1_r2_2),
    .imm1_2(id_ex_1_imm1_2), .IR_2(EX_IR), .PC_2(EX_PC), .PC_4_2(id_ex_1_pc_4_2),
    .RS1_Forward_2(id_ex_1_rs1_forward_2), .RS2_Forward_2(id_ex_1_rs2_forward_2), .Reset(RST), .Flush(flush),
    .en(not_5_out), .clk(CLK), .URET(ID_URET), .URET_2(EX_URET), .imm2j(bit_extender_2_out),
    .imm2j_2(id_ex_1_imm2j_2), .imm2b(bit_extender_1_out), .imm2b_2(id_ex_1_imm2b_2));  // open: SType_2, PredictJump, PredictJump_2
  not not_5 (not_5_out, halt);
  or or_8 (\无条件分支 , id_ex_1_jalr_2[0], id_ex_1_jal_2);
  Shifter #(.width(32), .shift("ll")) shifter_1 (.in(id_ex_1_imm2b_2), .\dist (5'b00001), .out(shifter_1_out));
  Shifter #(.width(32), .shift("ll")) shifter_2 (.in(id_ex_1_imm2j_2), .\dist (5'b00001), .out(shifter_2_out));
  Multiplexer #(.select(2), .width(32), .disabled("Z"), .enable("false")) multiplexer_11 (
    .in0(id_ex_1_r1_2), .in1(RDin), .in2(MEM_ALUresult), .out(EX_R1), .sel(id_ex_1_rs1_forward_2));  // open: in3
  Multiplexer #(.select(2), .width(32), .disabled("Z"), .enable("false")) multiplexer_12 (
    .in0(id_ex_1_r2_2), .in1(RDin), .in2(MEM_ALUresult), .out(EX_R2), .sel(id_ex_1_rs2_forward_2));  // open: in3
  Comparator #(.width(32), .mode("twosComplement")) comparator_4 (
    .a(EX_R1), .b(32'h22), .eq(comparator_4_eq));  // open: gt, lt
  or or_9 (BranchTaken, id_ex_1_jalr_2[0], id_ex_1_jalr_2[1]);
  Multiplexer #(.select(1), .width(32), .disabled("Z"), .enable("false")) multiplexer_13 (
    .in0(EX_R2), .in1(id_ex_1_imm1_2), .out(multiplexer_13_out), .sel(id_ex_1_alusrc_2));
  Adder #(.width(32)) adder_2 (.a(shifter_1_out), .b(EX_PC), .out(adder_2_out));  // open: cin, cout
  Adder #(.width(32)) adder_3 (.a(shifter_2_out), .b(EX_PC), .out(adder_3_out));  // open: cin, cout
  and and_15 (EX_halt, EX_ecall, not_6_out);
  not not_6 (not_6_out, comparator_4_eq);
  Register #(.width(32), .trigger("rising"), .Select("low")) PC_2 (
    .D(EX_R2), .en(and_16_out), .Q(LedData), .clk(CLK));  // open: clr
  and and_16 (and_16_out, comparator_4_eq, EX_ecall);
  Counter #(.width(16), .max('hffff), .ongoal("wrap"), .trigger("rising"), .behavior("old")) counter_5 (
    .count(1'b1), .Q(\插入气泡数 ), .clk(multiplexer_14_out), .clr(RST));  // open: load, D, carry, preset
  Multiplexer #(.select(1), .width(1), .disabled("Z"), .enable("false")) multiplexer_14 (
    .in0(and_17_out), .in1(1'b0), .out(multiplexer_14_out), .sel(CLK));
  and and_17 (and_17_out, and_18_out, CLK);
  and and_18 (and_18_out, ~halt, flush);  // AND_Gate
  or or_10 (\条件分支 , and_19_out, and_20_out, and_21_out);
  or or_11 (id_ex_1_jalr_2[1], id_ex_1_jal_2, and_19_out, and_20_out, and_21_out);
  and and_19 (and_19_out, id_ex_1_beq_2, alu_1_equal);
  and and_20 (and_20_out, ~alu_1_equal, id_ex_1_bne_2);  // AND_Gate
  ALU alu_1 (
    .X(EX_R1), .Y(multiplexer_13_out), .AluOP(id_ex_1_alu_op_2), .Equal(alu_1_equal), .Result(Alu_add),
    .out_4(alu_1_out_4), .out_6(alu_1_out_6));  // open: Result_2
  Multiplexer #(.select(1), .width(32), .disabled("Z"), .enable("false")) multiplexer_15 (
    .in0(adder_2_out), .in1(adder_3_out), .out(Branch_add), .sel(id_ex_1_jal_2));
  and and_21 (and_21_out, id_ex_1_bge_2, alu_1_out_4);
  EX_MEM ex_mem_1 (
    .Jal(id_ex_1_jal_2), .Jalr(id_ex_1_jalr_2[0]), .MemToReg(id_ex_1_memtoreg_2),
    .MemWrite(id_ex_1_menwrite), .RegWrite(id_ex_1_regwrite_2), .Halt(EX_halt), .URET(EX_URET),
    .SLTIU(id_ex_1_sltiu_2), .SH(id_ex_1_sh_2), .ALU(alu_1_out_6), .rd(id_ex_1_rd_2), .result(Alu_add),
    .WriteData(EX_R2), .IR(EX_IR), .PC(EX_PC), .PC_4(id_ex_1_pc_4_2), .Jal_2(ex_mem_1_jal_2),
    .Jalr_2(ex_mem_1_jalr_2), .MemToReg_2(ex_mem_1_memtoreg_2), .MemWrite_2(MemWrite),
    .RegWrite_2(ex_mem_1_regwrite_2), .Halt_2(ex_mem_1_halt_2), .URET_2(MEM_URET),
    .SLTIU_2(ex_mem_1_sltiu_2), .SH_2(MEM_SH), .ALU_2(ex_mem_1_alu_2), .rd_2(ex_mem_1_rd_2),
    .result_2(MEM_ALUresult), .Writedata_2(MEM_R2), .IR_2(MEM_IR), .PC_2(M_PC), .PC_4_2(ex_mem_1_pc_4_2),
    .reset(RST), .en(not_5_out), .clk(CLK));
  and and_22 (and_22_out, LoadUse, CLK);
  Counter #(.width(16), .max('hffff), .ongoal("wrap"), .trigger("rising"), .behavior("old")) counter_6 (
    .count(1'b1), .Q(\LoadUse次数 ), .clk(multiplexer_16_out), .clr(RST));  // open: load, D, carry, preset
  Multiplexer #(.select(1), .width(1), .disabled("Z"), .enable("false")) multiplexer_16 (
    .in0(and_22_out), .in1(1'b0), .out(multiplexer_16_out), .sel(CLK));
  Multiplexer #(.select(1), .width(32), .disabled("Z"), .enable("false")) multiplexer_17 (
    .in0(MEM_R2), .in1(shifter_3_out), .out(MDin), .sel(MEM_ALUresult[1]));
  Shifter #(.width(32), .shift("ll")) shifter_3 (.in(MEM_R2), .\dist (5'b10000), .out(shifter_3_out));
  // MIPS_RAM mips_ram_1: pin names not known; wires that end beside it: MEM_ALUresult[11:2], MDin, MemWrite, RAM_Sel, CLK, 1'b1, RST, mips_ram_1_p8
  Multiplexer #(.select(1), .width(4), .disabled("Z"), .enable("false")) multiplexer_18 (
    .in0(4'b1111), .in1({{2{multiplexer_19_out[3]}}, {2{multiplexer_19_out[1]}}}), .out(RAM_Sel), .sel(MEM_SH));
  Multiplexer #(.select(1), .width(1), .disabled("Z"), .enable("false")) multiplexer_19 (
    .in0(1'b1), .in1(1'b0), .out(multiplexer_19_out[1]), .sel(MEM_ALUresult[1]));
  MEM_WB mem_wb_1 (
    .Jal(ex_mem_1_jal_2), .Jalr(ex_mem_1_jalr_2), .MemToReg(ex_mem_1_memtoreg_2),
    .RegWrite(ex_mem_1_regwrite_2), .Halt(ex_mem_1_halt_2), .rd(ex_mem_1_rd_2), .AluResult(MEM_ALUresult),
    .ReadData(mips_ram_1_p8), .IR(MEM_IR), .PC(M_PC), .PC_4(ex_mem_1_pc_4_2), .Jal_2(mem_wb_1_jal_2),
    .Jalr_2(mem_wb_1_jalr_2), .MemToReg_2(mem_wb_1_memtoreg_2[0]), .RegWrite_2(RegWrite),
    .Halt_2(mem_wb_1_halt_2), .rd_2(WB_rd), .AluResult_2(mem_wb_1_aluresult_2),
    .Readdata_2(mem_wb_1_readdata_2), .IR_2(WB_IR), .PC_2(WB_PC), .PC_4_2(mem_wb_1_pc_4_2), .reset(RST),
    .en(not_5_out), .clk(CLK), .URET(MEM_URET), .URET_2(WB_URET), .SLTIU(ex_mem_1_sltiu_2),
    .SLTIU_2(WB_SLTIU), .ALU(ex_mem_1_alu_2), .ALU_2(WB_ALU));  // open: SH, SH_2
  Multiplexer #(.select(1), .width(1), .disabled("Z"), .enable("false")) multiplexer_20 (
    .in0(1'b0), .in1(1'b1), .out(multiplexer_19_out[3]), .sel(MEM_ALUresult[1]));
  or or_12 (mem_wb_1_memtoreg_2[1], mem_wb_1_jal_2, mem_wb_1_jalr_2);
  Multiplexer #(.select(2), .width(32), .disabled("Z"), .enable("false")) multiplexer_21 (
    .in0(mem_wb_1_aluresult_2), .in1(mem_wb_1_readdata_2), .in2(mem_wb_1_pc_4_2), .out(multiplexer_21_out),
    .sel(mem_wb_1_memtoreg_2));  // open: in3
  or or_13 (or_13_out, mem_wb_1_halt_2, halt);
  Multiplexer #(.select(1), .width(32), .disabled("Z"), .enable("false")) multiplexer_22 (
    .in0({32{1'b0}}), .in1(32'h1), .out(multiplexer_22_out), .sel(WB_ALU));
  D_Flip_Flop #(.trigger("falling"), .Pre_Clr_Positions("ABOVE_BELOW"), .NegatePresetClear("false"), .enable("false"), .NewFFLayout("true")) d_ff_6 (
    .clk(CLK), .D(or_13_out), .Q(halt), .reset(Go));  // open: Qn, preset
  Multiplexer #(.select(1), .width(32), .disabled("Z"), .enable("false")) multiplexer_23 (
    .in0(multiplexer_21_out), .in1(multiplexer_22_out), .out(RDin), .sel(WB_SLTIU));

  // Other names for the same wires on the sheet: MEM_PC[31:0] = M_PC; stall = LoadUse; WB_RegWrite = RegWrite

  // Notes on the sheet:
  //   中断源
  //   时空图监测，可删除
  //   中断等待指示
  //   数码管输出
  //   Reset 
  //   Reset 
  //   Reset 
  //   控制位
  //   流水调试日志用
  //   暂停节拍，不能为0
  //   戳工具置1进入计数暂停模式，ctrl+k时钟自动运行到对应节拍暂停
  //   ctrl+k关闭时钟连续运行，将控制位置零，进入单步调试模式调试
  //   可计数暂停的时钟源
  //   指令存储器
  //   指令探针
  //   contents of rom_1 (hex, n*v repeats v):
  //   7d000113 100413 1f41993 41f9d993 433 c00913 800b13 140413 f47413 800293 100313 499993 89e9b3 1300533
  //   2200893 73 406282b3 fe0294e3 140413 f00f93 1f47433 1c41413 800293 100313 49d993 89e9b3 1300533
  //   2200893 73 406282b3 fe0294e3 1c45413 406b0b33 b0463 f95ff06f 2b3 fff2c293 1029293 fff2e293 500533
  //   2200893 73 f5dff06f 1112023 410113 a12023 410113 812023 410113 1312023 410113 1412023 410113 1512023
  //   410113 1612023 410113 100b13 300a13 100a93 1600433 441413 14469b3 1300533 2200893 73 fe0416e3
  //   415a0a33 fe0a10e3 ffc10113 12b03 ffc10113 12a83 ffc10113 12a03 ffc10113 12983 ffc10113 12403
  //   ffc10113 12503 ffc10113 12883 200073 1112023 410113 a12023 410113 812023 410113 1312023 410113
  //   1412023 410113 1512023 410113 1612023 410113 200b13 300a13 100a93 1600433 441413 14469b3 1300533
  //   2200893 73 fe0416e3 415a0a33 fe0a10e3 ffc10113 12b03 ffc10113 12a83 ffc10113 12a03 ffc10113 12983
  //   ffc10113 12403 ffc10113 12503 ffc10113 12883 200073 1112023 410113 a12023 410113 812023 410113
  //   1312023 410113 1412023 410113 1512023 410113 1612023 410113 300b13 300a13 100a93 1600433 441413
  //   14469b3 1300533 2200893 73 fe0416e3 415a0a33 fe0a10e3 ffc10113 12b03 ffc10113 12a83 ffc10113 12a03
  //   ffc10113 12983 ffc10113 12403 ffc10113 12503 ffc10113 12883 200073
  //   为方便自动评测，需要输出流水线各段保存的PC值，注意是PC不是PC+4，另外ID段寄存器写入信息，Mem段内存写入信息也要输出
  //   rs1
  //   rs2
  //   imm-i
  //   rd
  //   JAL
  //   JALR
  //   URET
  //   imm-j
  //   beq/bne
  //   jal
  //   rd
  //   Beq
  //   Bne
  //   MemToReg
  //   MemWrite
  //   AluOP
  //   AluSrcB
  //   RegWrite
  //   S_type
  //   Beq
  //   Jal
  //   Jalr
  //   Bne
  //   数据存储器
endmodule

module \分支预测  (
  output RegWrite,
  output MemWrite,
  output [31:0] IF_PC,
  output [31:0] ID_PC,
  output [31:0] EX_PC,
  output [31:0] M_PC,
  output [31:0] WB_PC,
  output [31:0] RDin,
  output [31:0] MDin,
  output [31:0] LedData
);

  wire alu_1_equal, alu_1_out_4, alu_1_out_6, and_2_out, and_4_out, and_5_out, and_6_out, and_7_out,
       and_8_out, and_10_out, and_11_out, and_12_out, and_13_out, and_14_out, BGE, BranchTaken, CLK,
       clock_1_out, comparator_1_eq, comparator_1_lt, comparator_2_eq, comparator_3_eq, d_ff_1_q, ecall,
       EX_Beq, EX_BGE, EX_Bne, EX_ecall, EX_halt, EX_JAL, EX_JALR, ex_mem_1_alu_2, ex_mem_1_halt_2,
       ex_mem_1_jal_2, ex_mem_1_jalr_2, ex_mem_1_memtoreg_2, ex_mem_1_regwrite_2, ex_mem_1_sltiu_2,
       EX_PredictJump, flush, Go, halt, id_ex_1_alusrc_2, id_ex_1_memtoreg_2, id_ex_1_menwrite,
       id_ex_1_regwrite_2, id_ex_1_sh_2, id_ex_1_sltiu_2, ID_PredictJump, IF_PredictJump, IR1, IR2, IR3,
       MEM_SH, mem_wb_1_halt_2, mem_wb_1_jal_2, mem_wb_1_jalr_2, multiplexer_4_out, multiplexer_9_out,
       multiplexer_14_out, multiplexer_15_out, nand_1_out, not_1_out, not_2_out, not_3_out, not_5_out,
       not_6_out, not_7_out, or_2_out, or_9_out, PredictError, RST, SH, SLTIU, SRL, stall, W1, W2, W3,
       WB_ALU, WB_SLTIU, \单周期硬布线控制器_1_alu_src , \单周期硬布线控制器_1_beq , \单周期硬布线控制器_1_bne , \单周期硬布线控制器_1_jal ,
       \单周期硬布线控制器_1_jalr , \单周期硬布线控制器_1_memtoreg , \单周期硬布线控制器_1_memwrite , \单周期硬布线控制器_1_regwrite ,
       \单周期硬布线控制器_1_rs1_used , \单周期硬布线控制器_1_rs2_used , \单周期硬布线控制器_1_s_type , \单周期硬布线控制器_1_uret , \无条件分支 ,
       \条件分支 ;
  wire [1:0] id_ex_1_rs1_forward_2, id_ex_1_rs2_forward_2, mem_wb_1_memtoreg_2, \重定向处理逻辑_1_rs1_forward ,
       \重定向处理逻辑_1_rs2_forward ;
  wire [1:1] or_1_out, or_6_out;
  wire [3:0] id_ex_1_alu_op_2, RAM_Sel, \单周期硬布线控制器_1_alu_op ;
  wire [3:1] multiplexer_18_out;
  wire [4:0] ex_mem_1_rd_2, id_ex_1_rd_2, multiplexer_6_out, multiplexer_7_out, WB_rd;
  wire [11:0] multiplexer_8_out;
  wire [12:0] CNT_num;
  wire [15:0] \LoadUse次数 , \总周期数 , \插入气泡数 , \无条件分支数 , \条件分支成功数 ;
  wire [31:0] adder_2_out, adder_3_out, Alu_add, and_1_out, and_3_out, bit_extender_1_out,
       bit_extender_2_out, bit_extender_3_out, Branch_add, btb_1_btb_jumpaddr, EX_IR, ex_mem_1_pc_4_2,
       EX_PC_4, EX_R1, EX_R2, id_ex_1_imm1_2, id_ex_1_imm2b_2, id_ex_1_imm2j_2, id_ex_1_r1_2, id_ex_1_r2_2,
       ID_IR, if_id_1_pc_4_2, IF_IR, IF_PC_4, MEM_ALUresult, MEM_IR, MEM_R2, mem_wb_1_aluresult_2,
       mem_wb_1_pc_4_2, mem_wb_1_readdata_2, mips_ram_1_p8, multiplexer_1_out, multiplexer_2_out,
       multiplexer_3_out, multiplexer_12_out, multiplexer_20_out, multiplexer_22_out, PredictAdd,
       regifile_1_r1, regifile_1_r2, shifter_1_out, shifter_2_out, shifter_3_out, WB_IR;

  Button \u_总复位  (.out(RST));
  Button _1 (.out(IR1));
  Button _2 (.out(IR2));
  Button _3 (.out(IR3));
  // Probe on \总周期数 
  // Probe on \总周期数 
  Button \u_继续运行  (.out(Go));
  LED #(.active("true")) led_1 (.in(W1));
  LED #(.active("true")) led_2 (.in(W2));
  LED #(.active("true")) led_3 (.in(W3));
  Hex_Digit_Display hex_digit_display_1 (.value(LedData[31:28]));  // open: dp
  // Probe on IF_PC[19:0]
  // RiscV_Probe riscv_probe_1: pin names not known; wires that end beside it: IF_IR
  Hex_Digit_Display hex_digit_display_2 (.value(LedData[23:20]));  // open: dp
  Hex_Digit_Display hex_digit_display_3 (.value(LedData[27:24]));  // open: dp
  // Probe on ID_PC[19:0]
  // RiscV_Probe riscv_probe_2: pin names not known; wires that end beside it: ID_IR
  Hex_Digit_Display hex_digit_display_4 (.value(LedData[19:16]));  // open: dp
  Hex_Digit_Display hex_digit_display_5 (.value(LedData[15:12]));  // open: dp
  Hex_Digit_Display hex_digit_display_6 (.value(LedData[11:8]));  // open: dp
  Hex_Digit_Display hex_digit_display_7 (.value(LedData[7:4]));  // open: dp
  // Probe on EX_PC[19:0]
  // RiscV_Probe riscv_probe_3: pin names not known; wires that end beside it: EX_IR
  Hex_Digit_Display hex_digit_display_8 (.value(LedData[3:0]));  // open: dp
  // Probe on \总周期数 
  // Probe on M_PC[19:0]
  // RiscV_Probe riscv_probe_4: pin names not known; wires that end beside it: MEM_IR
  // Probe on \总周期数 
  // Probe on \无条件分支数 
  // Probe on \条件分支成功数 
  // Probe on \插入气泡数 
  // Probe on \LoadUse次数 
  \重定向处理逻辑  \u_重定向处理逻辑_1  (
    .IR(ID_IR), .BranchTaken(BranchTaken), .EX_MemToReg(id_ex_1_memtoreg_2), .ecall(ecall),
    .rs1_used(\单周期硬布线控制器_1_rs1_used ), .EX_RegWrite(id_ex_1_regwrite_2), .rs2_used(\单周期硬布线控制器_1_rs2_used ),
    .MEM_RegWrite(ex_mem_1_regwrite_2), .EX_rd(id_ex_1_rd_2), .MEM_rd(ex_mem_1_rd_2), .stall(stall),
    .rs1_Forward(\重定向处理逻辑_1_rs1_forward ), .rs2_Forward(\重定向处理逻辑_1_rs2_forward ));  // open: flush
  assign and_1_out = Alu_add & 32'hfffffffe;  // AND_Gate and_1, 32 bits wide
  not not_1 (not_1_out, stall);
  not not_2 (not_2_out, halt);
  // Probe on IF_PC[11:0]
  // Probe on WB_PC[19:0]
  // RiscV_Probe riscv_probe_5: pin names not known; wires that end beside it: WB_IR
  Multiplexer #(.select(2), .width(32), .disabled("Z"), .enable("false")) multiplexer_1 (
    .in0(EX_PC_4), .in1(and_1_out), .in2(Branch_add), .out(multiplexer_1_out), .sel({or_6_out[1], EX_JALR}));  // open: in3
  and and_2 (and_2_out, not_1_out, not_2_out);
  // Probe on ID_PC[11:0]
  // Probe on EX_PC[11:0]
  Multiplexer #(.select(1), .width(32), .disabled("Z"), .enable("false")) multiplexer_2 (
    .in0(PredictAdd), .in1(multiplexer_1_out), .out(multiplexer_2_out), .sel(PredictError));
  // Probe on M_PC[11:0]
  D_Flip_Flop #(.trigger("high"), .Pre_Clr_Positions("LEGACY"), .NegatePresetClear("false"), .enable("true"), .NewFFLayout("false")) d_ff_1 (.Q(d_ff_1_q));  // open: clk, D, Qn, preset, en, reset
  // Probe on 13'hdc
  Register #(.width(32), .trigger("rising"), .Select("low")) PC (
    .D(multiplexer_2_out), .en(and_2_out), .Q(IF_PC), .clk(CLK), .clr(RST));
  // Probe on WB_PC[11:0]
  Comparator #(.width(13), .mode("twosComplement")) comparator_1 (
    .a(CNT_num), .b(13'hdc), .eq(comparator_1_eq), .lt(comparator_1_lt));  // open: gt
  Clock #(.highDuration(1), .lowDuration(1)) clock_1 (.out(clock_1_out));
  Adder #(.width(32)) adder_1 (.a(IF_PC), .b(32'h4), .out(IF_PC_4), .cin(1'b0));  // open: cout
  assign and_3_out = Alu_add & 32'hfffffffe;  // AND_Gate and_3, 32 bits wide
  or or_1 (or_1_out[1], EX_BGE, EX_Beq, EX_Bne, EX_JAL);
  nand nand_1 (nand_1_out, d_ff_1_q, comparator_1_eq);
  Counter #(.width(13), .max('h1fff), .ongoal("stay"), .trigger("rising"), .behavior("old")) counter_1 (
    .count(comparator_1_lt), .Q(CNT_num), .clk(clock_1_out));  // open: load, D, carry, clr, preset
  assign CLK = nand_1_out ? clock_1_out : 1'bz;  // Controlled_Buffer controlled_buffer_1
  not not_3 (not_3_out, halt);
  Multiplexer #(.select(2), .width(32), .disabled("Z"), .enable("false")) multiplexer_3 (
    .in0(IF_PC), .in1(and_3_out), .in2(Branch_add), .out(multiplexer_3_out), .sel({or_1_out[1], EX_JALR}));  // open: in3
  or or_2 (or_2_out, EX_JALR, or_1_out[1]);
  Pull_Resistor #(.pull(1)) pull_resistor_1 (.node(CLK));
  // RiscV_Probe riscv_probe_6: pin names not known; wires that end beside it: IF_IR, IF_PC_4
  ROM #(.addrWidth(10), .dataWidth(32), .Select("high")) rom_1 (.addr(IF_PC[11:2]), .data(IF_IR));
  Counter #(.width(16), .max('hffff), .ongoal("wrap"), .trigger("rising"), .behavior("new")) counter_2 (
    .count(not_3_out), .Q(\总周期数 ), .clk(CLK));  // open: load, D, carry, clr, preset, down
  and and_4 (and_4_out, ~stall, ~halt);  // AND_Gate
  IF_ID if_id_1 (
    .IR(IF_IR), .PC(IF_PC), .PC_4(IF_PC_4), .IR_2(ID_IR), .PC_2(ID_PC), .PC_4_2(if_id_1_pc_4_2), .reset(RST),
    .BranchTaken(PredictError), .en(and_4_out), .clk(CLK), .PredictJump(IF_PredictJump),
    .PredictJump_2(ID_PredictJump));
  BTB btb_1 (
    .PC(IF_PC), .EX_PC(EX_PC), .EX_BranchAddr(multiplexer_3_out), .EX_Branch(or_2_out),
    .EX_Branched(BranchTaken), .in_6(CLK), .IF_PredictJump(IF_PredictJump), .BTB_JumpAddr(btb_1_btb_jumpaddr));
  not not_4 (PredictError, comparator_2_eq);
  Comparator #(.width(1), .mode("twosComplement")) comparator_2 (
    .a(BranchTaken), .b(EX_PredictJump), .eq(comparator_2_eq));  // open: gt, lt
  Multiplexer #(.select(1), .width(1), .disabled("Z"), .enable("false")) multiplexer_4 (
    .in0(and_5_out), .in1(1'b0), .out(multiplexer_4_out), .sel(CLK));
  and and_5 (and_5_out, \无条件分支 , CLK);
  Counter #(.width(16), .max('hffff), .ongoal("wrap"), .trigger("rising"), .behavior("old")) counter_3 (
    .count(1'b1), .Q(\无条件分支数 ), .clk(multiplexer_4_out), .clr(RST));  // open: load, D, carry, preset
  or or_3 (\无条件分支 , EX_JALR, EX_JAL);
  \单周期硬布线控制器  \u_单周期硬布线控制器_1  (
    .Funct({ID_IR[30], ID_IR[25], ID_IR[14:12]}), .OP(ID_IR[6:2]), .ALU_OP(\单周期硬布线控制器_1_alu_op ),
    .MemToReg(\单周期硬布线控制器_1_memtoreg ), .MemWrite(\单周期硬布线控制器_1_memwrite ), .ALU_SRC(\单周期硬布线控制器_1_alu_src ),
    .RegWrite(\单周期硬布线控制器_1_regwrite ), .ecall(ecall), .S_type(\单周期硬布线控制器_1_s_type ),
    .Jalr(\单周期硬布线控制器_1_jalr ), .Beq(\单周期硬布线控制器_1_beq ), .JAL(\单周期硬布线控制器_1_jal ), .Bne(\单周期硬布线控制器_1_bne ),
    .in_3(ID_IR[21]), .uret(\单周期硬布线控制器_1_uret ), .SRL(SRL), .SLTIU(SLTIU), .SH(SH), .BGE(BGE),
    .rs1_used(\单周期硬布线控制器_1_rs1_used ), .rs2_used(\单周期硬布线控制器_1_rs2_used ));  // open: CSRRSI, CSRRCI
  assign bit_extender_1_out = {{20{ID_IR[31]}}, {ID_IR[31], ID_IR[7], ID_IR[30:25], ID_IR[11:8]}};  // Bit_Extender bit_extender_1
  assign bit_extender_2_out = {{12{ID_IR[31]}}, {ID_IR[31], ID_IR[19:12], ID_IR[20], ID_IR[30:21]}};  // Bit_Extender bit_extender_2
  Multiplexer #(.select(1), .width(32), .disabled("Z"), .enable("false")) multiplexer_5 (
    .in0(IF_PC_4), .in1(btb_1_btb_jumpaddr), .out(PredictAdd), .sel(IF_PredictJump));
  Multiplexer #(.select(1), .width(5), .disabled("Z"), .enable("false")) multiplexer_6 (
    .in0(ID_IR[19:15]), .in1(5'b10001), .out(multiplexer_6_out), .sel(ecall));
  Multiplexer #(.select(1), .width(5), .disabled("Z"), .enable("false")) multiplexer_7 (
    .in0(ID_IR[24:20]), .in1(5'b01010), .out(multiplexer_7_out), .sel(ecall));
  Multiplexer #(.select(1), .width(12), .disabled("Z"), .enable("false")) multiplexer_8 (
    .in0(ID_IR[31:20]), .in1({ID_IR[31:25], ID_IR[11:7]}), .out(multiplexer_8_out), .sel(\单周期硬布线控制器_1_s_type ));
  or or_4 (flush, PredictError, stall);
  assign bit_extender_3_out = {{20{multiplexer_8_out[11]}}, multiplexer_8_out};  // Bit_Extender bit_extender_3
  not not_5 (not_5_out, CLK);
  and and_6 (and_6_out, \条件分支 , CLK);
  ID_EX id_ex_1 (
    .Beq(\单周期硬布线控制器_1_beq ), .Bne(\单周期硬布线控制器_1_bne ), .MemToReg(\单周期硬布线控制器_1_memtoreg ),
    .MemWrite(\单周期硬布线控制器_1_memwrite ), .AluSrc(\单周期硬布线控制器_1_alu_src ), .RegWrite(\单周期硬布线控制器_1_regwrite ),
    .SType(\单周期硬布线控制器_1_s_type ), .ecall(ecall), .Jal(\单周期硬布线控制器_1_jal ), .Jalr(\单周期硬布线控制器_1_jalr ),
    .SLTIU(SLTIU), .SH(SH), .BGE(BGE), .ALU_OP(\单周期硬布线控制器_1_alu_op ), .rd(ID_IR[11:7]), .R1(regifile_1_r1),
    .R2(regifile_1_r2), .imm1(bit_extender_3_out), .IR(ID_IR), .PC(ID_PC), .PC_4(if_id_1_pc_4_2),
    .RS1_Forward(\重定向处理逻辑_1_rs1_forward ), .RS2_Forward(\重定向处理逻辑_1_rs2_forward ), .Beq_2(EX_Beq),
    .Bne_2(EX_Bne), .MemToReg_2(id_ex_1_memtoreg_2), .MenWrite(id_ex_1_menwrite),
    .AluSrc_2(id_ex_1_alusrc_2), .RegWrite_2(id_ex_1_regwrite_2), .ecall_2(EX_ecall), .Jal_2(EX_JAL),
    .Jalr_2(EX_JALR), .SLTIU_2(id_ex_1_sltiu_2), .SH_2(id_ex_1_sh_2), .BGE_2(EX_BGE),
    .ALU_OP_2(id_ex_1_alu_op_2), .rd_2(id_ex_1_rd_2), .R1_2(id_ex_1_r1_2), .R2_2(id_ex_1_r2_2),
    .imm1_2(id_ex_1_imm1_2), .IR_2(EX_IR), .PC_2(EX_PC), .PC_4_2(EX_PC_4),
    .RS1_Forward_2(id_ex_1_rs1_forward_2), .RS2_Forward_2(id_ex_1_rs2_forward_2), .Reset(RST), .Flush(flush),
    .en(not_6_out), .clk(CLK), .imm2j(bit_extender_2_out), .imm2j_2(id_ex_1_imm2j_2),
    .imm2b(bit_extender_1_out), .imm2b_2(id_ex_1_imm2b_2), .PredictJump(ID_PredictJump),
    .PredictJump_2(EX_PredictJump));  // open: SType_2, URET, URET_2
  Regifile regifile_1 (
    .Din(RDin), .Clk(not_5_out), .R1(regifile_1_r1), .R2(regifile_1_r2), .WE(RegWrite), .W_num(WB_rd),
    .R1_num(multiplexer_6_out), .R2_num(multiplexer_7_out));
  not not_6 (not_6_out, halt);
  Counter #(.width(16), .max('hffff), .ongoal("wrap"), .trigger("rising"), .behavior("old")) counter_4 (
    .count(1'b1), .Q(\条件分支成功数 ), .clk(multiplexer_9_out), .clr(RST));  // open: load, D, carry, preset
  Multiplexer #(.select(1), .width(1), .disabled("Z"), .enable("false")) multiplexer_9 (
    .in0(and_6_out), .in1(1'b0), .out(multiplexer_9_out), .sel(CLK));
  Multiplexer #(.select(2), .width(32), .disabled("Z"), .enable("false")) multiplexer_10 (
    .in0(id_ex_1_r1_2), .in1(RDin), .in2(MEM_ALUresult), .out(EX_R1), .sel(id_ex_1_rs1_forward_2));  // open: in3
  Multiplexer #(.select(2), .width(32), .disabled("Z"), .enable("false")) multiplexer_11 (
    .in0(id_ex_1_r2_2), .in1(RDin), .in2(MEM_ALUresult), .out(EX_R2), .sel(id_ex_1_rs2_forward_2));  // open: in3
  Shifter #(.width(32), .shift("ll")) shifter_1 (.in(id_ex_1_imm2b_2), .\dist (5'b00001), .out(shifter_1_out));
  Shifter #(.width(32), .shift("ll")) shifter_2 (.in(id_ex_1_imm2j_2), .\dist (5'b00001), .out(shifter_2_out));
  Comparator #(.width(32), .mode("twosComplement")) comparator_3 (
    .a(EX_R1), .b(32'h22), .eq(comparator_3_eq));  // open: gt, lt
  Multiplexer #(.select(1), .width(32), .disabled("Z"), .enable("false")) multiplexer_12 (
    .in0(EX_R2), .in1(id_ex_1_imm1_2), .out(multiplexer_12_out), .sel(id_ex_1_alusrc_2));
  Adder #(.width(32)) adder_2 (.a(shifter_1_out), .b(EX_PC), .out(adder_2_out));  // open: cin, cout
  Adder #(.width(32)) adder_3 (.a(shifter_2_out), .b(EX_PC), .out(adder_3_out));  // open: cin, cout
  not not_7 (not_7_out, comparator_3_eq);
  Register #(.width(32), .trigger("rising"), .Select("low")) PC_2 (
    .D(EX_R2), .en(and_7_out), .Q(LedData), .clk(CLK));  // open: clr
  and and_7 (and_7_out, comparator_3_eq, EX_ecall);
  or or_5 (BranchTaken, EX_JALR, or_6_out[1]);
  or or_6 (or_6_out[1], EX_JAL, and_8_out, and_11_out, and_10_out);
  and and_8 (and_8_out, EX_Beq, alu_1_equal);
  ALU alu_1 (
    .X(EX_R1), .Y(multiplexer_12_out), .AluOP(id_ex_1_alu_op_2), .Equal(alu_1_equal), .Result(Alu_add),
    .out_4(alu_1_out_4), .out_6(alu_1_out_6));  // open: Result_2
  Multiplexer #(.select(1), .width(32), .disabled("Z"), .enable("false")) multiplexer_13 (
    .in0(adder_2_out), .in1(adder_3_out), .out(Branch_add), .sel(EX_JAL));
  and and_9 (EX_halt, EX_ecall, not_7_out);
  or or_7 (\条件分支 , and_8_out, and_11_out, and_10_out);
  and and_10 (and_10_out, EX_BGE, alu_1_out_4);
  and and_11 (and_11_out, ~alu_1_equal, EX_Bne);  // AND_Gate
  Counter #(.width(16), .max('hffff), .ongoal("wrap"), .trigger("rising"), .behavior("old")) counter_5 (
    .count(1'b1), .Q(\插入气泡数 ), .clk(multiplexer_14_out), .clr(RST));  // open: load, D, carry, preset
  Multiplexer #(.select(1), .width(1), .disabled("Z"), .enable("false")) multiplexer_14 (
    .in0(and_12_out), .in1(1'b0), .out(multiplexer_14_out), .sel(CLK));
  and and_12 (and_12_out, and_13_out, CLK);
  and and_13 (and_13_out, ~halt, flush);  // AND_Gate
  EX_MEM ex_mem_1 (
    .Jal(EX_JAL), .Jalr(EX_JALR), .MemToReg(id_ex_1_memtoreg_2), .MemWrite(id_ex_1_menwrite),
    .RegWrite(id_ex_1_regwrite_2), .Halt(EX_halt), .SLTIU(id_ex_1_sltiu_2), .SH(id_ex_1_sh_2),
    .ALU(alu_1_out_6), .rd(id_ex_1_rd_2), .result(Alu_add), .WriteData(EX_R2), .IR(EX_IR), .PC(EX_PC),
    .PC_4(EX_PC_4), .Jal_2(ex_mem_1_jal_2), .Jalr_2(ex_mem_1_jalr_2), .MemToReg_2(ex_mem_1_memtoreg_2),
    .MemWrite_2(MemWrite), .RegWrite_2(ex_mem_1_regwrite_2), .Halt_2(ex_mem_1_halt_2),
    .SLTIU_2(ex_mem_1_sltiu_2), .SH_2(MEM_SH), .ALU_2(ex_mem_1_alu_2), .rd_2(ex_mem_1_rd_2),
    .result_2(MEM_ALUresult), .Writedata_2(MEM_R2), .IR_2(MEM_IR), .PC_2(M_PC), .PC_4_2(ex_mem_1_pc_4_2),
    .reset(RST), .en(not_6_out), .clk(CLK));  // open: URET, URET_2
  and and_14 (and_14_out, stall, CLK);
  Shifter #(.width(32), .shift("ll")) shifter_3 (.in(MEM_R2), .\dist (5'b10000), .out(shifter_3_out));
  Counter #(.width(16), .max('hffff), .ongoal("wrap"), .trigger("rising"), .behavior("old")) counter_6 (
    .count(1'b1), .Q(\LoadUse次数 ), .clk(multiplexer_15_out), .clr(RST));  // open: load, D, carry, preset
  Multiplexer #(.select(1), .width(1), .disabled("Z"), .enable("false")) multiplexer_15 (
    .in0(and_14_out), .in1(1'b0), .out(multiplexer_15_out), .sel(CLK));
  Multiplexer #(.select(1), .width(32), .disabled("Z"), .enable("false")) multiplexer_16 (
    .in0(MEM_R2), .in1(shifter_3_out), .out(MDin), .sel(MEM_ALUresult[1]));
  // MIPS_RAM mips_ram_1: pin names not known; wires that end beside it: MEM_ALUresult[11:2], MDin, MemWrite, RAM_Sel, CLK, 1'b1, RST, mips_ram_1_p8
  Multiplexer #(.select(1), .width(4), .disabled("Z"), .enable("false")) multiplexer_17 (
    .in0(4'b1111), .in1({{2{multiplexer_18_out[3]}}, {2{multiplexer_18_out[1]}}}), .out(RAM_Sel), .sel(MEM_SH));
  Multiplexer #(.select(1), .width(1), .disabled("Z"), .enable("false")) multiplexer_18 (
    .in0(1'b1), .in1(1'b0), .out(multiplexer_18_out[1]), .sel(MEM_ALUresult[1]));
  Multiplexer #(.select(1), .width(1), .disabled("Z"), .enable("false")) multiplexer_19 (
    .in0(1'b0), .in1(1'b1), .out(multiplexer_18_out[3]), .sel(MEM_ALUresult[1]));
  MEM_WB mem_wb_1 (
    .Jal(ex_mem_1_jal_2), .Jalr(ex_mem_1_jalr_2), .MemToReg(ex_mem_1_memtoreg_2),
    .RegWrite(ex_mem_1_regwrite_2), .Halt(ex_mem_1_halt_2), .rd(ex_mem_1_rd_2), .AluResult(MEM_ALUresult),
    .ReadData(mips_ram_1_p8), .IR(MEM_IR), .PC(M_PC), .PC_4(ex_mem_1_pc_4_2), .Jal_2(mem_wb_1_jal_2),
    .Jalr_2(mem_wb_1_jalr_2), .MemToReg_2(mem_wb_1_memtoreg_2[0]), .RegWrite_2(RegWrite),
    .Halt_2(mem_wb_1_halt_2), .rd_2(WB_rd), .AluResult_2(mem_wb_1_aluresult_2),
    .Readdata_2(mem_wb_1_readdata_2), .IR_2(WB_IR), .PC_2(WB_PC), .PC_4_2(mem_wb_1_pc_4_2), .reset(RST),
    .en(not_6_out), .clk(CLK), .SLTIU(ex_mem_1_sltiu_2), .SLTIU_2(WB_SLTIU), .ALU(ex_mem_1_alu_2),
    .ALU_2(WB_ALU));  // open: URET, URET_2, SH, SH_2
  or or_8 (mem_wb_1_memtoreg_2[1], mem_wb_1_jal_2, mem_wb_1_jalr_2);
  Multiplexer #(.select(2), .width(32), .disabled("Z"), .enable("false")) multiplexer_20 (
    .in0(mem_wb_1_aluresult_2), .in1(mem_wb_1_readdata_2), .in2(mem_wb_1_pc_4_2), .out(multiplexer_20_out),
    .sel(mem_wb_1_memtoreg_2));  // open: in3
  or or_9 (or_9_out, mem_wb_1_halt_2, halt);
  D_Flip_Flop #(.trigger("falling"), .Pre_Clr_Positions("ABOVE_BELOW"), .NegatePresetClear("false"), .enable("false"), .NewFFLayout("true")) d_ff_2 (
    .clk(CLK), .D(or_9_out), .Q(halt), .reset(Go));  // open: Qn, preset
  Multiplexer #(.select(1), .width(32), .disabled("Z"), .enable("false")) multiplexer_21 (
    .in0(multiplexer_20_out), .in1(multiplexer_22_out), .out(RDin), .sel(WB_SLTIU));
  Multiplexer #(.select(1), .width(32), .disabled("Z"), .enable("false")) multiplexer_22 (
    .in0({32{1'b0}}), .in1(32'h1), .out(multiplexer_22_out), .sel(WB_ALU));

  // Other names for the same wires on the sheet: MEM_PC[31:0] = M_PC; WB_RegWrite = RegWrite

  // Notes on the sheet:
  //   中断源
  //   时空图监测，可删除
  //   中断等待指示
  //   数码管输出
  //   控制位
  //   流水调试日志用
  //   暂停节拍，不能为0
  //   戳工具置1进入计数暂停模式，ctrl+k时钟自动运行到对应节拍暂停
  //   ctrl+k关闭时钟连续运行，将控制位置零，进入单步调试模式调试
  //   可计数暂停的时钟源
  //   指令存储器
  //   contents of rom_1 (hex, n*v repeats v):
  //   100493 100006f 100493 200913 300993 100006f 100493 200913 300993 100006f 100493 200913 300993
  //   100006f 100493 200913 300993 29c000ef 100413 100493 1f49493 900533 2200893 73 24d493 48463 fedff06f
  //   900533 2200893 73 100493 249493 900533 2200893 73 48463 fedff06f 100493 1f49493 900533 2200893 73
  //   4034d493 900533 2200893 73 4044d493 900533 2200893 73 4044d493 900533 2200893 73 4044d493 900533
  //   2200893 73 4044d493 900533 2200893 73 4044d493 900533 2200893 73 4044d493 900533 2200893 73 4044d493
  //   900533 2200893 73 100413 1f41993 41f9d993 433 c00913 300b13 140413 f47413 800293 100313 499993
  //   89e9b3 1300533 2200893 73 406282b3 fe0294e3 140413 f00f93 1f47433 1c41413 800293 100313 49d993
  //   89e9b3 1300533 2200893 73 406282b3 fe0294e3 1c45413 406b0b33 b0463 f95ff06f 2b3 fff2c293 829293
  //   ff2e293 500533 2200893 73 fff00413 493 84a023 140413 448493 84a023 140413 448493 84a023 140413
  //   448493 84a023 140413 448493 84a023 140413 448493 84a023 140413 448493 84a023 140413 448493 84a023
  //   140413 448493 84a023 140413 448493 84a023 140413 448493 84a023 140413 448493 84a023 140413 448493
  //   84a023 140413 448493 84a023 140413 448493 84a023 140413 448493 84a023 140413 448493 140413 433
  //   3c00493 42983 4aa03 149a2b3 28663 134a023 1442023 ffc48493 fe9412e3 800533 2200893 73 440413 3c00493
  //   fc9416e3 a00893 73 413 140413 800533 2200893 73 240413 800533 2200893 73 340413 800533 2200893 73
  //   440413 800533 2200893 73 540413 800533 2200893 73 640413 800533 2200893 73 740413 800533 2200893 73
  //   840413 800533 2200893 2200893 73 8067
  //   指令探针
  //   为方便自动评测，需要输出流水线各段保存的PC值，注意是PC不是PC+4，另外ID段寄存器写入信息，Mem段内存写入信息也要输出
  //   JAL
  //   JALR
  //   URET
  //   rs1
  //   rs2
  //   imm-i
  //   rd
  //   imm-j
  //   beq/bne
  //   jal
  //   rd
  //   Beq
  //   Bne
  //   MemToReg
  //   MemWrite
  //   AluOP
  //   AluSrcB
  //   RegWrite
  //   S_type
  //   Beq
  //   Jal
  //   Jalr
  //   Bne
  //   数据存储器
endmodule

module \封装正确性测试  (
);

  wire IR1, IR2, IR3, MemW, RegW;
  wire [31:0] EX_PC, ID_PC, IF_PC, IR, LED, MDin, MDinr, MEM_PC, PC, RDin, RDinr, WB_PC;

  \单周期RISC_V  \u_单周期risc_v_1  (
    .IR1(IR1), .IR2(IR2), .IR3(IR3), .RegWrite(RegW), .MemWrite(MemW), .PC(PC), .IR(IR), .RDin(RDin),
    .MDin(MDin), .LedData(LED));
  \气泡流水线  \u_气泡流水线_1  (
    .RegWrite(RegW), .MemWrite(MemW), .IF_PC(IF_PC), .ID_PC(ID_PC), .EX_PC(EX_PC), .M_PC(MEM_PC),
    .WB_PC(WB_PC), .RDin(RDinr), .MDin(MDinr), .LedData(LED));
  \单周期_单级中断  \u_单周期_单级中断_1  (
    .IR1(IR1), .IR2(IR2), .IR3(IR3), .RegWrite(RegW), .MemWrite(MemW), .PC(PC), .IR(IR), .RDin(RDin),
    .MDin(MDin), .LedData(LED));
  \理想流水线  \u_理想流水线_1  (
    .RegWrite(RegW), .MemWrite(MemW), .IF_PC(IF_PC), .ID_PC(ID_PC), .EX_PC(EX_PC), .M_PC(MEM_PC),
    .WB_PC(WB_PC), .RDin(RDinr), .MDin(MDinr), .LedData(LED));
  \重定向流水线  \u_重定向流水线_1  (
    .RegWrite(RegW), .MemWrite(MemW), .IF_PC(IF_PC), .ID_PC(ID_PC), .EX_PC(EX_PC), .M_PC(MEM_PC),
    .WB_PC(WB_PC), .RDin(RDinr), .MDin(MDinr), .LedData(LED));
  \单周期_多级中断  \u_单周期_多级中断_1  (
    .IR1(IR1), .IR2(IR2), .IR3(IR3), .RegWrite(RegW), .MemWrite(MemW), .PC(PC), .IR(IR), .RDin(RDin),
    .MDin(MDin), .LedData(LED));

  // Notes on the sheet:
  //   单周期封装测试
  //   气泡流水封装测试
  //   单周期+单级中断封装测试
  //   请检查上面封装有无位宽不匹配，引脚标签是否和连接的标签相对应，否则无法在educoder平台上正确测试
  //   理想流水封装测试
  //   重定向流水封装测试
  //   单周期+多级中断封装测试
endmodule

module IF_ID (
  input  PredictJump,
  input  [31:0] IR,
  input  [31:0] PC,
  input  [31:0] PC_4,
  input  en,
  input  clk,
  input  reset,
  input  BranchTaken,
  output PredictJump_2,
  output [31:0] IR_2,
  output [31:0] PC_2,
  output [31:0] PC_4_2
);

  wire multiplexer_1_out, or_1_out;
  wire [31:0] multiplexer_2_out, multiplexer_3_out, multiplexer_4_out;

  Multiplexer #(.select(1), .width(1), .disabled("Z"), .enable("false")) multiplexer_1 (
    .in0(PredictJump), .in1(1'b0), .out(multiplexer_1_out), .sel(or_1_out));
  Multiplexer #(.select(1), .width(32), .disabled("Z"), .enable("false")) multiplexer_2 (
    .in0(IR), .in1({32{1'b0}}), .out(multiplexer_2_out), .sel(or_1_out));
  Multiplexer #(.select(1), .width(32), .disabled("Z"), .enable("false")) multiplexer_3 (
    .in0(PC), .in1({32{1'b0}}), .out(multiplexer_3_out), .sel(or_1_out));
  Multiplexer #(.select(1), .width(32), .disabled("Z"), .enable("false")) multiplexer_4 (
    .in0(PC_4), .in1({32{1'b0}}), .out(multiplexer_4_out), .sel(or_1_out));
  or or_1 (or_1_out, reset, BranchTaken);
  Register #(.width(1), .trigger("rising"), .Select("low")) register_1 (
    .D(multiplexer_1_out), .en(en), .Q(PredictJump_2), .clk(clk));  // open: clr
  Register #(.width(32), .trigger("rising"), .Select("low")) register_2 (
    .D(multiplexer_2_out), .en(en), .Q(IR_2), .clk(clk));  // open: clr
  Register #(.width(32), .trigger("rising"), .Select("low")) register_3 (
    .D(multiplexer_3_out), .en(en), .Q(PC_2), .clk(clk));  // open: clr
  Register #(.width(32), .trigger("rising"), .Select("low")) register_4 (
    .D(multiplexer_4_out), .en(en), .Q(PC_4_2), .clk(clk));  // open: clr
endmodule

module ID_EX (
  input  PredictJump,
  input  Beq,
  input  Bne,
  input  MemToReg,
  input  MemWrite,
  input  AluSrc,
  input  RegWrite,
  input  SType,
  input  ecall,
  input  Jal,
  input  Jalr,
  input  URET,
  input  SLTIU,
  input  SH,
  input  BGE,
  input  [3:0] ALU_OP,
  input  [4:0] rd,
  input  [31:0] R1,
  input  [31:0] R2,
  input  [31:0] imm1,
  input  [31:0] imm2b,
  input  [31:0] imm2j,
  input  [31:0] IR,
  input  [31:0] PC,
  input  [31:0] PC_4,
  input  [1:0] RS1_Forward,
  input  [1:0] RS2_Forward,
  input  Reset,
  input  Flush,
  input  en,
  input  clk,
  output PredictJump_2,
  output Beq_2,
  output Bne_2,
  output MemToReg_2,
  output MenWrite,
  output AluSrc_2,
  output RegWrite_2,
  output SType_2,
  output ecall_2,
  output Jal_2,
  output Jalr_2,
  output URET_2,
  output SLTIU_2,
  output SH_2,
  output BGE_2,
  output [3:0] ALU_OP_2,
  output [4:0] rd_2,
  output [31:0] R1_2,
  output [31:0] R2_2,
  output [31:0] imm1_2,
  output [31:0] imm2b_2,
  output [31:0] imm2j_2,
  output [31:0] IR_2,
  output [31:0] PC_2,
  output [31:0] PC_4_2,
  output [1:0] RS1_Forward_2,
  output [1:0] RS2_Forward_2
);

  wire multiplexer_1_out, multiplexer_2_out, multiplexer_3_out, multiplexer_4_out, multiplexer_5_out,
       multiplexer_6_out, multiplexer_7_out, multiplexer_8_out, multiplexer_9_out, multiplexer_10_out,
       multiplexer_11_out, multiplexer_12_out, multiplexer_13_out, multiplexer_14_out, multiplexer_15_out,
       or_1_out;
  wire [1:0] multiplexer_26_out, multiplexer_27_out;
  wire [3:0] multiplexer_16_out;
  wire [4:0] multiplexer_17_out;
  wire [31:0] multiplexer_18_out, multiplexer_19_out, multiplexer_20_out, multiplexer_21_out,
       multiplexer_22_out, multiplexer_23_out, multiplexer_24_out, multiplexer_25_out;

  Multiplexer #(.select(1), .width(1), .disabled("Z"), .enable("false")) multiplexer_1 (
    .in0(PredictJump), .in1(1'b0), .out(multiplexer_1_out), .sel(or_1_out));
  Multiplexer #(.select(1), .width(1), .disabled("Z"), .enable("false")) multiplexer_2 (
    .in0(Beq), .in1(1'b0), .out(multiplexer_2_out), .sel(or_1_out));
  Multiplexer #(.select(1), .width(1), .disabled("Z"), .enable("false")) multiplexer_3 (
    .in0(Bne), .in1(1'b0), .out(multiplexer_3_out), .sel(or_1_out));
  Multiplexer #(.select(1), .width(1), .disabled("Z"), .enable("false")) multiplexer_4 (
    .in0(MemToReg), .in1(1'b0), .out(multiplexer_4_out), .sel(or_1_out));
  Multiplexer #(.select(1), .width(1), .disabled("Z"), .enable("false")) multiplexer_5 (
    .in0(MemWrite), .in1(1'b0), .out(multiplexer_5_out), .sel(or_1_out));
  Multiplexer #(.select(1), .width(1), .disabled("Z"), .enable("false")) multiplexer_6 (
    .in0(AluSrc), .in1(1'b0), .out(multiplexer_6_out), .sel(or_1_out));
  Multiplexer #(.select(1), .width(1), .disabled("Z"), .enable("false")) multiplexer_7 (
    .in0(RegWrite), .in1(1'b0), .out(multiplexer_7_out), .sel(or_1_out));
  Multiplexer #(.select(1), .width(1), .disabled("Z"), .enable("false")) multiplexer_8 (
    .in0(SType), .in1(1'b0), .out(multiplexer_8_out), .sel(or_1_out));
  Multiplexer #(.select(1), .width(1), .disabled("Z"), .enable("false")) multiplexer_9 (
    .in0(ecall), .in1(1'b0), .out(multiplexer_9_out), .sel(or_1_out));
  Multiplexer #(.select(1), .width(1), .disabled("Z"), .enable("false")) multiplexer_10 (
    .in0(Jal), .in1(1'b0), .out(multiplexer_10_out), .sel(or_1_out));
  Multiplexer #(.select(1), .width(1), .disabled("Z"), .enable("false")) multiplexer_11 (
    .in0(Jalr), .in1(1'b0), .out(multiplexer_11_out), .sel(or_1_out));
  Multiplexer #(.select(1), .width(1), .disabled("Z"), .enable("false")) multiplexer_12 (
    .in0(URET), .in1(1'b0), .out(multiplexer_12_out), .sel(or_1_out));
  Multiplexer #(.select(1), .width(1), .disabled("Z"), .enable("false")) multiplexer_13 (
    .in0(SLTIU), .in1(1'b0), .out(multiplexer_13_out), .sel(or_1_out));
  Multiplexer #(.select(1), .width(1), .disabled("Z"), .enable("false")) multiplexer_14 (
    .in0(SH), .in1(1'b0), .out(multiplexer_14_out), .sel(or_1_out));
  Multiplexer #(.select(1), .width(1), .disabled("Z"), .enable("false")) multiplexer_15 (
    .in0(BGE), .in1(1'b0), .out(multiplexer_15_out), .sel(or_1_out));
  Multiplexer #(.select(1), .width(4), .disabled("Z"), .enable("false")) multiplexer_16 (
    .in0(ALU_OP), .in1(4'b0000), .out(multiplexer_16_out), .sel(or_1_out));
  Multiplexer #(.select(1), .width(5), .disabled("Z"), .enable("false")) multiplexer_17 (
    .in0(rd), .in1({5{1'b0}}), .out(multiplexer_17_out), .sel(or_1_out));
  Multiplexer #(.select(1), .width(32), .disabled("Z"), .enable("false")) multiplexer_18 (
    .in0(R1), .in1({32{1'b0}}), .out(multiplexer_18_out), .sel(or_1_out));
  Multiplexer #(.select(1), .width(32), .disabled("Z"), .enable("false")) multiplexer_19 (
    .in0(R2), .in1({32{1'b0}}), .out(multiplexer_19_out), .sel(or_1_out));
  Multiplexer #(.select(1), .width(32), .disabled("Z"), .enable("false")) multiplexer_20 (
    .in0(imm1), .in1({32{1'b0}}), .out(multiplexer_20_out), .sel(or_1_out));
  Multiplexer #(.select(1), .width(32), .disabled("Z"), .enable("false")) multiplexer_21 (
    .in0(imm2b), .in1({32{1'b0}}), .out(multiplexer_21_out), .sel(or_1_out));
  Multiplexer #(.select(1), .width(32), .disabled("Z"), .enable("false")) multiplexer_22 (
    .in0(imm2j), .in1({32{1'b0}}), .out(multiplexer_22_out), .sel(or_1_out));
  Multiplexer #(.select(1), .width(32), .disabled("Z"), .enable("false")) multiplexer_23 (
    .in0(IR), .in1({32{1'b0}}), .out(multiplexer_23_out), .sel(or_1_out));
  Multiplexer #(.select(1), .width(32), .disabled("Z"), .enable("false")) multiplexer_24 (
    .in0(PC), .in1({32{1'b0}}), .out(multiplexer_24_out), .sel(or_1_out));
  Multiplexer #(.select(1), .width(32), .disabled("Z"), .enable("false")) multiplexer_25 (
    .in0(PC_4), .in1({32{1'b0}}), .out(multiplexer_25_out), .sel(or_1_out));
  Multiplexer #(.select(1), .width(2), .disabled("Z"), .enable("false")) multiplexer_26 (
    .in0(RS1_Forward), .in1(2'b00), .out(multiplexer_26_out), .sel(or_1_out));
  Multiplexer #(.select(1), .width(2), .disabled("Z"), .enable("false")) multiplexer_27 (
    .in0(RS2_Forward), .in1(2'b00), .out(multiplexer_27_out), .sel(or_1_out));
  or or_1 (or_1_out, Reset, Flush);
  Register #(.width(1), .trigger("rising"), .Select("low")) register_1 (
    .D(multiplexer_1_out), .en(en), .Q(PredictJump_2), .clk(clk));  // open: clr
  Register #(.width(1), .trigger("rising"), .Select("low")) register_2 (
    .D(multiplexer_2_out), .en(en), .Q(Beq_2), .clk(clk));  // open: clr
  Register #(.width(1), .trigger("rising"), .Select("low")) register_3 (
    .D(multiplexer_3_out), .en(en), .Q(Bne_2), .clk(clk));  // open: clr
  Register #(.width(1), .trigger("rising"), .Select("low")) register_4 (
    .D(multiplexer_4_out), .en(en), .Q(MemToReg_2), .clk(clk));  // open: clr
  Register #(.width(1), .trigger("rising"), .Select("low")) register_5 (
    .D(multiplexer_5_out), .en(en), .Q(MenWrite), .clk(clk));  // open: clr
  Register #(.width(1), .trigger("rising"), .Select("low")) register_6 (
    .D(multiplexer_6_out), .en(en), .Q(AluSrc_2), .clk(clk));  // open: clr
  Register #(.width(1), .trigger("rising"), .Select("low")) register_7 (
    .D(multiplexer_7_out), .en(en), .Q(RegWrite_2), .clk(clk));  // open: clr
  Register #(.width(1), .trigger("rising"), .Select("low")) register_8 (
    .D(multiplexer_8_out), .en(en), .Q(SType_2), .clk(clk));  // open: clr
  Register #(.width(1), .trigger("rising"), .Select("low")) register_9 (
    .D(multiplexer_9_out), .en(en), .Q(ecall_2), .clk(clk));  // open: clr
  Register #(.width(1), .trigger("rising"), .Select("low")) register_10 (
    .D(multiplexer_10_out), .en(en), .Q(Jal_2), .clk(clk));  // open: clr
  Register #(.width(1), .trigger("rising"), .Select("low")) register_11 (
    .D(multiplexer_11_out), .en(en), .Q(Jalr_2), .clk(clk));  // open: clr
  Register #(.width(1), .trigger("rising"), .Select("low")) register_12 (
    .D(multiplexer_12_out), .en(en), .Q(URET_2), .clk(clk));  // open: clr
  Register #(.width(1), .trigger("rising"), .Select("low")) register_13 (
    .D(multiplexer_13_out), .en(en), .Q(SLTIU_2), .clk(clk));  // open: clr
  Register #(.width(1), .trigger("rising"), .Select("low")) register_14 (
    .D(multiplexer_14_out), .en(en), .Q(SH_2), .clk(clk));  // open: clr
  Register #(.width(1), .trigger("rising"), .Select("low")) register_15 (
    .D(multiplexer_15_out), .en(en), .Q(BGE_2), .clk(clk));  // open: clr
  Register #(.width(4), .trigger("rising"), .Select("low")) register_16 (
    .D(multiplexer_16_out), .en(en), .Q(ALU_OP_2), .clk(clk));  // open: clr
  Register #(.width(5), .trigger("rising"), .Select("low")) register_17 (
    .D(multiplexer_17_out), .en(en), .Q(rd_2), .clk(clk));  // open: clr
  Register #(.width(32), .trigger("rising"), .Select("low")) register_18 (
    .D(multiplexer_18_out), .en(en), .Q(R1_2), .clk(clk));  // open: clr
  Register #(.width(32), .trigger("rising"), .Select("low")) register_19 (
    .D(multiplexer_19_out), .en(en), .Q(R2_2), .clk(clk));  // open: clr
  Register #(.width(32), .trigger("rising"), .Select("low")) register_20 (
    .D(multiplexer_20_out), .en(en), .Q(imm1_2), .clk(clk));  // open: clr
  Register #(.width(32), .trigger("rising"), .Select("low")) register_21 (
    .D(multiplexer_21_out), .en(en), .Q(imm2b_2), .clk(clk));  // open: clr
  Register #(.width(32), .trigger("rising"), .Select("low")) register_22 (
    .D(multiplexer_22_out), .en(en), .Q(imm2j_2), .clk(clk));  // open: clr
  Register #(.width(32), .trigger("rising"), .Select("low")) register_23 (
    .D(multiplexer_23_out), .en(en), .Q(IR_2), .clk(clk));  // open: clr
  Register #(.width(32), .trigger("rising"), .Select("low")) register_24 (
    .D(multiplexer_24_out), .en(en), .Q(PC_2), .clk(clk));  // open: clr
  Register #(.width(32), .trigger("rising"), .Select("low")) register_25 (
    .D(multiplexer_25_out), .en(en), .Q(PC_4_2), .clk(clk));  // open: clr
  Register #(.width(2), .trigger("rising"), .Select("low")) register_26 (
    .D(multiplexer_26_out), .en(en), .Q(RS1_Forward_2), .clk(clk));  // open: clr
  Register #(.width(2), .trigger("rising"), .Select("low")) register_27 (
    .D(multiplexer_27_out), .en(en), .Q(RS2_Forward_2), .clk(clk));  // open: clr
endmodule

module EX_MEM (
  input  Jal,
  input  Jalr,
  input  MemToReg,
  input  MemWrite,
  input  RegWrite,
  input  Halt,
  input  URET,
  input  SLTIU,
  input  SH,
  input  ALU,
  input  [4:0] rd,
  input  [31:0] result,
  input  [31:0] WriteData,
  input  [31:0] IR,
  input  [31:0] PC,
  input  [31:0] PC_4,
  input  reset,
  input  en,
  input  clk,
  output Jal_2,
  output Jalr_2,
  output MemToReg_2,
  output MemWrite_2,
  output RegWrite_2,
  output Halt_2,
  output URET_2,
  output SLTIU_2,
  output SH_2,
  output ALU_2,
  output [4:0] rd_2,
  output [31:0] result_2,
  output [31:0] Writedata_2,
  output [31:0] IR_2,
  output [31:0] PC_2,
  output [31:0] PC_4_2
);

  wire multiplexer_1_out, multiplexer_2_out, multiplexer_3_out, multiplexer_4_out, multiplexer_5_out,
       multiplexer_6_out, multiplexer_7_out, multiplexer_8_out, multiplexer_9_out, multiplexer_10_out;
  wire [4:0] multiplexer_11_out;
  wire [31:0] multiplexer_12_out, multiplexer_13_out, multiplexer_14_out, multiplexer_15_out,
       multiplexer_16_out;

  Multiplexer #(.select(1), .width(1), .disabled("Z"), .enable("false")) multiplexer_1 (
    .in0(Jal), .in1(1'b0), .out(multiplexer_1_out), .sel(reset));
  Multiplexer #(.select(1), .width(1), .disabled("Z"), .enable("false")) multiplexer_2 (
    .in0(Jalr), .in1(1'b0), .out(multiplexer_2_out), .sel(reset));
  Multiplexer #(.select(1), .width(1), .disabled("Z"), .enable("false")) multiplexer_3 (
    .in0(MemToReg), .out(multiplexer_3_out), .sel(reset));  // open: in1
  Multiplexer #(.select(1), .width(1), .disabled("Z"), .enable("false")) multiplexer_4 (
    .in0(MemWrite), .in1(1'b0), .out(multiplexer_4_out), .sel(reset));
  Multiplexer #(.select(1), .width(1), .disabled("Z"), .enable("false")) multiplexer_5 (
    .in0(RegWrite), .in1(1'b0), .out(multiplexer_5_out), .sel(reset));
  Multiplexer #(.select(1), .width(1), .disabled("Z"), .enable("false")) multiplexer_6 (
    .in0(Halt), .in1(1'b0), .out(multiplexer_6_out), .sel(reset));
  Multiplexer #(.select(1), .width(1), .disabled("Z"), .enable("false")) multiplexer_7 (
    .in0(URET), .in1(1'b0), .out(multiplexer_7_out), .sel(reset));
  Multiplexer #(.select(1), .width(1), .disabled("Z"), .enable("false")) multiplexer_8 (
    .in0(SLTIU), .in1(1'b0), .out(multiplexer_8_out), .sel(reset));
  Multiplexer #(.select(1), .width(1), .disabled("Z"), .enable("false")) multiplexer_9 (
    .in0(SH), .in1(1'b0), .out(multiplexer_9_out), .sel(reset));
  Multiplexer #(.select(1), .width(1), .disabled("Z"), .enable("false")) multiplexer_10 (
    .in0(ALU), .in1(1'b0), .out(multiplexer_10_out), .sel(reset));
  Multiplexer #(.select(1), .width(5), .disabled("Z"), .enable("false")) multiplexer_11 (
    .in0(rd), .in1({5{1'b0}}), .out(multiplexer_11_out), .sel(reset));
  Multiplexer #(.select(1), .width(32), .disabled("Z"), .enable("false")) multiplexer_12 (
    .in0(result), .in1({32{1'b0}}), .out(multiplexer_12_out), .sel(reset));
  Multiplexer #(.select(1), .width(32), .disabled("Z"), .enable("false")) multiplexer_13 (
    .in0(WriteData), .in1({32{1'b0}}), .out(multiplexer_13_out), .sel(reset));
  Multiplexer #(.select(1), .width(32), .disabled("Z"), .enable("false")) multiplexer_14 (
    .in0(IR), .in1({32{1'b0}}), .out(multiplexer_14_out), .sel(reset));
  Multiplexer #(.select(1), .width(32), .disabled("Z"), .enable("false")) multiplexer_15 (
    .in0(PC), .in1({32{1'b0}}), .out(multiplexer_15_out), .sel(reset));
  Multiplexer #(.select(1), .width(32), .disabled("Z"), .enable("false")) multiplexer_16 (
    .in0(PC_4), .in1({32{1'b0}}), .out(multiplexer_16_out), .sel(reset));
  Register #(.width(1), .trigger("rising"), .Select("low")) register_1 (
    .D(multiplexer_1_out), .en(en), .Q(Jal_2), .clk(clk));  // open: clr
  Register #(.width(1), .trigger("rising"), .Select("low")) register_2 (
    .D(multiplexer_2_out), .en(en), .Q(Jalr_2), .clk(clk));  // open: clr
  Register #(.width(1), .trigger("rising"), .Select("low")) register_3 (
    .D(multiplexer_3_out), .en(en), .Q(MemToReg_2), .clk(clk));  // open: clr
  Register #(.width(1), .trigger("rising"), .Select("low")) register_4 (
    .D(multiplexer_4_out), .en(en), .Q(MemWrite_2), .clk(clk));  // open: clr
  Register #(.width(1), .trigger("rising"), .Select("low")) register_5 (
    .D(multiplexer_5_out), .en(en), .Q(RegWrite_2), .clk(clk));  // open: clr
  Register #(.width(1), .trigger("rising"), .Select("low")) register_6 (
    .D(multiplexer_6_out), .en(en), .Q(Halt_2), .clk(clk));  // open: clr
  Register #(.width(1), .trigger("rising"), .Select("low")) register_7 (
    .D(multiplexer_7_out), .en(en), .Q(URET_2), .clk(clk));  // open: clr
  Register #(.width(1), .trigger("rising"), .Select("low")) register_8 (
    .D(multiplexer_8_out), .en(en), .Q(SLTIU_2), .clk(clk));  // open: clr
  Register #(.width(1), .trigger("rising"), .Select("low")) register_9 (
    .D(multiplexer_9_out), .en(en), .Q(SH_2), .clk(clk));  // open: clr
  Register #(.width(1), .trigger("rising"), .Select("low")) register_10 (
    .D(multiplexer_10_out), .en(en), .Q(ALU_2), .clk(clk));  // open: clr
  Register #(.width(5), .trigger("rising"), .Select("low")) register_11 (
    .D(multiplexer_11_out), .en(en), .Q(rd_2), .clk(clk));  // open: clr
  Register #(.width(32), .trigger("rising"), .Select("low")) register_12 (
    .D(multiplexer_12_out), .en(en), .Q(result_2), .clk(clk));  // open: clr
  Register #(.width(32), .trigger("rising"), .Select("low")) register_13 (
    .D(multiplexer_13_out), .en(en), .Q(Writedata_2), .clk(clk));  // open: clr
  Register #(.width(32), .trigger("rising"), .Select("low")) register_14 (
    .D(multiplexer_14_out), .en(en), .Q(IR_2), .clk(clk));  // open: clr
  Register #(.width(32), .trigger("rising"), .Select("low")) register_15 (
    .D(multiplexer_15_out), .en(en), .Q(PC_2), .clk(clk));  // open: clr
  Register #(.width(32), .trigger("rising"), .Select("low")) register_16 (
    .D(multiplexer_16_out), .en(en), .Q(PC_4_2), .clk(clk));  // open: clr
endmodule

module MEM_WB (
  input  URET,
  input  SLTIU,
  input  SH,
  input  ALU,
  input  Jal,
  input  Jalr,
  input  MemToReg,
  input  RegWrite,
  input  Halt,
  input  [4:0] rd,
  input  [31:0] AluResult,
  input  [31:0] ReadData,
  input  [31:0] IR,
  input  [31:0] PC,
  input  [31:0] PC_4,
  input  reset,
  input  en,
  input  clk,
  output URET_2,
  output SLTIU_2,
  output SH_2,
  output ALU_2,
  output Jal_2,
  output Jalr_2,
  output MemToReg_2,
  output RegWrite_2,
  output Halt_2,
  output [4:0] rd_2,
  output [31:0] AluResult_2,
  output [31:0] Readdata_2,
  output [31:0] IR_2,
  output [31:0] PC_2,
  output [31:0] PC_4_2
);

  wire multiplexer_1_out, multiplexer_2_out, multiplexer_3_out, multiplexer_4_out, multiplexer_5_out,
       multiplexer_6_out, multiplexer_7_out, multiplexer_8_out, multiplexer_9_out;
  wire [4:0] multiplexer_10_out;
  wire [31:0] multiplexer_11_out, multiplexer_12_out, multiplexer_13_out, multiplexer_14_out,
       multiplexer_15_out;

  Multiplexer #(.select(1), .width(1), .disabled("Z"), .enable("false")) multiplexer_1 (
    .in0(URET), .in1(1'b0), .out(multiplexer_1_out), .sel(reset));
  Multiplexer #(.select(1), .width(1), .disabled("Z"), .enable("false")) multiplexer_2 (
    .in0(SLTIU), .in1(1'b0), .out(multiplexer_2_out), .sel(reset));
  Multiplexer #(.select(1), .width(1), .disabled("Z"), .enable("false")) multiplexer_3 (
    .in0(SH), .in1(1'b0), .out(multiplexer_3_out), .sel(reset));
  Multiplexer #(.select(1), .width(1), .disabled("Z"), .enable("false")) multiplexer_4 (
    .in0(ALU), .in1(1'b0), .out(multiplexer_4_out), .sel(reset));
  Multiplexer #(.select(1), .width(1), .disabled("Z"), .enable("false")) multiplexer_5 (
    .in0(Jal), .in1(1'b0), .out(multiplexer_5_out), .sel(reset));
  Multiplexer #(.select(1), .width(1), .disabled("Z"), .enable("false")) multiplexer_6 (
    .in0(Jalr), .in1(1'b0), .out(multiplexer_6_out), .sel(reset));
  Multiplexer #(.select(1), .width(1), .disabled("Z"), .enable("false")) multiplexer_7 (
    .in0(MemToReg), .in1(1'b0), .out(multiplexer_7_out), .sel(reset));
  Multiplexer #(.select(1), .width(1), .disabled("Z"), .enable("false")) multiplexer_8 (
    .in0(RegWrite), .in1(1'b0), .out(multiplexer_8_out), .sel(reset));
  Multiplexer #(.select(1), .width(1), .disabled("Z"), .enable("false")) multiplexer_9 (
    .in0(Halt), .in1(1'b0), .out(multiplexer_9_out), .sel(reset));
  Multiplexer #(.select(1), .width(5), .disabled("Z"), .enable("false")) multiplexer_10 (
    .in0(rd), .in1({5{1'b0}}), .out(multiplexer_10_out), .sel(reset));
  Multiplexer #(.select(1), .width(32), .disabled("Z"), .enable("false")) multiplexer_11 (
    .in0(AluResult), .in1({32{1'b0}}), .out(multiplexer_11_out), .sel(reset));
  Multiplexer #(.select(1), .width(32), .disabled("Z"), .enable("false")) multiplexer_12 (
    .in0(ReadData), .in1({32{1'b0}}), .out(multiplexer_12_out), .sel(reset));
  Multiplexer #(.select(1), .width(32), .disabled("Z"), .enable("false")) multiplexer_13 (
    .in0(IR), .in1({32{1'b0}}), .out(multiplexer_13_out), .sel(reset));
  Multiplexer #(.select(1), .width(32), .disabled("Z"), .enable("false")) multiplexer_14 (
    .in0(PC), .in1({32{1'b0}}), .out(multiplexer_14_out), .sel(reset));
  Multiplexer #(.select(1), .width(32), .disabled("Z"), .enable("false")) multiplexer_15 (
    .in0(PC_4), .in1({32{1'b0}}), .out(multiplexer_15_out), .sel(reset));
  Register #(.width(1), .trigger("rising"), .Select("low")) register_1 (
    .D(multiplexer_1_out), .en(en), .Q(URET_2), .clk(clk));  // open: clr
  Register #(.width(1), .trigger("rising"), .Select("low")) register_2 (
    .D(multiplexer_2_out), .en(en), .Q(SLTIU_2), .clk(clk));  // open: clr
  Register #(.width(1), .trigger("rising"), .Select("low")) register_3 (
    .D(multiplexer_3_out), .en(en), .Q(SH_2), .clk(clk));  // open: clr
  Register #(.width(1), .trigger("rising"), .Select("low")) register_4 (
    .D(multiplexer_4_out), .en(en), .Q(ALU_2), .clk(clk));  // open: clr
  Register #(.width(1), .trigger("rising"), .Select("low")) register_5 (
    .D(multiplexer_5_out), .en(en), .Q(Jal_2), .clk(clk));  // open: clr
  Register #(.width(1), .trigger("rising"), .Select("low")) register_6 (
    .D(multiplexer_6_out), .en(en), .Q(Jalr_2), .clk(clk));  // open: clr
  Register #(.width(1), .trigger("rising"), .Select("low")) register_7 (
    .D(multiplexer_7_out), .en(en), .Q(MemToReg_2), .clk(clk));  // open: clr
  Register #(.width(1), .trigger("rising"), .Select("low")) register_8 (
    .D(multiplexer_8_out), .en(en), .Q(RegWrite_2), .clk(clk));  // open: clr
  Register #(.width(1), .trigger("rising"), .Select("low")) register_9 (
    .D(multiplexer_9_out), .en(en), .Q(Halt_2), .clk(clk));  // open: clr
  Register #(.width(5), .trigger("rising"), .Select("low")) register_10 (
    .D(multiplexer_10_out), .en(en), .Q(rd_2), .clk(clk));  // open: clr
  Register #(.width(32), .trigger("rising"), .Select("low")) register_11 (
    .D(multiplexer_11_out), .en(en), .Q(AluResult_2), .clk(clk));  // open: clr
  Register #(.width(32), .trigger("rising"), .Select("low")) register_12 (
    .D(multiplexer_12_out), .en(en), .Q(Readdata_2), .clk(clk));  // open: clr
  Register #(.width(32), .trigger("rising"), .Select("low")) register_13 (
    .D(multiplexer_13_out), .en(en), .Q(IR_2), .clk(clk));  // open: clr
  Register #(.width(32), .trigger("rising"), .Select("low")) register_14 (
    .D(multiplexer_14_out), .en(en), .Q(PC_2), .clk(clk));  // open: clr
  Register #(.width(32), .trigger("rising"), .Select("low")) register_15 (
    .D(multiplexer_15_out), .en(en), .Q(PC_4_2), .clk(clk));  // open: clr
endmodule

module \气泡处理逻辑  (
  input  BranchTaken,
  input  [31:0] IR,
  input  ecall,
  input  rs1_used,
  input  EX_RegWrite,
  input  rs2_used,
  input  MEM_RegWrite,
  input  [4:0] EX_rd,
  input  [4:0] MEM_rd,
  output stall,
  output flush
);

  wire and_1_out, and_2_out, and_3_out, and_4_out, and_5_out, and_6_out, and_7_out, and_8_out, and_9_out,
       and_10_out, and_11_out, and_12_out, and_13_out, and_14_out, and_15_out, and_16_out, comparator_1_eq,
       comparator_2_eq, comparator_3_eq, comparator_4_eq, comparator_5_eq, comparator_6_eq, comparator_7_eq,
       comparator_8_eq, comparator_9_eq, comparator_10_eq, comparator_11_eq, comparator_12_eq, not_1_out,
       not_2_out, not_3_out, not_4_out, or_1_out, or_2_out;

  Comparator #(.width(5), .mode("twosComplement")) comparator_1 (
    .a({5{1'b0}}), .b(IR[19:15]), .eq(comparator_1_eq));  // open: gt, lt
  Comparator #(.width(5), .mode("twosComplement")) comparator_2 (
    .a(IR[19:15]), .b(EX_rd), .eq(comparator_2_eq));  // open: gt, lt
  Comparator #(.width(5), .mode("twosComplement")) comparator_3 (
    .a({5{1'b0}}), .b(IR[24:20]), .eq(comparator_3_eq));  // open: gt, lt
  Comparator #(.width(5), .mode("twosComplement")) comparator_4 (
    .a(IR[24:20]), .b(EX_rd), .eq(comparator_4_eq));  // open: gt, lt
  Comparator #(.width(5), .mode("twosComplement")) comparator_5 (
    .a({5{1'b0}}), .b(IR[19:15]), .eq(comparator_5_eq));  // open: gt, lt
  Comparator #(.width(5), .mode("twosComplement")) comparator_6 (
    .a(IR[19:15]), .b(MEM_rd), .eq(comparator_6_eq));  // open: gt, lt
  Comparator #(.width(5), .mode("twosComplement")) comparator_7 (
    .a({5{1'b0}}), .b(IR[24:20]), .eq(comparator_7_eq));  // open: gt, lt
  Comparator #(.width(5), .mode("twosComplement")) comparator_8 (
    .a(IR[24:20]), .b(MEM_rd), .eq(comparator_8_eq));  // open: gt, lt
  not not_1 (not_1_out, comparator_1_eq);
  and and_1 (and_1_out, comparator_2_eq, EX_RegWrite);
  not not_2 (not_2_out, comparator_3_eq);
  and and_2 (and_2_out, comparator_4_eq, EX_RegWrite);
  not not_3 (not_3_out, comparator_5_eq);
  and and_3 (and_3_out, comparator_6_eq, MEM_RegWrite);
  not not_4 (not_4_out, comparator_7_eq);
  and and_4 (and_4_out, comparator_8_eq, MEM_RegWrite);
  and and_5 (and_5_out, ecall, EX_RegWrite);
  Comparator #(.width(5), .mode("twosComplement")) comparator_9 (
    .a(5'b10001), .b(EX_rd), .eq(comparator_9_eq));  // open: gt, lt
  or or_1 (or_1_out, comparator_9_eq, comparator_10_eq);
  Comparator #(.width(5), .mode("twosComplement")) comparator_10 (
    .a(EX_rd), .b(5'b01010), .eq(comparator_10_eq));  // open: gt, lt
  and and_6 (and_6_out, ecall, MEM_RegWrite);
  Comparator #(.width(5), .mode("twosComplement")) comparator_11 (
    .a(5'b10001), .b(MEM_rd), .eq(comparator_11_eq));  // open: gt, lt
  or or_2 (or_2_out, comparator_11_eq, comparator_12_eq);
  Comparator #(.width(5), .mode("twosComplement")) comparator_12 (
    .a(MEM_rd), .b(5'b01010), .eq(comparator_12_eq));  // open: gt, lt
  and and_7 (and_7_out, not_1_out, and_1_out);
  and and_8 (and_8_out, not_2_out, and_2_out);
  and and_9 (and_9_out, not_3_out, and_3_out);
  and and_10 (and_10_out, not_4_out, and_4_out);
  and and_11 (and_11_out, and_7_out, rs1_used);
  and and_12 (and_12_out, and_8_out, rs2_used);
  and and_13 (and_13_out, and_9_out, rs1_used);
  and and_14 (and_14_out, and_10_out, rs2_used);
  and and_15 (and_15_out, and_5_out, or_1_out);
  and and_16 (and_16_out, and_6_out, or_2_out);
  or or_3 (stall, and_11_out, and_12_out, and_13_out, and_14_out, and_15_out, and_16_out);
  or or_4 (flush, stall, BranchTaken);

  // Other names for the same wires on the sheet: Data_hazzard = stall; rs1[4:0] = IR[19:15]; rs2[4:0] = IR[24:20]
endmodule

module \重定向处理逻辑  (
  input  [31:0] IR,
  input  BranchTaken,
  input  EX_MemToReg,
  input  ecall,
  input  rs1_used,
  input  EX_RegWrite,
  input  rs2_used,
  input  MEM_RegWrite,
  input  [4:0] EX_rd,
  input  [4:0] MEM_rd,
  output stall,
  output flush,
  output [1:0] rs1_Forward,
  output [1:0] rs2_Forward
);

  wire and_1_out, and_2_out, and_3_out, and_4_out, and_5_out, and_6_out, and_7_out, and_8_out, and_9_out,
       and_10_out, and_11_out, and_12_out, and_13_out, and_14_out, and_15_out, and_16_out, and_17_out,
       and_18_out, and_21_out, and_22_out, and_23_out, and_24_out, comparator_1_eq, comparator_2_eq,
       comparator_3_eq, comparator_4_eq, comparator_5_eq, comparator_6_eq, comparator_7_eq, comparator_8_eq,
       comparator_9_eq, comparator_10_eq, comparator_11_eq, comparator_12_eq, comparator_13_eq,
       comparator_14_eq, comparator_15_eq, comparator_16_eq, ecall1, ecall2, ecall3, ecall4, or_3_out,
       or_5_out;

  Comparator #(.width(5), .mode("twosComplement")) comparator_1 (
    .a({5{1'b0}}), .b(IR[19:15]), .eq(comparator_1_eq));  // open: gt, lt
  Comparator #(.width(5), .mode("twosComplement")) comparator_2 (
    .a(IR[19:15]), .b(EX_rd), .eq(comparator_2_eq));  // open: gt, lt
  Comparator #(.width(5), .mode("twosComplement")) comparator_3 (
    .a(EX_rd), .b(IR[24:20]), .eq(comparator_3_eq));  // open: gt, lt
  Comparator #(.width(5), .mode("twosComplement")) comparator_4 (
    .a(IR[24:20]), .b({5{1'b0}}), .eq(comparator_4_eq));  // open: gt, lt
  Comparator #(.width(5), .mode("twosComplement")) comparator_5 (
    .a({5{1'b0}}), .b(IR[19:15]), .eq(comparator_5_eq));  // open: gt, lt
  Comparator #(.width(5), .mode("twosComplement")) comparator_6 (
    .a(IR[19:15]), .b(EX_rd), .eq(comparator_6_eq));  // open: gt, lt
  Comparator #(.width(5), .mode("twosComplement")) comparator_7 (
    .a(MEM_rd), .b(IR[19:15]), .eq(comparator_7_eq));  // open: gt, lt
  Comparator #(.width(5), .mode("twosComplement")) comparator_8 (
    .a(IR[19:15]), .b({5{1'b0}}), .eq(comparator_8_eq));  // open: gt, lt
  Comparator #(.width(5), .mode("twosComplement")) comparator_9 (
    .a({5{1'b0}}), .b(IR[24:20]), .eq(comparator_9_eq));  // open: gt, lt
  Comparator #(.width(5), .mode("twosComplement")) comparator_10 (
    .a(IR[24:20]), .b(EX_rd), .eq(comparator_10_eq));  // open: gt, lt
  Comparator #(.width(5), .mode("twosComplement")) comparator_11 (
    .a(MEM_rd), .b(IR[24:20]), .eq(comparator_11_eq));  // open: gt, lt
  Comparator #(.width(5), .mode("twosComplement")) comparator_12 (
    .a(IR[24:20]), .b({5{1'b0}}), .eq(comparator_12_eq));  // open: gt, lt
  and and_1 (and_1_out, rs1_used, ~comparator_1_eq);  // AND_Gate
  and and_2 (and_2_out, ~comparator_4_eq, rs2_used);  // AND_Gate
  and and_3 (and_3_out, rs1_used, ~comparator_5_eq);  // AND_Gate
  and and_4 (and_4_out, ~comparator_8_eq, rs1_used);  // AND_Gate
  and and_5 (and_5_out, rs2_used, ~comparator_9_eq);  // AND_Gate
  and and_6 (and_6_out, ~comparator_12_eq, rs2_used);  // AND_Gate
  and and_7 (and_7_out, and_1_out, EX_MemToReg);
  and and_8 (and_8_out, EX_MemToReg, and_2_out);
  and and_9 (and_9_out, and_7_out, comparator_2_eq);
  and and_10 (and_10_out, comparator_3_eq, and_8_out);
  and and_11 (and_11_out, and_3_out, EX_RegWrite);
  and and_12 (and_12_out, MEM_RegWrite, and_4_out);
  and and_13 (and_13_out, and_5_out, EX_RegWrite);
  and and_14 (and_14_out, MEM_RegWrite, and_6_out);
  or or_1 (stall, and_9_out, and_10_out);
  and and_15 (and_15_out, and_11_out, comparator_6_eq);
  and and_16 (and_16_out, comparator_7_eq, and_12_out);
  and and_17 (and_17_out, and_13_out, comparator_10_eq);
  and and_18 (and_18_out, comparator_11_eq, and_14_out);
  or or_2 (rs1_Forward[1], and_15_out, ecall1);
  or or_3 (or_3_out, ecall2, and_16_out);
  or or_4 (rs2_Forward[1], and_17_out, ecall3);
  or or_5 (or_5_out, ecall4, and_18_out);
  and and_19 (rs1_Forward[0], ~rs1_Forward[1], or_3_out);  // AND_Gate
  and and_20 (rs2_Forward[0], ~rs2_Forward[1], or_5_out);  // AND_Gate
  or or_6 (flush, stall, BranchTaken);
  and and_21 (and_21_out, EX_RegWrite, ecall);
  and and_22 (and_22_out, MEM_RegWrite, ecall);
  and and_23 (and_23_out, EX_RegWrite, ecall);
  and and_24 (and_24_out, MEM_RegWrite, ecall);
  Comparator #(.width(5), .mode("twosComplement")) comparator_13 (
    .a(EX_rd), .b(5'b10001), .eq(comparator_13_eq));  // open: gt, lt
  Comparator #(.width(5), .mode("twosComplement")) comparator_14 (
    .a(MEM_rd), .b(5'b10001), .eq(comparator_14_eq));  // open: gt, lt
  Comparator #(.width(5), .mode("twosComplement")) comparator_15 (
    .a(EX_rd), .b(5'b01010), .eq(comparator_15_eq));  // open: gt, lt
  Comparator #(.width(5), .mode("twosComplement")) comparator_16 (
    .a(MEM_rd), .b(5'b01010), .eq(comparator_16_eq));  // open: gt, lt
  and and_25 (ecall1, and_21_out, comparator_13_eq);
  and and_26 (ecall2, and_22_out, comparator_14_eq);
  and and_27 (ecall3, and_23_out, comparator_15_eq);
  and and_28 (ecall4, and_24_out, comparator_16_eq);

  // Other names for the same wires on the sheet: rs1[4:0] = IR[19:15]; rs2[4:0] = IR[24:20]; loadused = stall
endmodule

module MAX (
  input  [15:0] Y,
  input  [15:0] X,
  input  [2:0] Y_num,
  input  [2:0] X_num,
  output [15:0] MAX,
  output [2:0] Max_num
);

  wire comparator_1_eq, comparator_1_gt, or_1_out;

  Comparator #(.width(16), .mode("unsigned")) comparator_1 (
    .a(X), .b(Y), .gt(comparator_1_gt), .eq(comparator_1_eq));  // open: lt
  Multiplexer #(.select(1), .width(16), .disabled("Z"), .enable("false")) multiplexer_1 (
    .in0(Y), .in1(X), .out(MAX), .sel(or_1_out));
  or or_1 (or_1_out, comparator_1_gt, comparator_1_eq);
  Multiplexer #(.select(1), .width(3), .disabled("Z"), .enable("false")) multiplexer_2 (
    .in0(Y_num), .in1(X_num), .out(Max_num), .sel(or_1_out));

  // Notes on the sheet:
  //   输出两个输入中的较大值，并输出较大值的3位编号
endmodule

module FSM (
  input  high,
  input  low,
  input  jump,
  output NextHigh,
  output NextLow
);

  wire and_1_out, and_2_out, and_3_out, and_4_out, not_1_out, not_2_out, not_3_out, not_4_out, not_5_out;

  not not_1 (not_1_out, low);
  not not_2 (not_2_out, high);
  not not_3 (not_3_out, low);
  not not_4 (not_4_out, low);
  not not_5 (not_5_out, jump);
  and and_1 (and_1_out, low, jump);
  and and_2 (and_2_out, high, not_1_out);
  and and_3 (and_3_out, not_2_out, not_3_out, jump);
  and and_4 (and_4_out, high, not_4_out, not_5_out);
  or or_1 (NextHigh, and_1_out, and_2_out);
  or or_2 (NextLow, and_3_out, and_4_out);
endmodule
module BTB (
  input  [31:0] PC,
  input  [31:0] EX_PC,
  input  [31:0] EX_BranchAddr,
  input  EX_Branch,
  input  EX_Branched,
  input  in_6,
  output IF_PredictJump,
  output [31:0] BTB_JumpAddr
);

  wire and_17_out, and_26_out, and_27_out, and_28_out, and_29_out, and_30_out, and_31_out, and_32_out,
       and_33_out, comparator_1_eq, comparator_2_eq, comparator_3_eq, comparator_4_eq, comparator_5_eq,
       comparator_6_eq, comparator_7_eq, comparator_8_eq, comparator_9_eq, comparator_10_eq,
       comparator_11_eq, comparator_12_eq, comparator_13_eq, comparator_14_eq, comparator_15_eq,
       comparator_16_eq, d_ff_1_q, d_ff_2_q, d_ff_3_q, d_ff_4_q, d_ff_5_q, d_ff_6_q, d_ff_7_q, d_ff_8_q,
       decoder_1_out0, decoder_1_out1, decoder_1_out2, decoder_1_out3, decoder_1_out4, decoder_1_out5,
       decoder_1_out6, decoder_1_out7, decoder_2_out0, decoder_2_out1, decoder_2_out2, decoder_2_out3,
       decoder_2_out4, decoder_2_out5, decoder_2_out6, decoder_2_out7, EX_Hit, EX_Miss, L0, L1, L2, L3, L4,
       L5, L6, L7, M0, M1, M2, M3, M4, M5, M6, M7, not_1_out, not_2_out, not_3_out, not_4_out, not_5_out,
       not_6_out, not_7_out, not_8_out, or_1_out, or_2_out, or_3_out, or_4_out, or_5_out, or_6_out, or_7_out,
       or_8_out, or_10_out, or_11_out, or_12_out, or_13_out, or_14_out, or_15_out, or_16_out, or_17_out,
       priority_encoder_1_gs, v0, v1, v2, v3, v4, v5, v6, v7, write0, write1, write2, write3, write4, write5,
       write6, write7;
  wire [0:0] controlled_buffer_9_out, controlled_buffer_10_out, controlled_buffer_11_out,
       controlled_buffer_12_out, controlled_buffer_13_out, controlled_buffer_14_out,
       controlled_buffer_15_out, controlled_buffer_16_out;
  wire [1:0] fsm_1_nextlow, fsm_2_nextlow, fsm_3_nextlow, fsm_4_nextlow, fsm_5_nextlow, fsm_6_nextlow,
       fsm_7_nextlow, fsm_8_nextlow, predict0, predict1, predict2, predict3, predict4, predict5, predict6,
       predict7;
  wire [2:0] max_1_max_num, max_2_max_num, max_3_max_num, max_4_max_num, max_5_max_num, max_6_max_num,
       max_7_max_num, priority_encoder_1_out;
  wire [15:0] c0, c1, c2, c3, c4, c5, c6, c7, max_1_max, max_2_max, max_3_max, max_4_max, max_5_max,
       max_6_max;
  wire [31:0] register_17_q, register_18_q, register_19_q, register_20_q, register_21_q, register_22_q,
       register_23_q, register_24_q, tag0, tag1, tag2, tag3, tag4, tag5, tag6, tag7;

  LED #(.active("true")) led_1 (.in(v0));
  Register #(.width(1), .trigger("rising"), .Select("low")) register_1 (
    .D(1'b1), .en(write0), .Q(v0), .clk(in_6));  // open: clr
  LED #(.active("true")) led_2 (.in(v1));
  Register #(.width(1), .trigger("rising"), .Select("low")) register_2 (
    .D(1'b1), .en(write1), .Q(v1), .clk(in_6));  // open: clr
  LED #(.active("true")) led_3 (.in(v2));
  Register #(.width(1), .trigger("rising"), .Select("low")) register_3 (
    .D(1'b1), .en(write2), .Q(v2), .clk(in_6));  // open: clr
  LED #(.active("true")) led_4 (.in(v3));
  Register #(.width(1), .trigger("rising"), .Select("low")) register_4 (
    .D(1'b1), .en(write3), .Q(v3), .clk(in_6));  // open: clr
  LED #(.active("true")) led_5 (.in(v4));
  Register #(.width(1), .trigger("rising"), .Select("low")) register_5 (
    .D(1'b1), .en(write4), .Q(v4), .clk(in_6));  // open: clr
  LED #(.active("true")) led_6 (.in(v5));
  Register #(.width(1), .trigger("rising"), .Select("low")) register_6 (
    .D(1'b1), .en(write5), .Q(v5), .clk(in_6));  // open: clr
  LED #(.active("true")) led_7 (.in(v6));
  Register #(.width(1), .trigger("rising"), .Select("low")) register_7 (
    .D(1'b1), .en(write6), .Q(v6), .clk(in_6));  // open: clr
  Register #(.width(1), .trigger("rising"), .Select("low")) register_8 (
    .D(1'b1), .en(write7), .Q(v7), .clk(in_6));  // open: clr
  LED #(.active("true")) led_8 (.in(v7));
  // Probe on tag0
  Register #(.width(32), .trigger("rising"), .Select("low")) register_9 (
    .D(EX_PC), .en(write0), .Q(tag0), .clk(in_6));  // open: clr
  // Probe on tag1
  Register #(.width(32), .trigger("rising"), .Select("low")) register_10 (
    .D(EX_PC), .en(write1), .Q(tag1), .clk(in_6));  // open: clr
  // Probe on tag2
  Register #(.width(32), .trigger("rising"), .Select("low")) register_11 (
    .D(EX_PC), .en(write2), .Q(tag2), .clk(in_6));  // open: clr
  // Probe on tag3
  Register #(.width(32), .trigger("rising"), .Select("low")) register_12 (
    .D(EX_PC), .en(write3), .Q(tag3), .clk(in_6));  // open: clr
  // Probe on tag4
  Register #(.width(32), .trigger("rising"), .Select("low")) register_13 (
    .D(EX_PC), .en(write4), .Q(tag4), .clk(in_6));  // open: clr
  // Probe on tag5
  Register #(.width(32), .trigger("rising"), .Select("low")) register_14 (
    .D(EX_PC), .en(write5), .Q(tag5), .clk(in_6));  // open: clr
  Register #(.width(32), .trigger("rising"), .Select("low")) register_15 (
    .D(EX_PC), .en(write6), .Q(tag6), .clk(in_6));  // open: clr
  // Probe on tag7
  Register #(.width(32), .trigger("rising"), .Select("low")) register_16 (
    .D(EX_PC), .en(write7), .Q(tag7), .clk(in_6));  // open: clr
  // Probe on tag6
  Counter #(.width(16), .max('hffff), .ongoal("wrap"), .trigger("rising"), .behavior("new")) counter_1 (
    .Q(c0), .clk(in_6), .clr(d_ff_3_q));  // open: load, D, count, carry, preset, down
  or or_1 (or_1_out, write0, L0);
  Counter #(.width(16), .max('hffff), .ongoal("wrap"), .trigger("rising"), .behavior("new")) counter_2 (
    .Q(c1), .clk(in_6), .clr(d_ff_4_q));  // open: load, D, count, carry, preset, down
  or or_2 (or_2_out, write1, L1);
  Counter #(.width(16), .max('hffff), .ongoal("wrap"), .trigger("rising"), .behavior("new")) counter_3 (
    .Q(c2), .clk(in_6), .clr(d_ff_5_q));  // open: load, D, count, carry, preset, down
  or or_3 (or_3_out, write2, L2);
  Counter #(.width(16), .max('hffff), .ongoal("wrap"), .trigger("rising"), .behavior("new")) counter_4 (
    .Q(c3), .clk(in_6), .clr(d_ff_6_q));  // open: load, D, count, carry, preset, down
  or or_4 (or_4_out, write3, L3);
  Counter #(.width(16), .max('hffff), .ongoal("wrap"), .trigger("rising"), .behavior("new")) counter_5 (
    .Q(c4), .clk(in_6), .clr(d_ff_1_q));  // open: load, D, count, carry, preset, down
  D_Flip_Flop #(.trigger("rising"), .Pre_Clr_Positions("ABOVE_BELOW"), .NegatePresetClear("false"), .enable("false"), .NewFFLayout("false")) d_ff_1 (
    .clk(in_6), .D(or_5_out), .Q(d_ff_1_q));  // open: Qn, preset, reset
  or or_5 (or_5_out, write4, L4);
  Counter #(.width(16), .max('hffff), .ongoal("wrap"), .trigger("rising"), .behavior("new")) counter_6 (
    .Q(c5), .clk(in_6), .clr(d_ff_7_q));  // open: load, D, count, carry, preset, down
  or or_6 (or_6_out, write5, L5);
  Counter #(.width(16), .max('hffff), .ongoal("wrap"), .trigger("rising"), .behavior("new")) counter_7 (
    .Q(c6), .clk(in_6), .clr(d_ff_8_q));  // open: load, D, count, carry, preset, down
  or or_7 (or_7_out, write6, L6);
  Counter #(.width(16), .max('hffff), .ongoal("wrap"), .trigger("rising"), .behavior("new")) counter_8 (
    .Q(c7), .clk(in_6), .clr(d_ff_2_q));  // open: load, D, count, carry, preset, down
  D_Flip_Flop #(.trigger("rising"), .Pre_Clr_Positions("LEGACY"), .NegatePresetClear("false"), .enable("true"), .NewFFLayout("false")) d_ff_2 (
    .clk(in_6), .D(or_8_out), .Q(d_ff_2_q));  // open: Qn, preset, en, reset
  or or_8 (or_8_out, write7, L7);
  D_Flip_Flop #(.trigger("rising"), .Pre_Clr_Positions("ABOVE_BELOW"), .NegatePresetClear("false"), .enable("false"), .NewFFLayout("false")) d_ff_3 (
    .clk(in_6), .D(or_1_out), .Q(d_ff_3_q));  // open: Qn, preset, reset
  D_Flip_Flop #(.trigger("rising"), .Pre_Clr_Positions("ABOVE_BELOW"), .NegatePresetClear("false"), .enable("false"), .NewFFLayout("false")) d_ff_4 (
    .clk(in_6), .D(or_2_out), .Q(d_ff_4_q));  // open: Qn, preset, reset
  D_Flip_Flop #(.trigger("rising"), .Pre_Clr_Positions("ABOVE_BELOW"), .NegatePresetClear("false"), .enable("false"), .NewFFLayout("false")) d_ff_5 (
    .clk(in_6), .D(or_3_out), .Q(d_ff_5_q));  // open: Qn, preset, reset
  D_Flip_Flop #(.trigger("rising"), .Pre_Clr_Positions("ABOVE_BELOW"), .NegatePresetClear("false"), .enable("false"), .NewFFLayout("false")) d_ff_6 (
    .clk(in_6), .D(or_4_out), .Q(d_ff_6_q));  // open: Qn, preset, reset
  D_Flip_Flop #(.trigger("rising"), .Pre_Clr_Positions("ABOVE_BELOW"), .NegatePresetClear("false"), .enable("false"), .NewFFLayout("false")) d_ff_7 (
    .clk(in_6), .D(or_6_out), .Q(d_ff_7_q));  // open: Qn, preset, reset
  D_Flip_Flop #(.trigger("rising"), .Pre_Clr_Positions("LEGACY"), .NegatePresetClear("false"), .enable("true"), .NewFFLayout("false")) d_ff_8 (
    .clk(in_6), .D(or_7_out), .Q(d_ff_8_q));  // open: Qn, preset, en, reset
  Register #(.width(32), .trigger("rising"), .Select("low")) register_17 (
    .D(EX_BranchAddr), .en(write0), .Q(register_17_q), .clk(in_6));  // open: clr
  Register #(.width(32), .trigger("rising"), .Select("low")) register_18 (
    .D(EX_BranchAddr), .en(write1), .Q(register_18_q), .clk(in_6));  // open: clr
  Register #(.width(32), .trigger("rising"), .Select("low")) register_19 (
    .D(EX_BranchAddr), .en(write2), .Q(register_19_q), .clk(in_6));  // open: clr
  Register #(.width(32), .trigger("rising"), .Select("low")) register_20 (
    .D(EX_BranchAddr), .en(write3), .Q(register_20_q), .clk(in_6));  // open: clr
  Register #(.width(32), .trigger("rising"), .Select("low")) register_21 (
    .D(EX_BranchAddr), .en(write4), .Q(register_21_q), .clk(in_6));  // open: clr
  Register #(.width(32), .trigger("rising"), .Select("low")) register_22 (
    .D(EX_BranchAddr), .en(write5), .Q(register_22_q), .clk(in_6));  // open: clr
  Register #(.width(32), .trigger("rising"), .Select("low")) register_23 (
    .D(EX_BranchAddr), .en(write6), .Q(register_23_q), .clk(in_6));  // open: clr
  Register #(.width(32), .trigger("rising"), .Select("low")) register_24 (
    .D(EX_BranchAddr), .en(write7), .Q(register_24_q), .clk(in_6));  // open: clr
  assign BTB_JumpAddr = L0 ? register_17_q : 32'bz;  // Controlled_Buffer controlled_buffer_1
  assign BTB_JumpAddr = L1 ? register_18_q : 32'bz;  // Controlled_Buffer controlled_buffer_2
  assign BTB_JumpAddr = L2 ? register_19_q : 32'bz;  // Controlled_Buffer controlled_buffer_3
  assign BTB_JumpAddr = L3 ? register_20_q : 32'bz;  // Controlled_Buffer controlled_buffer_4
  assign BTB_JumpAddr = L4 ? register_21_q : 32'bz;  // Controlled_Buffer controlled_buffer_5
  assign BTB_JumpAddr = L5 ? register_22_q : 32'bz;  // Controlled_Buffer controlled_buffer_6
  assign BTB_JumpAddr = L6 ? register_23_q : 32'bz;  // Controlled_Buffer controlled_buffer_7
  assign BTB_JumpAddr = L7 ? register_24_q : 32'bz;  // Controlled_Buffer controlled_buffer_8
  Comparator #(.width(32), .mode("twosComplement")) comparator_1 (
    .a(tag0), .b(PC), .eq(comparator_1_eq));  // open: gt, lt
  Comparator #(.width(32), .mode("twosComplement")) comparator_2 (
    .a(tag1), .b(PC), .eq(comparator_2_eq));  // open: gt, lt
  Comparator #(.width(32), .mode("twosComplement")) comparator_3 (
    .a(tag2), .b(PC), .eq(comparator_3_eq));  // open: gt, lt
  Comparator #(.width(32), .mode("twosComplement")) comparator_4 (
    .a(tag3), .b(PC), .eq(comparator_4_eq));  // open: gt, lt
  Comparator #(.width(32), .mode("twosComplement")) comparator_5 (
    .a(tag4), .b(PC), .eq(comparator_5_eq));  // open: gt, lt
  Comparator #(.width(32), .mode("twosComplement")) comparator_6 (
    .a(tag5), .b(PC), .eq(comparator_6_eq));  // open: gt, lt
  Comparator #(.width(32), .mode("twosComplement")) comparator_7 (
    .a(tag6), .b(PC), .eq(comparator_7_eq));  // open: gt, lt
  Comparator #(.width(32), .mode("twosComplement")) comparator_8 (
    .a(tag7), .b(PC), .eq(comparator_8_eq));  // open: gt, lt
  and and_1 (L0, v0, comparator_1_eq);
  and and_2 (L1, v1, comparator_2_eq);
  and and_3 (L2, v2, comparator_3_eq);
  and and_4 (L3, v3, comparator_4_eq);
  and and_5 (L4, v4, comparator_5_eq);
  and and_6 (L5, v5, comparator_6_eq);
  and and_7 (L6, v6, comparator_7_eq);
  and and_8 (L7, v7, comparator_8_eq);
  Comparator #(.width(32), .mode("twosComplement")) comparator_9 (
    .a(tag0), .b(EX_PC), .eq(comparator_9_eq));  // open: gt, lt
  Comparator #(.width(32), .mode("twosComplement")) comparator_10 (
    .a(tag1), .b(EX_PC), .eq(comparator_10_eq));  // open: gt, lt
  Comparator #(.width(32), .mode("twosComplement")) comparator_11 (
    .a(tag2), .b(EX_PC), .eq(comparator_11_eq));  // open: gt, lt
  Comparator #(.width(32), .mode("twosComplement")) comparator_12 (
    .a(tag3), .b(EX_PC), .eq(comparator_12_eq));  // open: gt, lt
  Comparator #(.width(32), .mode("twosComplement")) comparator_13 (
    .a(tag4), .b(EX_PC), .eq(comparator_13_eq));  // open: gt, lt
  Comparator #(.width(32), .mode("twosComplement")) comparator_14 (
    .a(tag5), .b(EX_PC), .eq(comparator_14_eq));  // open: gt, lt
  Comparator #(.width(32), .mode("twosComplement")) comparator_15 (
    .a(tag6), .b(EX_PC), .eq(comparator_15_eq));  // open: gt, lt
  Comparator #(.width(32), .mode("twosComplement")) comparator_16 (
    .a(tag7), .b(EX_PC), .eq(comparator_16_eq));  // open: gt, lt
  and and_9 (M0, v0, comparator_9_eq);
  and and_10 (M1, v1, comparator_10_eq);
  and and_11 (M2, v2, comparator_11_eq);
  and and_12 (M3, v3, comparator_12_eq);
  and and_13 (M4, v4, comparator_13_eq);
  and and_14 (M5, v5, comparator_14_eq);
  and and_15 (M6, v6, comparator_15_eq);
  and and_16 (M7, v7, comparator_16_eq);
  not not_1 (not_1_out, v0);
  not not_2 (not_2_out, v1);
  not not_3 (not_3_out, v2);
  not not_4 (not_4_out, v3);
  not not_5 (not_5_out, v4);
  not not_6 (not_6_out, v5);
  not not_7 (not_7_out, v6);
  not not_8 (not_8_out, v7);
  MAX max_1 (.Y(c1), .X(c0), .Y_num(3'b001), .X_num(3'b000), .MAX(max_1_max), .Max_num(max_1_max_num));
  MAX max_2 (.Y(c3), .X(c2), .Y_num(3'b011), .X_num(3'b010), .MAX(max_2_max), .Max_num(max_2_max_num));
  MAX max_3 (.Y(c5), .X(c4), .Y_num(3'b101), .X_num(3'b100), .MAX(max_3_max), .Max_num(max_3_max_num));
  MAX max_4 (.Y(c7), .X(c6), .Y_num(3'b111), .X_num(3'b110), .MAX(max_4_max), .Max_num(max_4_max_num));
  or or_9 (EX_Hit, M0, M1, M2, M3, M4, M5, M6, M7);
  not not_9 (EX_Miss, EX_Hit);
  Priority_Encoder #(.select(3), .disabled("Z")) priority_encoder_1 (
    .in0(not_1_out), .in1(not_2_out), .in2(not_3_out), .in3(not_4_out), .in4(not_5_out), .in5(not_6_out),
    .in6(not_7_out), .in7(not_8_out), .out(priority_encoder_1_out), .gs(priority_encoder_1_gs));  // open: en_out, en_in
  MAX max_5 (
    .Y(max_2_max), .X(max_1_max), .Y_num(max_2_max_num), .X_num(max_1_max_num), .MAX(max_5_max),
    .Max_num(max_5_max_num));
  MAX max_6 (
    .Y(max_4_max), .X(max_3_max), .Y_num(max_4_max_num), .X_num(max_3_max_num), .MAX(max_6_max),
    .Max_num(max_6_max_num));
  and and_17 (and_17_out, v0, v1, v2, v3, v4, v5, v6, v7);
  Decoder #(.select(3), .tristate("false"), .disabled(0), .enable("true")) decoder_1 (
    .out0(decoder_1_out0), .out1(decoder_1_out1), .out2(decoder_1_out2), .out3(decoder_1_out3),
    .out4(decoder_1_out4), .out5(decoder_1_out5), .out6(decoder_1_out6), .out7(decoder_1_out7),
    .sel(priority_encoder_1_out), .en(priority_encoder_1_gs));
  Decoder #(.select(3), .tristate("false"), .disabled(0), .enable("true")) decoder_2 (
    .out0(decoder_2_out0), .out1(decoder_2_out1), .out2(decoder_2_out2), .out3(decoder_2_out3),
    .out4(decoder_2_out4), .out5(decoder_2_out5), .out6(decoder_2_out6), .out7(decoder_2_out7),
    .sel(max_7_max_num), .en(and_17_out));
  MAX max_7 (
    .Y(max_6_max), .X(max_5_max), .Y_num(max_6_max_num), .X_num(max_5_max_num), .Max_num(max_7_max_num));  // open: MAX
  or or_10 (or_10_out, decoder_1_out0, decoder_2_out0);
  or or_11 (or_11_out, decoder_1_out1, decoder_2_out1);
  or or_12 (or_12_out, decoder_1_out2, decoder_2_out2);
  or or_13 (or_13_out, decoder_1_out3, decoder_2_out3);
  or or_14 (or_14_out, decoder_1_out4, decoder_2_out4);
  or or_15 (or_15_out, decoder_1_out5, decoder_2_out5);
  or or_16 (or_16_out, decoder_1_out6, decoder_2_out6);
  or or_17 (or_17_out, decoder_1_out7, decoder_2_out7);
  and and_18 (write0, or_10_out, EX_Miss, EX_Branch);
  and and_19 (write1, or_11_out, EX_Miss, EX_Branch);
  and and_20 (write2, or_12_out, EX_Miss, EX_Branch);
  and and_21 (write3, or_13_out, EX_Miss, EX_Branch);
  and and_22 (write4, or_14_out, EX_Miss, EX_Branch);
  and and_23 (write5, or_15_out, EX_Miss, EX_Branch);
  and and_24 (write6, or_16_out, EX_Miss, EX_Branch);
  and and_25 (write7, or_17_out, EX_Miss, EX_Branch);
  assign {IF_PredictJump, controlled_buffer_9_out[0]} = L0 ? predict0 : 2'bz;  // Controlled_Buffer controlled_buffer_9
  assign {IF_PredictJump, controlled_buffer_10_out[0]} = L1 ? predict1 : 2'bz;  // Controlled_Buffer controlled_buffer_10
  assign {IF_PredictJump, controlled_buffer_11_out[0]} = L2 ? predict2 : 2'bz;  // Controlled_Buffer controlled_buffer_11
  assign {IF_PredictJump, controlled_buffer_12_out[0]} = L3 ? predict3 : 2'bz;  // Controlled_Buffer controlled_buffer_12
  assign {IF_PredictJump, controlled_buffer_13_out[0]} = L4 ? predict4 : 2'bz;  // Controlled_Buffer controlled_buffer_13
  assign {IF_PredictJump, controlled_buffer_14_out[0]} = L5 ? predict5 : 2'bz;  // Controlled_Buffer controlled_buffer_14
  assign {IF_PredictJump, controlled_buffer_15_out[0]} = L6 ? predict6 : 2'bz;  // Controlled_Buffer controlled_buffer_15
  assign {IF_PredictJump, controlled_buffer_16_out[0]} = L7 ? predict7 : 2'bz;  // Controlled_Buffer controlled_buffer_16
  Pull_Resistor #(.pull(0)) pull_resistor_1 (.node(IF_PredictJump));
  FSM fsm_1 (
    .high(predict0[1]), .low(predict0[0]), .jump(EX_Branched), .NextHigh(fsm_1_nextlow[1]),
    .NextLow(fsm_1_nextlow[0]));
  FSM fsm_2 (
    .high(predict1[1]), .low(predict1[0]), .jump(EX_Branched), .NextHigh(fsm_2_nextlow[1]),
    .NextLow(fsm_2_nextlow[0]));
  FSM fsm_3 (
    .high(predict2[1]), .low(predict2[0]), .jump(EX_Branched), .NextHigh(fsm_3_nextlow[1]),
    .NextLow(fsm_3_nextlow[0]));
  FSM fsm_4 (
    .high(predict3[1]), .low(predict3[0]), .jump(EX_Branched), .NextHigh(fsm_4_nextlow[1]),
    .NextLow(fsm_4_nextlow[0]));
  FSM fsm_5 (
    .high(predict4[1]), .low(predict4[0]), .jump(EX_Branched), .NextHigh(fsm_5_nextlow[1]),
    .NextLow(fsm_5_nextlow[0]));
  FSM fsm_6 (
    .high(predict5[1]), .low(predict5[0]), .jump(EX_Branched), .NextHigh(fsm_6_nextlow[1]),
    .NextLow(fsm_6_nextlow[0]));
  FSM fsm_7 (
    .high(predict6[1]), .low(predict6[0]), .jump(EX_Branched), .NextHigh(fsm_7_nextlow[1]),
    .NextLow(fsm_7_nextlow[0]));
  FSM fsm_8 (
    .high(predict7[1]), .low(predict7[0]), .jump(EX_Branched), .NextHigh(fsm_8_nextlow[1]),
    .NextLow(fsm_8_nextlow[0]));
  and and_26 (and_26_out, EX_Branch, M0);
  Register #(.width(2), .trigger("rising"), .Select("low")) register_25 (
    .D(fsm_1_nextlow), .en(and_26_out), .Q(predict0), .clk(in_6));  // open: clr
  and and_27 (and_27_out, EX_Branch, M1);
  Register #(.width(2), .trigger("rising"), .Select("low")) register_26 (
    .D(fsm_2_nextlow), .en(and_27_out), .Q(predict1), .clk(in_6));  // open: clr
  and and_28 (and_28_out, EX_Branch, M2);
  Register #(.width(2), .trigger("rising"), .Select("low")) register_27 (
    .D(fsm_3_nextlow), .en(and_28_out), .Q(predict2), .clk(in_6));  // open: clr
  and and_29 (and_29_out, EX_Branch, M3);
  Register #(.width(2), .trigger("rising"), .Select("low")) register_28 (
    .D(fsm_4_nextlow), .en(and_29_out), .Q(predict3), .clk(in_6));  // open: clr
  and and_30 (and_30_out, EX_Branch, M4);
  Register #(.width(2), .trigger("rising"), .Select("low")) register_29 (
    .D(fsm_5_nextlow), .en(and_30_out), .Q(predict4), .clk(in_6));  // open: clr
  and and_31 (and_31_out, EX_Branch, M5);
  Register #(.width(2), .trigger("rising"), .Select("low")) register_30 (
    .D(fsm_6_nextlow), .en(and_31_out), .Q(predict5), .clk(in_6));  // open: clr
  and and_32 (and_32_out, EX_Branch, M6);
  Register #(.width(2), .trigger("rising"), .Select("low")) register_31 (
    .D(fsm_7_nextlow), .en(and_32_out), .Q(predict6), .clk(in_6));  // open: clr
  and and_33 (and_33_out, EX_Branch, M7);
  Register #(.width(2), .trigger("rising"), .Select("low")) register_32 (
    .D(fsm_8_nextlow), .en(and_33_out), .Q(predict7), .clk(in_6));  // open: clr

  // Other names for the same wires on the sheet: CLK = in_6; Tag[31:0] = EX_PC

  // Notes on the sheet:
  //   EX写入逻辑
  //   历史预测位
  //   与PC比较数据命中  选择L而不是M
  //   EX.PC如果数据命中，需要根据EX.Branched的值依据预测位状态机更新分支预测历史位的值
endmodule
